// Logisim project MIPSmulticyclePARALELOLD.circ as structural Verilog: 22 circuits, main circuit main
module main (
  input  clk,
  input  rst
);

  wire button_1_out, button_2_out, button_3_out, button_4_out, button_5_out, clk_t, cU3B, cUHW, equalALU,
       equalBR, halt, isOpALU, jmpE, lnk, mips_panel_1_clko, mips_panel_1_ex, mips_panel_1_id,
       mips_panel_1_if, mips_panel_1_mem, mips_panel_1_out_14, mips_panel_1_out_15, mips_panel_1_out_16,
       mips_panel_1_out_17, mips_panel_1_out_18, mips_panel_1_out_19, mips_panel_1_out_20, mips_panel_1_wb,
       not_1_out, not_2_out, not_3_out, rDM, rst_t, wBREG, wDM;
  wire [0:0] or_1_out;
  wire [1:0] jmpM;
  wire [4:0] instruction_register_32b_1_rs, mips_panel_1_a0_l0, mips_panel_1_a1_l0, mips_panel_1_a2_l0,
       mips_panel_1_a3_l0, mips_panel_1_a4_l1, mips_panel_1_a5_l1, mips_panel_1_a6_l1, mips_panel_1_a7_l1,
       mips_panel_1_a8_l2, mips_panel_1_a9_l2, mips_panel_1_a10_l2, mips_panel_1_a11_l2, mips_panel_1_a12_l3,
       mips_panel_1_a13_l3, mips_panel_1_a14_l3, mips_panel_1_a15_l3, mips_panel_1_a16_l4,
       mips_panel_1_a17_l4, mips_panel_1_a18_l4, mips_panel_1_a19__l4, mips_panel_1_a20_l5,
       mips_panel_1_a21_l5, mips_panel_1_a22_l5, mips_panel_1_a23_l5, mips_panel_1_a24_l5,
       mips_panel_1_a25_l5, mips_panel_1_a26_l5, mips_panel_1_a27_l5, mips_panel_1_a28_l5,
       mips_panel_1_a29_l5, mips_panel_1_a30_l5, mips_panel_1_a31_l5, mips_panel_1_i0___l0,
       mips_panel_1_i1___l0, mips_panel_1_i2___l0, mips_panel_1_i3___l0, mips_panel_1_i4___l1,
       mips_panel_1_i5___l1, mips_panel_1_i6___l1, mips_panel_1_i7___l1, mips_panel_1_i9___l2,
       mips_panel_1_i10___l2, mips_panel_1_i11___l3, mips_panel_1_i12___l2, mips_panel_1_i13___l3,
       mips_panel_1_i13___l3_2, mips_panel_1_i14___l3, mips_panel_1_i14___l3_2, mips_panel_1_i15___l3,
       mips_panel_1_i15___l3_2, mips_panel_1_i16___l3, mips_panel_1_i16___l3_2, mips_panel_1_i17___l5,
       mips_panel_1_i18___l4, mips_panel_1_i19___l5, mips_panel_1_i20___l4, mips_panel_1_im0___l0,
       mips_panel_1_im1___l0, mips_panel_1_im2___l0, mips_panel_1_im3___l0, mips_panel_1_im4___l1,
       mips_panel_1_im5___l1, mips_panel_1_im6___l1, mips_panel_1_im7___l1, mips_panel_1_im9___l2,
       mips_panel_1_im10___l2, mips_panel_1_im11___l3, mips_panel_1_im12___l2, mips_panel_1_rd0___l0,
       mips_panel_1_rd1___l0, mips_panel_1_rd2___l0, mips_panel_1_rd3___l0, mips_panel_1_rd4___l1,
       mips_panel_1_rd5___l1, mips_panel_1_rd6___l1, mips_panel_1_rd7___l1, mips_panel_1_rs0___l0,
       mips_panel_1_rs1___l0, mips_panel_1_rs2___l0, mips_panel_1_rs3___l0, mips_panel_1_rs4___l1,
       mips_panel_1_rs5___l1, mips_panel_1_rs6___l1, mips_panel_1_rs7___l1, mips_panel_1_rt1___l0,
       mips_panel_1_rt2___l0, mips_panel_1_rt3___l0, mips_panel_1_rt4___l1, mips_panel_1_rt5___l1,
       mips_panel_1_rt6___l1, mips_panel_1_rt7___l1, mips_panel_1_rt___l0, mips_panel_1_sh0___l0,
       mips_panel_1_sh1___l0, mips_panel_1_sh2___l0, mips_panel_1_sh3___l0, mips_panel_1_sh4___l1,
       mips_panel_1_sh5___l1, mips_panel_1_sh6___l1, mips_panel_1_sh7___l1, multiplexer_3_out, rt, shamt,
       undriven, undriven_3;
  wire [5:0] funct, \function , multiplexer_7_out, opCode, undriven_2;
  wire [15:0] immd, multiplexer_8_out;
  wire [23:0] bit_extender_1_out, bit_extender_3_out;
  wire [25:0] adressJM;
  wire [31:0] adder_1_out, adder_2_out, ALUout, breg_1_value_2, DMout, Instruction_Memory_data, IR,
       multiplexer_1_out, multiplexer_4_out, multiplexer_5_out, multiplexer_6_out, multiplexer_9_out, PC,
       sgnExtImmd, vRs;
  wire [31:16] multiplexer_8_out_2;

  MIPS_Panel mips_panel_1 (
    .btControl(button_1_out), .btRun(button_2_out), .btStep(button_3_out), .btReset(button_4_out),
    .btExtra(button_5_out), .clk(clk), .rst(rst), .out_14(mips_panel_1_out_14), .out_15(mips_panel_1_out_15),
    .out_16(mips_panel_1_out_16), .out_17(mips_panel_1_out_17), .out_18(mips_panel_1_out_18),
    .out_19(mips_panel_1_out_19), .out_20(mips_panel_1_out_20), .clkO(mips_panel_1_clko), .rstO(rst_t),
    .I17___L5(mips_panel_1_i17___l5), .I18___L4(mips_panel_1_i18___l4), .I19___L5(mips_panel_1_i19___l5),
    .I20___L4(mips_panel_1_i20___l4), .IM(IR), .RS0___L0(mips_panel_1_rs0___l0),
    .RS1___L0(mips_panel_1_rs1___l0), .RS2___L0(mips_panel_1_rs2___l0), .RS3___L0(mips_panel_1_rs3___l0),
    .RS4___L1(mips_panel_1_rs4___l1), .RS5___L1(mips_panel_1_rs5___l1), .RS6___L1(mips_panel_1_rs6___l1),
    .RS7___L1(mips_panel_1_rs7___l1), .RT___L0(mips_panel_1_rt___l0), .RT1___L0(mips_panel_1_rt1___l0),
    .RT2___L0(mips_panel_1_rt2___l0), .RT3___L0(mips_panel_1_rt3___l0), .RT4___L1(mips_panel_1_rt4___l1),
    .RT5___L1(mips_panel_1_rt5___l1), .RT6___L1(mips_panel_1_rt6___l1), .RT7___L1(mips_panel_1_rt7___l1),
    .RD1___L0(mips_panel_1_rd1___l0), .RD2___L0(mips_panel_1_rd2___l0), .RD3___L0(mips_panel_1_rd3___l0),
    .RD4___L1(mips_panel_1_rd4___l1), .RD5___L1(mips_panel_1_rd5___l1), .RD6___L1(mips_panel_1_rd6___l1),
    .RD7___L1(mips_panel_1_rd7___l1), .I0___L0(mips_panel_1_i0___l0), .I1___L0(mips_panel_1_i1___l0),
    .I2___L0(mips_panel_1_i2___l0), .I3___L0(mips_panel_1_i3___l0), .I4___L1(mips_panel_1_i4___l1),
    .I5___L1(mips_panel_1_i5___l1), .I6___L1(mips_panel_1_i6___l1), .I7___L1(mips_panel_1_i7___l1),
    .I9___L2(mips_panel_1_i9___l2), .I10___L2(mips_panel_1_i10___l2), .I11___L3(mips_panel_1_i11___l3),
    .I12___L2(mips_panel_1_i12___l2), .I13___L3_2(mips_panel_1_i13___l3_2),
    .I14___L3_2(mips_panel_1_i14___l3_2), .I15___L3_2(mips_panel_1_i15___l3_2),
    .I16___L3_2(mips_panel_1_i16___l3_2), .IM0___L0(mips_panel_1_im0___l0), .IM1___L0(mips_panel_1_im1___l0),
    .IM2___L0(mips_panel_1_im2___l0), .IM4___L1(mips_panel_1_im4___l1), .IM5___L1(mips_panel_1_im5___l1),
    .IM6___L1(mips_panel_1_im6___l1), .IM7___L1(mips_panel_1_im7___l1), .IM9___L2(mips_panel_1_im9___l2),
    .IM10___L2(mips_panel_1_im10___l2), .IM11___L3(mips_panel_1_im11___l3),
    .IM12___L2(mips_panel_1_im12___l2), .I13___L3(mips_panel_1_i13___l3), .I14___L3(mips_panel_1_i14___l3),
    .I15___L3(mips_panel_1_i15___l3), .I16___L3(mips_panel_1_i16___l3), .SH0___L0(mips_panel_1_sh0___l0),
    .SH1___L0(mips_panel_1_sh1___l0), .SH2___L0(mips_panel_1_sh2___l0), .SH3___L0(mips_panel_1_sh3___l0),
    .SH4___L1(mips_panel_1_sh4___l1), .SH5___L1(mips_panel_1_sh5___l1), .IM3___L0(mips_panel_1_im3___l0),
    .SH6___L1(mips_panel_1_sh6___l1), .SH7___L1(mips_panel_1_sh7___l1), .RD0___L0(mips_panel_1_rd0___l0),
    .A12_L3(mips_panel_1_a12_l3), .A13_L3(mips_panel_1_a13_l3), .A14_L3(mips_panel_1_a14_l3),
    .A15_L3(mips_panel_1_a15_l3), .A16_L4(mips_panel_1_a16_l4), .A17_L4(mips_panel_1_a17_l4),
    .A18_L4(mips_panel_1_a18_l4), .A24_L5(mips_panel_1_a24_l5), .A25_L5(mips_panel_1_a25_l5),
    .A26_L5(mips_panel_1_a26_l5), .A27_L5(mips_panel_1_a27_l5), .A28_L5(mips_panel_1_a28_l5),
    .A29_L5(mips_panel_1_a29_l5), .A30_L5(mips_panel_1_a30_l5), .A31_L5(mips_panel_1_a31_l5),
    .A0_L0(mips_panel_1_a0_l0), .A1_L0(mips_panel_1_a1_l0), .A2_L0(mips_panel_1_a2_l0),
    .A3_L0(mips_panel_1_a3_l0), .A4_L1(mips_panel_1_a4_l1), .A5_L1(mips_panel_1_a5_l1),
    .A6_L1(mips_panel_1_a6_l1), .A7_L1(mips_panel_1_a7_l1), .A8_L2(mips_panel_1_a8_l2),
    .A10_L2(mips_panel_1_a10_l2), .A11_L2(mips_panel_1_a11_l2), .A9_L2(mips_panel_1_a9_l2),
    .A20_L5(mips_panel_1_a20_l5), .A21_L5(mips_panel_1_a21_l5), .A22_L5(mips_panel_1_a22_l5),
    .A23_L5(mips_panel_1_a23_l5), .A19__L4(mips_panel_1_a19__l4), .IF(mips_panel_1_if), .ID(mips_panel_1_id),
    .EX(mips_panel_1_ex), .MEM(mips_panel_1_mem), .WB(mips_panel_1_wb));
  DotMatrix #(.matrixcols(20), .matrixrows(5)) dotmatrix_1 (
    .col0(mips_panel_1_i0___l0), .col1(mips_panel_1_i1___l0), .col2(mips_panel_1_i2___l0),
    .col3(mips_panel_1_i3___l0), .col4(mips_panel_1_i4___l1), .col5(mips_panel_1_i5___l1),
    .col6(mips_panel_1_i6___l1), .col7(mips_panel_1_i7___l1), .col8(mips_panel_1_i9___l2),
    .col9(mips_panel_1_i10___l2), .col10(mips_panel_1_i11___l3), .col11(mips_panel_1_i12___l2),
    .col12(mips_panel_1_i13___l3_2), .col13(mips_panel_1_i14___l3_2), .col14(mips_panel_1_i15___l3_2),
    .col15(mips_panel_1_i16___l3_2), .col16(mips_panel_1_i17___l5), .col17(mips_panel_1_i18___l4),
    .col18(mips_panel_1_i19___l5), .col19(mips_panel_1_i20___l4));
  DotMatrix #(.matrixcols(8), .matrixrows(5)) dotmatrix_2 (
    .col0(mips_panel_1_rs0___l0), .col1(mips_panel_1_rs1___l0), .col2(mips_panel_1_rs2___l0),
    .col3(mips_panel_1_rs3___l0), .col4(mips_panel_1_rs4___l1), .col5(mips_panel_1_rs5___l1),
    .col6(mips_panel_1_rs6___l1), .col7(mips_panel_1_rs7___l1));
  Bit_Extender #(.in_width(32), .out_width(24), .\type ("zero")) bit_extender_1 (.in(PC), .out(bit_extender_1_out));
  DotMatrix #(.matrixcols(8), .matrixrows(5)) dotmatrix_3 (
    .col0(mips_panel_1_rt___l0), .col1(mips_panel_1_rt1___l0), .col2(mips_panel_1_rt2___l0),
    .col3(mips_panel_1_rt3___l0), .col4(mips_panel_1_rt4___l1), .col5(mips_panel_1_rt5___l1),
    .col6(mips_panel_1_rt6___l1), .col7(mips_panel_1_rt7___l1));
  LED led_1 (.in(mips_panel_1_out_19));
  LED led_2 (.in(mips_panel_1_out_14));
  LED led_3 (.in(mips_panel_1_out_20));
  Button button_1 (.out(button_1_out));
  Adder #(.width(32)) adder_1 (.a(PC), .b(sgnExtImmd), .out(adder_1_out), .cin(1'b0));  // open: cout
  LED led_4 (.in(mips_panel_1_out_15));
  Button button_2 (.out(button_2_out));
  ROM #(.addrWidth(24), .dataWidth(32), .Select("low")) Instruction_Memory (
    .addr(bit_extender_1_out), .data(Instruction_Memory_data), .sel(1'b0));
  Multiplexer #(.select(2), .width(32), .enable("false")) multiplexer_1 (
    .in0(vRs), .in1({PC[31:26], adressJM}), .in2(adder_1_out), .in3(adder_1_out), .out(multiplexer_1_out),
    .sel(jmpM));
  not not_1 (not_1_out, jmpE);
  DotMatrix #(.matrixcols(32), .matrixrows(5)) dotmatrix_4 (
    .col0(mips_panel_1_a0_l0), .col1(mips_panel_1_a1_l0), .col2(mips_panel_1_a2_l0),
    .col3(mips_panel_1_a3_l0), .col4(mips_panel_1_a4_l1), .col5(mips_panel_1_a5_l1),
    .col6(mips_panel_1_a6_l1), .col7(mips_panel_1_a7_l1), .col8(mips_panel_1_a8_l2),
    .col9(mips_panel_1_a9_l2), .col10(mips_panel_1_a10_l2), .col11(mips_panel_1_a11_l2),
    .col12(mips_panel_1_a12_l3), .col13(mips_panel_1_a13_l3), .col14(mips_panel_1_a14_l3),
    .col15(mips_panel_1_a15_l3), .col16(mips_panel_1_a16_l4), .col17(mips_panel_1_a17_l4),
    .col18(mips_panel_1_a18_l4), .col19(mips_panel_1_a19__l4), .col20(mips_panel_1_a20_l5),
    .col21(mips_panel_1_a21_l5), .col22(mips_panel_1_a22_l5), .col23(mips_panel_1_a23_l5),
    .col24(mips_panel_1_a24_l5), .col25(mips_panel_1_a25_l5), .col26(mips_panel_1_a26_l5),
    .col27(mips_panel_1_a27_l5), .col28(mips_panel_1_a28_l5), .col29(mips_panel_1_a29_l5),
    .col30(mips_panel_1_a30_l5), .col31(mips_panel_1_a31_l5));
  DotMatrix #(.matrixcols(8), .matrixrows(5)) dotmatrix_5 (
    .col0(mips_panel_1_rd0___l0), .col1(mips_panel_1_rd1___l0), .col2(mips_panel_1_rd2___l0),
    .col3(mips_panel_1_rd3___l0), .col4(mips_panel_1_rd4___l1), .col5(mips_panel_1_rd5___l1),
    .col6(mips_panel_1_rd6___l1), .col7(mips_panel_1_rd7___l1));
  LED led_5 (.in(mips_panel_1_out_16));
  Button button_3 (.out(button_3_out));
  Comparator #(.width(6)) comparator_1 (.a(opCode), .b({6{1'b0}}), .eq(isOpALU));  // open: gt, lt
  Counter #(.width(32), .max('hffff), .behavior("old")) u_PC (
    .load(jmpE), .D(multiplexer_1_out), .count(not_1_out), .Q(PC), .clk(clk_t), .clr(rst_t), .preset(1'b0));  // open: carry
  DotMatrix #(.matrixcols(16), .matrixrows(5)) dotmatrix_6 (
    .col0(mips_panel_1_im0___l0), .col1(mips_panel_1_im1___l0), .col2(mips_panel_1_im2___l0),
    .col3(mips_panel_1_im3___l0), .col4(mips_panel_1_im4___l1), .col5(mips_panel_1_im5___l1),
    .col6(mips_panel_1_im6___l1), .col7(mips_panel_1_im7___l1), .col8(mips_panel_1_im9___l2),
    .col9(mips_panel_1_im10___l2), .col10(mips_panel_1_im11___l3), .col11(mips_panel_1_im12___l2),
    .col12(mips_panel_1_i13___l3), .col13(mips_panel_1_i14___l3), .col14(mips_panel_1_i15___l3),
    .col15(mips_panel_1_i16___l3));
  LED led_6 (.in(mips_panel_1_out_17));
  LED led_7 (.in(mips_panel_1_out_18));
  Button button_4 (.out(button_4_out));
  Button button_5 (.out(button_5_out));
  Instruction_Register_32b instruction_register_32b_1 (
    .D(Instruction_Memory_data), .opCode(opCode), .Rs(instruction_register_32b_1_rs), .Q(IR));  // open: load, clk, isOpALU, Rt, Rd, rst, SHAMT, funct, immd, adrJMP, Q_for_visulization
  LED led_8 (.in(mips_panel_1_if));
  LED led_9 (.in(mips_panel_1_ex));
  DotMatrix #(.matrixcols(8), .matrixrows(5)) dotmatrix_7 (
    .col0(mips_panel_1_sh0___l0), .col1(mips_panel_1_sh1___l0), .col2(mips_panel_1_sh2___l0),
    .col3(mips_panel_1_sh3___l0), .col4(mips_panel_1_sh4___l1), .col5(mips_panel_1_sh5___l1),
    .col6(mips_panel_1_sh6___l1), .col7(mips_panel_1_sh7___l1));
  LED led_10 (.in(mips_panel_1_mem));
  LED led_11 (.in(mips_panel_1_wb));
  LED led_12 (.in(mips_panel_1_id));
  assign sgnExtImmd = {{16{immd[15]}}, immd};  // Bit_Extender bit_extender_2
  assign clk_t = ~halt ? mips_panel_1_clko : 1'bz;  // Controlled_Buffer controlled_buffer_1
  Multiplexer #(.width(6), .enable("false")) multiplexer_2 (
    .in0({1'b0, rt}), .in1(undriven_2), .out(\function ), .sel(isOpALU));
  Multiplexer #(.select(2), .width(5), .enable("false")) multiplexer_3 (
    .in0(undriven_3), .in1(undriven), .in2(undriven), .in3({5{1'b1}}), .out(multiplexer_3_out),
    .sel({lnk, or_1_out[0]}));
  or or_1 (or_1_out[0], lnk, isOpALU);
  BREG breg_1 (
    .source_1(instruction_register_32b_1_rs), .target(multiplexer_3_out), .source_2(undriven_3),
    .\input (multiplexer_4_out), .clk(clk_t), .value_1(vRs), .value_2(breg_1_value_2), .w(wBREG), .rst(rst_t));
  Multiplexer #(.select(2), .width(32), .enable("false")) multiplexer_4 (
    .in0({multiplexer_8_out_2, multiplexer_8_out}), .in1({{16{1'b0}}, multiplexer_8_out}),
    .in2({{24{1'b0}}, multiplexer_8_out[7:0]}), .in3({{24{1'b0}}, multiplexer_8_out[7:0]}),
    .out(multiplexer_4_out), .sel({cU3B, cUHW}));
  Comparator #(.width(32)) comparator_2 (.a(vRs), .b(breg_1_value_2), .eq(equalBR));  // open: gt, lt
  Control_Unit control_unit_1 (
    .opCode(opCode), .wBREG(wBREG), .clk(clk_t), .rst(rst_t), .jmpE(jmpE), .jmpM(jmpM), .wDM(wDM), .rDM(rDM),
    .cUHW(cUHW), .vRs(vRs), .\function (\function ), .link(lnk), .halt(halt), .cU3B(cU3B),
    .equalBREG(equalBR), .equalALU(equalALU));
  Multiplexer #(.width(32), .enable("false")) multiplexer_5 (
    .in0(sgnExtImmd), .in1(breg_1_value_2), .out(multiplexer_5_out), .sel(isOpALU));
  Multiplexer #(.select(2), .width(32), .enable("false")) multiplexer_6 (
    .in0(breg_1_value_2), .in1({{16{1'b0}}, breg_1_value_2[15:0]}), .in2({{24{1'b0}}, breg_1_value_2[7:0]}),
    .in3({{24{1'b0}}, breg_1_value_2[7:0]}), .out(multiplexer_6_out), .sel({cU3B, cUHW}));
  Adder #(.width(32)) adder_2 (.a(PC), .b(32'h1), .out(adder_2_out), .cin(1'b0));  // open: cout
  Multiplexer #(.width(6), .enable("false")) multiplexer_7 (
    .in0({6{1'b1}}), .in1(funct), .out(multiplexer_7_out), .sel(isOpALU));
  Bit_Extender #(.in_width(32), .out_width(24), .\type ("zero")) bit_extender_3 (.in(ALUout), .out(bit_extender_3_out));
  ALU alu_1 (
    .A(vRs), .B(multiplexer_5_out), .R(ALUout), .\function (multiplexer_7_out), .equal(equalALU),
    .shamt(shamt));
  Multiplexer #(.width(32), .disabled(0), .enable("false")) multiplexer_8 (
    .in0(adder_2_out), .in1(multiplexer_9_out), .out({multiplexer_8_out_2, multiplexer_8_out}),
    .sel(not_2_out));
  Multiplexer #(.width(32), .disabled(0), .enable("false")) multiplexer_9 (
    .in0(DMout), .in1(ALUout), .out(multiplexer_9_out), .sel(not_3_out));
  not not_2 (not_2_out, lnk);
  not not_3 (not_3_out, rDM);
  RAM #(.addrWidth(24), .dataWidth(32), .bus("separate"), .simpleMode("false"), .Select("low")) DM (
    .addr(bit_extender_3_out), .din(multiplexer_6_out), .data(DMout), .str(wDM), .sel(1'b0), .clk(clk_t),
    .ld(1'b1), .clr(rst_t));

  // Notes on the sheet:
  //        Branch's$(Relative Jumps)
  //   Jump Register
  //   Jump
  //   contents of Instruction_Memory (hex, n*v repeats v):
  //   20e58040 8c020004 221820 621822 10610002 ac000008 8000000 ac030008 8000000
endmodule

module ALU (
  input  [31:0] A,
  input  [31:0] B,
  input  [4:0] shamt,
  input  [5:0] \function ,
  output equal,
  output [31:0] R
);

  wire comparator_2_eq, isOpALU, lt, ltu, mux_funct_1b_1_output, registerInputs;
  wire [31:0] \and , bit_extender_1_out, bit_extender_2_out, dif, HI, LO, not_2_out, \or , rA_q, rB_q,
       shifter_1_out, shifter_2_out, sum;

  Comparator #(.width(32)) comparator_1 (.a(A), .b(B), .eq(equal), .lt(lt));  // open: gt
  Comparator #(.width(6)) comparator_2 (.a(\function ), .b({6{1'b1}}), .eq(comparator_2_eq));  // open: gt, lt
  Adder #(.width(32)) adder_1 (.a(A), .b(B), .out(sum), .cin(1'b0));  // open: cout
  Shifter #(.width(32), .shift("lr")) shifter_1 (.in(A), .\dist (shamt), .out(shifter_1_out));
  assign bit_extender_1_out = {{31{1'b0}}, lt};  // Bit_Extender bit_extender_1
  not not_1 (isOpALU, comparator_2_eq);
  Shifter #(.width(32)) shifter_2 (.in(A), .\dist (shamt), .out(shifter_2_out));
  assign not_2_out = ~\or ;  // NOT_Gate not_2, 32 bits wide
  assign bit_extender_2_out = {{31{1'b0}}, ltu};  // Bit_Extender bit_extender_2
  Subtractor #(.width(32)) subtractor_1 (.a(A), .b(B), .out(dif), .bin(1'b0));  // open: bout
  MUX_funct_32b mux_funct_32b_1 (
    .in_1(shifter_2_out), .in_3(shifter_1_out), .in_9(A), .in_17(HI), .in_19(LO), .in_25({32{1'b0}}),
    .sel(\function ), .in_34(sum), .in_35(sum), .in_36(dif), .in_37(dif), .in_38(\and ), .in_39(\or ),
    .in_41(not_2_out), .in_44(bit_extender_1_out), .in_45(bit_extender_2_out), .in_65(sum), .\output (R));  // open: in_2, in_4, in_5, in_6, in_7, in_8, in_10, in_11, in_12, in_13, in_14, in_15, in_16, in_18, in_20, in_21, in_22, in_23, in_24, in_26, in_27, in_28, in_29, in_30, in_31, in_32, in_40, in_42, in_43, in_46, in_47, in_48, in_49, in_50, in_51, in_52, in_53, in_54, in_55, in_56, in_57, in_58, in_59, in_60, in_61, in_62, in_63, in_64
  assign \and  = A & B;  // AND_Gate and_1, 32 bits wide
  assign \or  = A | B;  // OR_Gate or_1, 32 bits wide
  Comparator #(.width(32), .mode("unsigned")) comparator_3 (.a(A), .b(B), .lt(ltu));  // open: gt, eq
  MUX_funct_1b mux_funct_1b_1 (
    .in_1(1'b0), .in_2(1'b0), .in_3(1'b0), .in_4(1'b0), .in_5(1'b0), .in_6(1'b0), .in_7(1'b0), .in_8(1'b0),
    .in_9(1'b0), .in_10(1'b0), .in_11(1'b0), .in_12(1'b0), .in_13(1'b0), .in_14(1'b0), .in_15(1'b0),
    .in_16(1'b0), .in_17(1'b0), .in_18(1'b0), .in_19(1'b0), .in_20(1'b0), .in_21(1'b0), .in_22(1'b0),
    .in_23(1'b0), .in_24(1'b0), .in_25(1'b1), .in_26(1'b0), .in_27(1'b0), .in_28(1'b0), .in_29(1'b0),
    .in_30(1'b0), .in_31(1'b0), .in_32(1'b0), .sel(\function ), .in_34(1'b0), .in_35(1'b0), .in_36(1'b0),
    .in_37(1'b0), .in_38(1'b0), .in_39(1'b0), .in_40(1'b0), .in_41(1'b0), .in_42(1'b0), .in_43(1'b0),
    .in_44(1'b0), .in_45(1'b0), .in_46(1'b0), .in_47(1'b0), .in_48(1'b0), .in_49(1'b0), .in_50(1'b0),
    .in_51(1'b0), .in_52(1'b0), .in_53(1'b0), .in_54(1'b0), .in_55(1'b0), .in_56(1'b0), .in_57(1'b0),
    .in_58(1'b0), .in_59(1'b0), .in_60(1'b0), .in_61(1'b0), .in_62(1'b0), .in_63(1'b0), .in_64(1'b0),
    .in_65(1'b0), .\output (mux_funct_1b_1_output));
  Register #(.width(32), .Select("low")) rA (
    .D(A), .en(1'b1), .Q(rA_q), .clk(registerInputs), .clr(1'b0), .cs(1'b0), .preset(1'b0));
  Register #(.width(32), .Select("low")) rB (
    .D(B), .en(1'b1), .Q(rB_q), .clk(registerInputs), .clr(1'b0), .cs(1'b0), .preset(1'b0));
  Multiplexer #(.enable("false")) multiplexer_1 (
    .in0(1'b0), .in1(mux_funct_1b_1_output), .out(registerInputs), .sel(isOpALU));
  Multiplier #(.width(32)) multiplier_1 (.a(rA_q), .b(rB_q), .out(LO), .cin({32{1'b0}}), .cout(HI));
  // Probe on LO
  // Probe on HI
endmodule

module BREG (
  input  clk,
  input  rst,
  input  [31:0] \input ,
  input  [4:0] source_1,
  input  w,
  input  [4:0] target,
  input  [4:0] source_2,
  output [31:0] value_1,
  output [31:0] value_2
);

  wire decoder_1_out0, decoder_1_out1, decoder_1_out2, decoder_1_out3, decoder_1_out4, decoder_1_out5,
       decoder_1_out6, decoder_1_out7, decoder_1_out8, decoder_1_out9, decoder_1_out10, decoder_1_out11,
       decoder_1_out12, decoder_1_out13, decoder_1_out14, decoder_1_out15, decoder_1_out16, decoder_1_out17,
       decoder_1_out18, decoder_1_out19, decoder_1_out20, decoder_1_out21, decoder_1_out22, decoder_1_out23,
       decoder_1_out24, decoder_1_out25, decoder_1_out26, decoder_1_out27, decoder_1_out28, decoder_1_out29,
       decoder_1_out30, decoder_1_out31;
  wire [31:0] Q1, Q2, Q3, Q4, Q5, Q6, Q7, Q8, Q9, Q10, Q11, Q12, Q13, Q14, Q15, Q16, Q17, Q18, Q19, Q20, Q21,
       Q22, Q23, Q24, Q25, Q26, Q27, Q28, Q29, Q30, Q31;

  LED led_1 (.in(decoder_1_out0));
  Decoder #(.select(5), .disabled(0)) decoder_1 (
    .out0(decoder_1_out0), .out1(decoder_1_out1), .out2(decoder_1_out2), .out3(decoder_1_out3),
    .out4(decoder_1_out4), .out5(decoder_1_out5), .out6(decoder_1_out6), .out7(decoder_1_out7),
    .out8(decoder_1_out8), .out9(decoder_1_out9), .out10(decoder_1_out10), .out11(decoder_1_out11),
    .out12(decoder_1_out12), .out13(decoder_1_out13), .out14(decoder_1_out14), .out15(decoder_1_out15),
    .out16(decoder_1_out16), .out17(decoder_1_out17), .out18(decoder_1_out18), .out19(decoder_1_out19),
    .out20(decoder_1_out20), .out21(decoder_1_out21), .out22(decoder_1_out22), .out23(decoder_1_out23),
    .out24(decoder_1_out24), .out25(decoder_1_out25), .out26(decoder_1_out26), .out27(decoder_1_out27),
    .out28(decoder_1_out28), .out29(decoder_1_out29), .out30(decoder_1_out30), .out31(decoder_1_out31),
    .sel(target), .en(w));
  Register #(.width(32), .Select("high")) AT_R1 (
    .D(\input ), .en(decoder_1_out1), .Q(Q1), .clk(clk), .clr(rst), .cs(1'b1), .preset(1'b0));
  Register #(.width(32), .Select("high")) R2 (
    .D(\input ), .en(decoder_1_out2), .Q(Q2), .clk(clk), .clr(rst), .cs(1'b1), .preset(1'b0));
  Register #(.width(32), .Select("high")) R3 (
    .D(\input ), .en(decoder_1_out3), .Q(Q3), .clk(clk), .clr(rst), .cs(1'b1), .preset(1'b0));
  Register #(.width(32), .Select("high")) R28 (
    .D(\input ), .en(decoder_1_out28), .Q(Q28), .clk(clk), .clr(rst), .cs(1'b1), .preset(1'b0));
  Register #(.width(32), .Select("high")) R29 (
    .D(\input ), .en(decoder_1_out29), .Q(Q29), .clk(clk), .clr(rst), .cs(1'b1), .preset(1'b0));
  Register #(.width(32), .Select("high")) R30 (
    .D(\input ), .en(decoder_1_out30), .Q(Q30), .clk(clk), .clr(rst), .cs(1'b1), .preset(1'b0));
  Register #(.width(32), .Select("high")) Return_Adress__R31 (
    .D(\input ), .en(decoder_1_out31), .Q(Q31), .clk(clk), .clr(rst), .cs(1'b1), .preset(1'b0));
  Register #(.width(32), .Select("high")) R4 (
    .D(\input ), .en(decoder_1_out4), .Q(Q4), .clk(clk), .clr(rst), .cs(1'b1), .preset(1'b0));
  Register #(.width(32), .Select("high")) R5 (
    .D(\input ), .en(decoder_1_out5), .Q(Q5), .clk(clk), .clr(rst), .cs(1'b1), .preset(1'b0));
  Register #(.width(32), .Select("high")) R6 (
    .D(\input ), .en(decoder_1_out6), .Q(Q6), .clk(clk), .clr(rst), .cs(1'b1), .preset(1'b0));
  Register #(.width(32), .Select("high")) R7 (
    .D(\input ), .en(decoder_1_out7), .Q(Q7), .clk(clk), .clr(rst), .cs(1'b1), .preset(1'b0));
  Register #(.width(32), .Select("high")) R24 (
    .D(\input ), .en(decoder_1_out24), .Q(Q24), .clk(clk), .clr(rst), .cs(1'b1), .preset(1'b0));
  Register #(.width(32), .Select("high")) R25 (
    .D(\input ), .en(decoder_1_out25), .Q(Q25), .clk(clk), .clr(rst), .cs(1'b1), .preset(1'b0));
  Register #(.width(32), .Select("high")) R26 (
    .D(\input ), .en(decoder_1_out26), .Q(Q26), .clk(clk), .clr(rst), .cs(1'b1), .preset(1'b0));
  Register #(.width(32), .Select("high")) R27 (
    .D(\input ), .en(decoder_1_out27), .Q(Q27), .clk(clk), .clr(rst), .cs(1'b1), .preset(1'b0));
  Register #(.width(32), .Select("high")) R8 (
    .D(\input ), .en(decoder_1_out8), .Q(Q8), .clk(clk), .clr(rst), .cs(1'b1), .preset(1'b0));
  Register #(.width(32), .Select("high")) R9 (
    .D(\input ), .en(decoder_1_out9), .Q(Q9), .clk(clk), .clr(rst), .cs(1'b1), .preset(1'b0));
  Register #(.width(32), .Select("high")) R10 (
    .D(\input ), .en(decoder_1_out10), .Q(Q10), .clk(clk), .clr(rst), .cs(1'b1), .preset(1'b0));
  Register #(.width(32), .Select("high")) R11 (
    .D(\input ), .en(decoder_1_out11), .Q(Q11), .clk(clk), .clr(rst), .cs(1'b1), .preset(1'b0));
  Register #(.width(32), .Select("high")) R20 (
    .D(\input ), .en(decoder_1_out20), .Q(Q20), .clk(clk), .clr(rst), .cs(1'b1), .preset(1'b0));
  Register #(.width(32), .Select("high")) R21 (
    .D(\input ), .en(decoder_1_out21), .Q(Q21), .clk(clk), .clr(rst), .cs(1'b1), .preset(1'b0));
  Register #(.width(32), .Select("high")) R22 (
    .D(\input ), .en(decoder_1_out22), .Q(Q22), .clk(clk), .clr(rst), .cs(1'b1), .preset(1'b0));
  Register #(.width(32), .Select("high")) R23 (
    .D(\input ), .en(decoder_1_out23), .Q(Q23), .clk(clk), .clr(rst), .cs(1'b1), .preset(1'b0));
  Register #(.width(32), .Select("high")) R12 (
    .D(\input ), .en(decoder_1_out12), .Q(Q12), .clk(clk), .clr(rst), .cs(1'b1), .preset(1'b0));
  Register #(.width(32), .Select("high")) R13 (
    .D(\input ), .en(decoder_1_out13), .Q(Q13), .clk(clk), .clr(rst), .cs(1'b1), .preset(1'b0));
  Register #(.width(32), .Select("high")) R14 (
    .D(\input ), .en(decoder_1_out14), .Q(Q14), .clk(clk), .clr(rst), .cs(1'b1), .preset(1'b0));
  Register #(.width(32), .Select("high")) R15 (
    .D(\input ), .en(decoder_1_out15), .Q(Q15), .clk(clk), .clr(rst), .cs(1'b1), .preset(1'b0));
  Register #(.width(32), .Select("high")) R16 (
    .D(\input ), .en(decoder_1_out16), .Q(Q16), .clk(clk), .clr(rst), .cs(1'b1), .preset(1'b0));
  Register #(.width(32), .Select("high")) R17 (
    .D(\input ), .en(decoder_1_out17), .Q(Q17), .clk(clk), .clr(rst), .cs(1'b1), .preset(1'b0));
  Register #(.width(32), .Select("high")) R18 (
    .D(\input ), .en(decoder_1_out18), .Q(Q18), .clk(clk), .clr(rst), .cs(1'b1), .preset(1'b0));
  Register #(.width(32), .Select("high")) R19 (
    .D(\input ), .en(decoder_1_out19), .Q(Q19), .clk(clk), .clr(rst), .cs(1'b1), .preset(1'b0));
  Multiplexer #(.select(5), .width(32), .enable("false")) multiplexer_1 (
    .in0({32{1'b0}}), .in1(Q1), .in2(Q2), .in3(Q3), .in4(Q4), .in5(Q5), .in6(Q6), .in7(Q7), .in8(Q8),
    .in9(Q9), .in10(Q10), .in11(Q11), .in12(Q12), .in13(Q13), .in14(Q14), .in15(Q15), .in16(Q16), .in17(Q17),
    .in18(Q18), .in19(Q19), .in20(Q20), .in21(Q21), .in22(Q22), .in23(Q23), .in24(Q24), .in25(Q25),
    .in26(Q26), .in27(Q27), .in28(Q28), .in29(Q29), .in30(Q30), .in31(Q31), .out(value_1), .sel(source_1));
  Multiplexer #(.select(5), .width(32), .enable("false")) multiplexer_2 (
    .in0({32{1'b0}}), .in1(Q1), .in2(Q2), .in3(Q3), .in4(Q4), .in5(Q5), .in6(Q6), .in7(Q7), .in8(Q8),
    .in9(Q9), .in10(Q10), .in11(Q11), .in12(Q12), .in13(Q13), .in14(Q14), .in15(Q15), .in16(Q16), .in17(Q17),
    .in18(Q18), .in19(Q19), .in20(Q20), .in21(Q21), .in22(Q22), .in23(Q23), .in24(Q24), .in25(Q25),
    .in26(Q26), .in27(Q27), .in28(Q28), .in29(Q29), .in30(Q30), .in31(Q31), .out(value_2), .sel(source_2));

  // Other names for the same wires on the sheet: D[31:0] = \input 

  // Notes on the sheet:
  //   ZERO(R0)
endmodule

module Control_Unit (
  input  [5:0] \function ,
  input  [31:0] vRs,
  input  clk,
  input  rst,
  input  equalBREG,
  input  equalALU,
  input  [5:0] opCode,
  output wBREG,
  output wDM,
  output rDM,
  output cUHW,
  output cU3B,
  output jmpE,
  output link,
  output [1:0] jmpM,
  output halt
);

  wire Branch_Analyzer_jmpe, comparator_1_eq, comparator_3_eq, comparator_4_eq, isAtomic, Link_Analyzer_link,
       not_1_out, not_2_out, or_2_out;

  Comparator #(.width(6)) comparator_1 (.a(\function ), .b(6'b001000), .eq(comparator_1_eq));  // open: gt, lt
  // Probe on opCode
  not not_1 (not_1_out, comparator_1_eq);
  and and_1 (jmpM[1], ~opCode[1], jmpM[0]);  // AND_Gate
  or or_1 (jmpM[0], opCode[2], opCode[1], opCode[0]);
  MUX_opCode_1b mux_opcode_1b_1 (
    .in_1(not_1_out), .in_2(1'b0), .in_3(1'b0), .in_4(1'b1), .in_5(1'b0), .in_6(1'b0), .in_7(1'b0),
    .in_8(1'b0), .in_9(1'b1), .in_10(1'b1), .in_11(1'b1), .in_12(1'b1), .in_13(1'b1), .in_14(1'b1),
    .in_15(1'b0), .in_16(1'b1), .in_17(1'b1), .in_18(1'b0), .in_19(1'b0), .in_20(1'b0), .in_21(1'b0),
    .in_22(1'b0), .in_23(1'b0), .in_24(1'b0), .in_25(1'b0), .in_26(1'b0), .in_27(1'b0), .in_28(1'b0),
    .in_29(1'b0), .in_30(1'b0), .in_31(1'b0), .in_32(1'b0), .sel(opCode), .in_34(1'b0), .in_35(1'b0),
    .in_36(1'b0), .in_37(1'b1), .in_38(1'b1), .in_39(1'b1), .in_40(1'b0), .in_41(1'b0), .in_42(1'b0),
    .in_43(1'b0), .in_44(1'b0), .in_45(1'b0), .in_46(1'b0), .in_47(1'b0), .in_48(1'b0), .in_49(1'b0),
    .in_50(1'b1), .in_51(1'b0), .in_52(1'b0), .in_53(1'b0), .in_54(1'b0), .in_55(1'b0), .in_56(1'b0),
    .in_57(1'b0), .in_58(1'b0), .in_59(1'b0), .in_60(1'b0), .in_61(1'b0), .in_62(1'b0), .in_63(1'b0),
    .in_64(1'b0), .in_65(1'b0), .\output (wBREG));
  Comparator #(.width(6)) comparator_2 (.a(opCode), .b({6{1'b1}}), .eq(halt));  // open: gt, lt
  MUX_opCode_1b mux_opcode_1b_2 (
    .in_1(1'b0), .in_2(1'b0), .in_3(1'b0), .in_4(1'b0), .in_5(1'b0), .in_6(1'b0), .in_7(1'b0), .in_8(1'b0),
    .in_9(1'b0), .in_10(1'b0), .in_11(1'b0), .in_12(1'b0), .in_13(1'b0), .in_14(1'b0), .in_15(1'b0),
    .in_16(1'b0), .in_17(1'b0), .in_18(1'b0), .in_19(1'b0), .in_20(1'b0), .in_21(1'b0), .in_22(1'b0),
    .in_23(1'b0), .in_24(1'b0), .in_25(1'b0), .in_26(1'b0), .in_27(1'b0), .in_28(1'b0), .in_29(1'b0),
    .in_30(1'b0), .in_31(1'b0), .in_32(1'b0), .sel(opCode), .in_34(1'b0), .in_35(1'b0), .in_36(1'b0),
    .in_37(1'b0), .in_38(1'b0), .in_39(1'b0), .in_40(1'b0), .in_41(1'b0), .in_42(1'b1), .in_43(1'b1),
    .in_44(1'b0), .in_45(1'b1), .in_46(1'b0), .in_47(1'b0), .in_48(1'b0), .in_49(1'b0), .in_50(1'b0),
    .in_51(1'b0), .in_52(1'b0), .in_53(1'b0), .in_54(1'b0), .in_55(1'b0), .in_56(1'b0), .in_57(1'b0),
    .in_58(isAtomic), .in_59(1'b0), .in_60(1'b0), .in_61(1'b0), .in_62(1'b0), .in_63(1'b0), .in_64(1'b0),
    .in_65(1'b0), .\output (wDM));
  Comparator #(.width(6)) comparator_3 (.a(6'b110000), .b(opCode), .eq(comparator_3_eq));  // open: gt, lt
  Comparator #(.width(6)) comparator_4 (.a(opCode), .b(6'b111000), .eq(comparator_4_eq));  // open: gt, lt
  or or_2 (or_2_out, rst, 1'b0);
  S_R_Flip_Flop #(.trigger("latch")) s_r_ff_1 (
    .S(comparator_3_eq), .R(comparator_4_eq), .Q(isAtomic), .reset(or_2_out));  // open: Qn, preset
  MUX_opCode_1b mux_opcode_1b_3 (
    .in_1(1'b0), .in_2(1'b0), .in_3(1'b0), .in_4(1'b0), .in_5(1'b0), .in_6(1'b0), .in_7(1'b0), .in_8(1'b0),
    .in_9(1'b0), .in_10(1'b0), .in_11(1'b0), .in_12(1'b0), .in_13(1'b0), .in_14(1'b0), .in_15(1'b0),
    .in_16(1'b0), .in_17(1'b0), .in_18(1'b0), .in_19(1'b0), .in_20(1'b0), .in_21(1'b0), .in_22(1'b0),
    .in_23(1'b0), .in_24(1'b0), .in_25(1'b0), .in_26(1'b0), .in_27(1'b0), .in_28(1'b0), .in_29(1'b0),
    .in_30(1'b0), .in_31(1'b0), .in_32(1'b0), .sel(opCode), .in_34(1'b0), .in_35(1'b0), .in_36(1'b0),
    .in_37(1'b1), .in_38(1'b1), .in_39(1'b1), .in_40(1'b0), .in_41(1'b0), .in_42(1'b0), .in_43(1'b0),
    .in_44(1'b0), .in_45(1'b0), .in_46(1'b0), .in_47(1'b0), .in_48(1'b0), .in_49(1'b0), .in_50(1'b1),
    .in_51(1'b0), .in_52(1'b0), .in_53(1'b0), .in_54(1'b0), .in_55(1'b0), .in_56(1'b0), .in_57(1'b0),
    .in_58(1'b0), .in_59(1'b0), .in_60(1'b0), .in_61(1'b0), .in_62(1'b0), .in_63(1'b0), .in_64(1'b0),
    .in_65(1'b0), .\output (rDM));
  MUX_opCode_1b mux_opcode_1b_4 (
    .in_1(1'b0), .in_2(1'b0), .in_3(1'b0), .in_4(1'b0), .in_5(1'b0), .in_6(1'b0), .in_7(1'b0), .in_8(1'b0),
    .in_9(1'b0), .in_10(1'b0), .in_11(1'b0), .in_12(1'b0), .in_13(1'b0), .in_14(1'b0), .in_15(1'b0),
    .in_16(1'b0), .in_17(1'b0), .in_18(1'b0), .in_19(1'b0), .in_20(1'b0), .in_21(1'b0), .in_22(1'b0),
    .in_23(1'b0), .in_24(1'b0), .in_25(1'b0), .in_26(1'b0), .in_27(1'b0), .in_28(1'b0), .in_29(1'b0),
    .in_30(1'b0), .in_31(1'b0), .in_32(1'b0), .sel(opCode), .in_34(1'b0), .in_35(1'b0), .in_36(1'b0),
    .in_37(1'b0), .in_38(1'b1), .in_39(1'b1), .in_40(1'b0), .in_41(1'b0), .in_42(1'b1), .in_43(1'b1),
    .in_44(1'b0), .in_45(1'b0), .in_46(1'b0), .in_47(1'b0), .in_48(1'b0), .in_49(1'b0), .in_50(1'b0),
    .in_51(1'b0), .in_52(1'b0), .in_53(1'b0), .in_54(1'b0), .in_55(1'b0), .in_56(1'b0), .in_57(1'b0),
    .in_58(1'b0), .in_59(1'b0), .in_60(1'b0), .in_61(1'b0), .in_62(1'b0), .in_63(1'b0), .in_64(1'b0),
    .in_65(1'b0), .\output (cUHW));
  MUX_opCode_1b mux_opcode_1b_5 (
    .in_1(1'b0), .in_2(1'b0), .in_3(1'b0), .in_4(1'b0), .in_5(1'b0), .in_6(1'b0), .in_7(1'b0), .in_8(1'b0),
    .in_9(1'b0), .in_10(1'b0), .in_11(1'b0), .in_12(1'b0), .in_13(1'b0), .in_14(1'b0), .in_15(1'b0),
    .in_16(1'b0), .in_17(1'b0), .in_18(1'b0), .in_19(1'b0), .in_20(1'b0), .in_21(1'b0), .in_22(1'b0),
    .in_23(1'b0), .in_24(1'b0), .in_25(1'b0), .in_26(1'b0), .in_27(1'b0), .in_28(1'b0), .in_29(1'b0),
    .in_30(1'b0), .in_31(1'b0), .in_32(1'b0), .sel(opCode), .in_34(1'b0), .in_35(1'b0), .in_36(1'b0),
    .in_37(1'b0), .in_38(1'b1), .in_39(1'b0), .in_40(1'b0), .in_41(1'b0), .in_42(1'b1), .in_43(1'b0),
    .in_44(1'b0), .in_45(1'b0), .in_46(1'b0), .in_47(1'b0), .in_48(1'b0), .in_49(1'b0), .in_50(1'b0),
    .in_51(1'b0), .in_52(1'b0), .in_53(1'b0), .in_54(1'b0), .in_55(1'b0), .in_56(1'b0), .in_57(1'b0),
    .in_58(1'b0), .in_59(1'b0), .in_60(1'b0), .in_61(1'b0), .in_62(1'b0), .in_63(1'b0), .in_64(1'b0),
    .in_65(1'b0), .\output (cU3B));
  branch_analyzer Branch_Analyzer (.vRs(vRs), .jmpE(Branch_Analyzer_jmpe), .\function (\function ));
  not not_2 (not_2_out, equalBREG);
  MUX_opCode_1b mux_opcode_1b_6 (
    .in_1(comparator_1_eq), .in_2(Branch_Analyzer_jmpe), .in_3(1'b1), .in_4(1'b1), .in_5(equalBREG),
    .in_6(not_2_out), .in_7(1'b0), .in_8(1'b0), .in_9(1'b0), .in_10(1'b0), .in_11(1'b0), .in_12(1'b0),
    .in_13(1'b0), .in_14(1'b0), .in_15(1'b0), .in_16(1'b0), .in_17(1'b0), .in_18(1'b0), .in_19(1'b0),
    .in_20(1'b0), .in_21(1'b0), .in_22(1'b0), .in_23(1'b0), .in_24(1'b0), .in_25(1'b0), .in_26(1'b0),
    .in_27(1'b0), .in_28(1'b0), .in_29(1'b0), .in_30(1'b0), .in_31(1'b0), .in_32(1'b0), .sel(opCode),
    .in_34(1'b0), .in_35(1'b0), .in_36(1'b0), .in_37(1'b0), .in_38(1'b0), .in_39(1'b0), .in_40(1'b0),
    .in_41(1'b0), .in_42(1'b0), .in_43(1'b0), .in_44(1'b0), .in_45(1'b0), .in_46(1'b0), .in_47(1'b0),
    .in_48(1'b0), .in_49(1'b0), .in_50(1'b0), .in_51(1'b0), .in_52(1'b0), .in_53(1'b0), .in_54(1'b0),
    .in_55(1'b0), .in_56(1'b0), .in_57(1'b0), .in_58(1'b0), .in_59(1'b0), .in_60(1'b0), .in_61(1'b0),
    .in_62(1'b0), .in_63(1'b0), .in_64(1'b0), .in_65(1'b0), .\output (jmpE));
  link_analyzer Link_Analyzer (.jmpE(jmpE), .\function (\function ), .link(Link_Analyzer_link));
  MUX_opCode_1b mux_opcode_1b_7 (
    .in_1(1'b0), .in_2(Link_Analyzer_link), .in_3(1'b0), .in_4(1'b1), .in_5(1'b0), .in_6(1'b0), .in_7(1'b0),
    .in_8(1'b0), .in_9(1'b0), .in_10(1'b0), .in_11(1'b0), .in_12(1'b0), .in_13(1'b0), .in_14(1'b0),
    .in_15(1'b0), .in_16(1'b0), .in_17(1'b0), .in_18(1'b0), .in_19(1'b0), .in_20(1'b0), .in_21(1'b0),
    .in_22(1'b0), .in_23(1'b0), .in_24(1'b0), .in_25(1'b0), .in_26(1'b0), .in_27(1'b0), .in_28(1'b0),
    .in_29(1'b0), .in_30(1'b0), .in_31(1'b0), .in_32(1'b0), .sel(opCode), .in_34(1'b0), .in_35(1'b0),
    .in_36(1'b0), .in_37(1'b0), .in_38(1'b0), .in_39(1'b0), .in_40(1'b0), .in_41(1'b0), .in_42(1'b0),
    .in_43(1'b0), .in_44(1'b0), .in_45(1'b0), .in_46(1'b0), .in_47(1'b0), .in_48(1'b0), .in_49(1'b0),
    .in_50(1'b0), .in_51(1'b0), .in_52(1'b0), .in_53(1'b0), .in_54(1'b0), .in_55(1'b0), .in_56(1'b0),
    .in_57(1'b0), .in_58(1'b0), .in_59(1'b0), .in_60(1'b0), .in_61(1'b0), .in_62(1'b0), .in_63(1'b0),
    .in_64(1'b0), .in_65(1'b0), .\output (link));

  // Notes on the sheet:
  //   wBREG:
  //         Write sign to BREG
  //   jmpM:
  //         Jump Mode sign
  //         Write sign to Data Memory
  //   wDM:
  //   Atomicity Warranty
  //   rDM:
  //         Read from Data $Memory to BREG sign
  //   cUHW:
  //   Clear Upper Half-Word on data$ to BREG load and DM store
  //   cU3B:
  //   Clear Upper 3 Bytes on data to $BREG load and DM store
  //         Jump Enable sign
  //   jmpE:
  //   link:
  //   Link sign. Save PC+4 in R31
endmodule

module branch_analyzer (
  input  [31:0] vRs,
  input  [5:0] \function ,
  output jmpE
);

  wire comparator_1_lt;

  Comparator #(.width(32)) comparator_1 (.a(vRs), .b({32{1'b0}}), .lt(comparator_1_lt));  // open: gt, eq
  Multiplexer #(.select(5), .disabled(0), .enable("false")) multiplexer_1 (
    .in0(1'b0), .in1(1'b0), .in2(1'b0), .in3(1'b0), .in4(1'b0), .in5(1'b0), .in6(1'b0), .in7(1'b0),
    .in8(1'b0), .in9(1'b0), .in10(1'b0), .in11(1'b0), .in12(1'b0), .in13(1'b0), .in14(1'b0), .in15(1'b0),
    .in16(comparator_1_lt), .in17(1'b0), .in18(1'b0), .in19(1'b0), .in20(1'b0), .in21(1'b0), .in22(1'b0),
    .in23(1'b0), .in24(1'b0), .in25(1'b0), .in26(1'b0), .in27(1'b0), .in28(1'b0), .in29(1'b0), .in30(1'b0),
    .in31(1'b0), .out(jmpE), .sel(\function [4:0]));

  // Notes on the sheet:
  //   BLTZAL
endmodule

module link_analyzer (
  input  jmpE,
  input  [5:0] \function ,
  output link
);

  Multiplexer #(.select(5), .disabled(0), .enable("false")) multiplexer_1 (
    .in0(1'b0), .in1(1'b0), .in2(1'b0), .in3(1'b0), .in4(1'b0), .in5(1'b0), .in6(1'b0), .in7(1'b0),
    .in8(1'b0), .in9(1'b0), .in10(1'b0), .in11(1'b0), .in12(1'b0), .in13(1'b0), .in14(1'b0), .in15(1'b0),
    .in16(jmpE), .in17(1'b0), .in18(1'b0), .in19(1'b0), .in20(1'b0), .in21(1'b0), .in22(1'b0), .in23(1'b0),
    .in24(1'b0), .in25(1'b0), .in26(1'b0), .in27(1'b0), .in28(1'b0), .in29(1'b0), .in30(1'b0), .in31(1'b0),
    .out(link), .sel(\function [4:0]));

  // Notes on the sheet:
  //   BLTZAL
endmodule
module MIPS_Panel (
  input  btControl,
  input  btRun,
  input  btStep,
  input  btReset,
  input  btExtra,
  input  clk,
  input  rst,
  input  [31:0] IM,
  output IF,
  output ID,
  output EX,
  output MEM,
  output WB,
  output out_14,
  output out_15,
  output out_16,
  output out_17,
  output out_18,
  output out_19,
  output out_20,
  output clkO,
  output rstO,
  output [4:0] IM0___L0,
  output [4:0] IM1___L0,
  output [4:0] IM2___L0,
  output [4:0] IM3___L0,
  output [4:0] A0_L0,
  output [4:0] A1_L0,
  output [4:0] A2_L0,
  output [4:0] A3_L0,
  output [4:0] IM4___L1,
  output [4:0] IM5___L1,
  output [4:0] RS0___L0,
  output [4:0] IM6___L1,
  output [4:0] RS1___L0,
  output [4:0] IM7___L1,
  output [4:0] I0___L0,
  output [4:0] RS2___L0,
  output [4:0] I1___L0,
  output [4:0] RS3___L0,
  output [4:0] I2___L0,
  output [4:0] I3___L0,
  output [4:0] A4_L1,
  output [4:0] A5_L1,
  output [4:0] A6_L1,
  output [4:0] A7_L1,
  output [4:0] RS4___L1,
  output [4:0] IM9___L2,
  output [4:0] RS5___L1,
  output [4:0] IM10___L2,
  output [4:0] I4___L1,
  output [4:0] RS6___L1,
  output [4:0] IM11___L3,
  output [4:0] I5___L1,
  output [4:0] RS7___L1,
  output [4:0] IM12___L2,
  output [4:0] I6___L1,
  output [4:0] I7___L1,
  output [4:0] A8_L2,
  output [4:0] A9_L2,
  output [4:0] A10_L2,
  output [4:0] A11_L2,
  output [4:0] I13___L3,
  output [4:0] I9___L2,
  output [4:0] I14___L3,
  output [4:0] I10___L2,
  output [4:0] I15___L3,
  output [4:0] I11___L3,
  output [4:0] I16___L3,
  output [4:0] I12___L2,
  output [4:0] I13___L3_2,
  output [4:0] I14___L3_2,
  output [4:0] I15___L3_2,
  output [4:0] A12_L3,
  output [4:0] I16___L3_2,
  output [4:0] A13_L3,
  output [4:0] A14_L3,
  output [4:0] A15_L3,
  output [4:0] A16_L4,
  output [4:0] A17_L4,
  output [4:0] A18_L4,
  output [4:0] RT___L0,
  output [4:0] A19__L4,
  output [4:0] RT1___L0,
  output [4:0] I17___L5,
  output [4:0] RT2___L0,
  output [4:0] I18___L4,
  output [4:0] RT3___L0,
  output [4:0] I19___L5,
  output [4:0] I20___L4,
  output [4:0] RT4___L1,
  output [4:0] RT5___L1,
  output [4:0] RT6___L1,
  output [4:0] RT7___L1,
  output [4:0] A20_L5,
  output [4:0] A21_L5,
  output [4:0] A22_L5,
  output [4:0] A23_L5,
  output [4:0] A24_L5,
  output [4:0] A25_L5,
  output [4:0] A26_L5,
  output [4:0] A27_L5,
  output [4:0] A28_L5,
  output [4:0] A29_L5,
  output [4:0] A30_L5,
  output [4:0] A31_L5,
  output [4:0] RD0___L0,
  output [4:0] RD1___L0,
  output [4:0] RD2___L0,
  output [4:0] RD3___L0,
  output [4:0] RD4___L1,
  output [4:0] RD5___L1,
  output [4:0] RD6___L1,
  output [4:0] RD7___L1,
  output [4:0] SH0___L0,
  output [4:0] SH1___L0,
  output [4:0] SH2___L0,
  output [4:0] SH3___L0,
  output [4:0] SH4___L1,
  output [4:0] SH5___L1,
  output [4:0] SH6___L1,
  output [4:0] SH7___L1
);

  wire and_1_out, button_1_out, button_2_out, clock_1_out, comparator_1_eq, comparator_2_eq, comparator_3_eq,
       controlled_buffer_1_out, d_ff_1_qn, d_ff_2_q, d_ff_2_qn, multiplexer_7_out, mux_funct_1b_1_output,
       mux_funct_1b_2_output, mux_funct_1b_3_output, mux_opcode_1b_1_output, mux_opcode_1b_2_output,
       mux_opcode_1b_3_output, mux_opcode_1b_4_output, not_1_out, or_1_out, rst_t, xor_1_out;
  wire [1:0] mux_opcode_2b_1_output, undriven_2;
  wire [2:0] counter_2_q;
  wire [4:0] letter_matriz_decode_8_output_0, letter_matriz_decode_8_output_1,
       letter_matriz_decode_8_output_2, letter_matriz_decode_8_output_3;
  wire [5:0] buffer_1_out;
  wire [7:0] counter_1_q, multiplexer_1_out, multiplexer_2_out, multiplexer_4_out, multiplexer_5_out,
       multiplexer_6_out, multiplexer_13_out, multiplexer_14_out, multiplexer_15_out, multiplexer_16_out,
       multiplexer_17_out, multiplexer_18_out, multiplexer_19_out, multiplexer_20_out, multiplexer_21_out,
       multiplexer_22_out, multiplexer_23_out, multiplexer_24_out, multiplexer_25_out, multiplexer_26_out,
       mux_funct_8b_1_output, mux_opcode_8b_1_output;
  wire [15:0] multiplexer_10_out, multiplexer_11_out, multiplexer_12_out,
       n2_letters_merge_interface_1_word_4_letters, n2_letters_merge_interface_2_word_4_letters,
       n2_letters_merge_interface_3_word_4_letters, n2_letters_merge_interface_4_word_4_letters,
       n2_letters_merge_interface_5_word_4_letters, n2_letters_merge_interface_6_word_4_letters,
       n2_letters_merge_interface_7_word_4_letters, n2_letters_merge_interface_8_word_4_letters,
       n2_letters_merge_interface_9_word_4_letters, n2_letters_merge_interface_10_word_4_letters,
       n2_letters_merge_interface_11_word_4_letters, n2_letters_merge_interface_12_word_4_letters,
       n2_letters_merge_interface_13_word_4_letters, n2_letters_merge_interface_14_word_4_letters,
       n2_letters_merge_interface_15_word_4_letters, n2_letters_merge_interface_16_word_4_letters,
       n2_letters_merge_interface_17_word_4_letters, n2_letters_merge_interface_18_word_4_letters,
       n2_letters_merge_interface_19_word_4_letters, n2_letters_merge_interface_20_word_4_letters,
       n2_letters_merge_interface_21_word_4_letters, n2_letters_merge_interface_22_word_4_letters,
       n2_letters_merge_interface_23_word_4_letters, n2_letters_merge_interface_24_word_4_letters,
       n2_letters_merge_interface_25_word_4_letters, n2_letters_merge_interface_26_word_4_letters,
       n2_letters_merge_interface_27_word_4_letters, n2_letters_merge_interface_28_word_4_letters,
       n2_letters_merge_interface_29_word_4_letters, n2_letters_merge_interface_30_word_4_letters,
       n2_letters_merge_interface_31_word_4_letters, n2_letters_merge_interface_32_word_4_letters,
       n2_letters_merge_interface_33_word_4_letters, n2_letters_merge_interface_34_word_4_letters,
       n2_letters_merge_interface_35_word_4_letters, n2_letters_merge_interface_36_word_4_letters,
       n2_letters_merge_interface_37_word_4_letters, n2_letters_merge_interface_38_word_4_letters,
       n2_letters_merge_interface_39_word_4_letters, n2_letters_merge_interface_40_word_4_letters,
       n2_letters_merge_interface_41_word_4_letters, n2_letters_merge_interface_42_word_4_letters,
       n2_letters_merge_interface_43_word_4_letters, n2_letters_merge_interface_44_word_4_letters,
       n2_letters_merge_interface_45_word_4_letters, n2_letters_merge_interface_46_word_4_letters,
       n2_letters_merge_interface_47_word_4_letters, n2_letters_merge_interface_48_word_4_letters,
       n2_letters_merge_interface_49_word_4_letters, n2_letters_merge_interface_50_word_4_letters,
       n2_letters_merge_interface_51_word_4_letters, n2_letters_merge_interface_52_word_4_letters,
       n2_letters_merge_interface_53_word_4_letters, n2_letters_merge_interface_54_word_4_letters,
       n2_letters_merge_interface_55_word_4_letters, n2_letters_merge_interface_56_word_4_letters,
       n2_letters_merge_interface_57_word_4_letters, n2_letters_merge_interface_58_word_4_letters,
       n2_letters_merge_interface_59_word_4_letters, n2_letters_merge_interface_60_word_4_letters,
       n2_letters_merge_interface_61_word_4_letters, n2_letters_merge_interface_62_word_4_letters,
       n2_letters_merge_interface_63_word_4_letters, n2_letters_merge_interface_64_word_4_letters,
       n2_letters_merge_interface_65_word_4_letters, n2_letters_merge_interface_66_word_4_letters,
       n2_letters_merge_interface_67_word_4_letters, n2_letters_merge_interface_68_word_4_letters,
       n2_letters_merge_interface_69_word_4_letters, n2_letters_merge_interface_70_word_4_letters,
       n2_letters_merge_interface_71_word_4_letters, n2_letters_merge_interface_72_word_4_letters,
       n2_letters_merge_interface_73_word_4_letters, n2_letters_merge_interface_74_word_4_letters,
       n2_letters_merge_interface_75_word_4_letters, n2_letters_merge_interface_76_word_4_letters,
       n2_letters_merge_interface_77_word_4_letters, n2_letters_merge_interface_78_word_4_letters,
       n2_letters_merge_interface_79_word_4_letters, n2_letters_merge_interface_80_word_4_letters,
       n2_letters_merge_interface_81_word_4_letters, n2_letters_merge_interface_82_word_4_letters,
       n2_letters_merge_interface_83_word_4_letters, n2_letters_merge_interface_84_word_4_letters,
       n2_letters_merge_interface_85_word_4_letters, n2_letters_merge_interface_86_word_4_letters,
       n2_letters_merge_interface_87_word_4_letters, n2_letters_merge_interface_88_word_4_letters,
       n2_letters_merge_interface_89_word_4_letters, n2_letters_merge_interface_90_word_4_letters,
       n2_letters_merge_interface_91_word_4_letters, n2_letters_merge_interface_92_word_4_letters,
       n2_letters_merge_interface_93_word_4_letters, n2_letters_merge_interface_94_word_4_letters,
       n2_letters_merge_interface_95_word_4_letters, n2_letters_merge_interface_96_word_4_letters;
  wire [31:0] multiplexer_3_out, multiplexer_27_out, multiplexer_28_out, multiplexer_29_out,
       multiplexer_30_out, multiplexer_31_out, multiplexer_32_out, multiplexer_33_out, multiplexer_34_out,
       multiplexer_35_out, mux_funct_32b_1_output, mux_opcode_32b_1_output,
       n4_letters_merge_interface_1_word_4_letters, n4_letters_merge_interface_2_word_4_letters,
       n4_letters_merge_interface_3_word_4_letters, n4_letters_merge_interface_4_word_4_letters,
       n4_letters_merge_interface_5_word_4_letters, n4_letters_merge_interface_6_word_4_letters,
       n4_letters_merge_interface_7_word_4_letters, n4_letters_merge_interface_8_word_4_letters,
       n4_letters_merge_interface_9_word_4_letters, n4_letters_merge_interface_10_word_4_letters,
       n4_letters_merge_interface_11_word_4_letters, n4_letters_merge_interface_12_word_4_letters,
       n4_letters_merge_interface_13_word_4_letters, n4_letters_merge_interface_14_word_4_letters,
       n4_letters_merge_interface_15_word_4_letters, n4_letters_merge_interface_16_word_4_letters,
       n4_letters_merge_interface_17_word_4_letters, n4_letters_merge_interface_18_word_4_letters,
       n4_letters_merge_interface_19_word_4_letters, n4_letters_merge_interface_20_word_4_letters,
       n4_letters_merge_interface_21_word_4_letters, n4_letters_merge_interface_22_word_4_letters,
       n4_letters_merge_interface_23_word_4_letters, n4_letters_merge_interface_24_word_4_letters,
       n4_letters_merge_interface_25_word_4_letters, n4_letters_merge_interface_26_word_4_letters,
       n4_letters_merge_interface_27_word_4_letters, n4_letters_merge_interface_28_word_4_letters,
       n4_letters_merge_interface_29_word_4_letters, n4_letters_merge_interface_30_word_4_letters,
       n4_letters_merge_interface_31_word_4_letters, n4_letters_merge_interface_32_word_4_letters,
       n4_letters_merge_interface_33_word_4_letters, n4_letters_merge_interface_34_word_4_letters,
       n4_letters_merge_interface_35_word_4_letters, n4_letters_merge_interface_36_word_4_letters,
       n4_letters_merge_interface_37_word_4_letters, n4_letters_merge_interface_38_word_4_letters, RD_L0,
       RD_L1, rom_1_data, rom_2_data, rom_3_data, rom_4_data, rom_5_data, rom_6_data, rom_7_data, rom_8_data,
       rom_15_data, rom_16_data, rom_17_data, rom_18_data, RS_L0, RS_L1, RT_L0, RT_L1, undriven;

  _4_letters_merge_interface u_4_letters_merge_interface_1 (
    .letter_1(8'h44), .letter_2(8'h44), .word_4_letters(n4_letters_merge_interface_1_word_4_letters),
    .letter_3(8'h41), .letter_0(8'h55));
  _4_letters_merge_interface u_4_letters_merge_interface_2 (
    .letter_1(8'h42), .letter_2(8'h55), .word_4_letters(n4_letters_merge_interface_2_word_4_letters),
    .letter_3(8'h53), .letter_0(8'h55));
  _4_letters_merge_interface u_4_letters_merge_interface_3 (
    .letter_1(8'h52), .letter_2(8'h4f), .word_4_letters(n4_letters_merge_interface_3_word_4_letters),
    .letter_3(8'h20), .letter_0(8'h20));
  _4_letters_merge_interface u_4_letters_merge_interface_4 (
    .letter_1(8'h54), .letter_2(8'h4c), .word_4_letters(n4_letters_merge_interface_4_word_4_letters),
    .letter_3(8'h53), .letter_0(8'h55));
  _4_letters_merge_interface u_4_letters_merge_interface_5 (
    .letter_1(8'h4c), .letter_2(8'h4c), .word_4_letters(n4_letters_merge_interface_5_word_4_letters),
    .letter_3(8'h53), .letter_0(8'h20));
  _4_letters_merge_interface u_4_letters_merge_interface_6 (
    .letter_1(8'h4c), .letter_2(8'h52), .word_4_letters(n4_letters_merge_interface_6_word_4_letters),
    .letter_3(8'h53), .letter_0(8'h20));
  _4_letters_merge_interface u_4_letters_merge_interface_7 (
    .letter_1(8'h52), .letter_2(8'h4a), .word_4_letters(n4_letters_merge_interface_7_word_4_letters),
    .letter_3(8'h20), .letter_0(8'h20));
  _4_letters_merge_interface u_4_letters_merge_interface_8 (
    .letter_1(8'h48), .letter_2(8'h46), .word_4_letters(n4_letters_merge_interface_8_word_4_letters),
    .letter_3(8'h4d), .letter_0(8'h49));
  _4_letters_merge_interface u_4_letters_merge_interface_9 (
    .letter_1(8'h4c), .letter_2(8'h46), .word_4_letters(n4_letters_merge_interface_9_word_4_letters),
    .letter_3(8'h4d), .letter_0(8'h4f));
  _4_letters_merge_interface u_4_letters_merge_interface_10 (
    .letter_1(8'h4c), .letter_2(8'h55), .word_4_letters(n4_letters_merge_interface_10_word_4_letters),
    .letter_3(8'h4d), .letter_0(8'h54));
  _4_letters_merge_interface u_4_letters_merge_interface_11 (
    .letter_1(8'h44), .letter_2(8'h44), .word_4_letters(n4_letters_merge_interface_11_word_4_letters),
    .letter_3(8'h41), .letter_0(8'h20));
  _4_letters_merge_interface u_4_letters_merge_interface_12 (
    .letter_1(8'h42), .letter_2(8'h55), .word_4_letters(n4_letters_merge_interface_12_word_4_letters),
    .letter_3(8'h53), .letter_0(8'h20));
  _4_letters_merge_interface u_4_letters_merge_interface_13 (
    .letter_1(8'h44), .letter_2(8'h4e), .word_4_letters(n4_letters_merge_interface_13_word_4_letters),
    .letter_3(8'h41), .letter_0(8'h20));
  _4_letters_merge_interface u_4_letters_merge_interface_14 (
    .letter_1(8'h52), .letter_2(8'h4f), .word_4_letters(n4_letters_merge_interface_14_word_4_letters),
    .letter_3(8'h4e), .letter_0(8'h20));
  _4_letters_merge_interface u_4_letters_merge_interface_15 (
    .letter_1(8'h54), .letter_2(8'h4c), .word_4_letters(n4_letters_merge_interface_15_word_4_letters),
    .letter_3(8'h53), .letter_0(8'h20));
  _4_letters_merge_interface u_4_letters_merge_interface_16 (
    .letter_1(8'h54), .letter_2(8'h4c), .word_4_letters(n4_letters_merge_interface_16_word_4_letters),
    .letter_3(8'h42), .letter_0(8'h5a));
  _4_letters_merge_interface u_4_letters_merge_interface_17 (
    .letter_1(8'h50), .letter_2(8'h4f), .word_4_letters(n4_letters_merge_interface_17_word_4_letters),
    .letter_3(8'h4e), .letter_0(8'h20));
  Comparator #(.width(6)) comparator_1 (.a({6{1'b0}}), .b(IM[5:0]), .eq(comparator_1_eq));  // open: gt, lt
  Comparator #(.width(6)) comparator_2 (.a(IM[5:0]), .b(6'b000001), .eq(comparator_2_eq));  // open: gt, lt
  Comparator #(.width(6)) comparator_3 (.a(IM[31:26]), .b({6{1'b0}}), .eq(comparator_3_eq));  // open: gt, lt
  Multiplexer #(.width(8), .enable("false")) multiplexer_1 (
    .in0(8'h30), .in1(8'h31), .out(multiplexer_1_out), .sel(IM[10]));
  Multiplexer #(.select(4), .width(8), .enable("false")) multiplexer_2 (
    .in0(8'h30), .in1(8'h31), .in2(8'h32), .in3(8'h33), .in4(8'h34), .in5(8'h35), .in6(8'h36), .in7(8'h37),
    .in8(8'h38), .in9(8'h39), .in10(8'h41), .in11(8'h42), .in12(8'h43), .in13(8'h44), .in14(8'h45),
    .in15(8'h46), .out(multiplexer_2_out), .sel(IM[9:6]));
  D_Flip_Flop d_ff_1 (.clk(btControl), .D(d_ff_1_qn), .Q(out_14), .Qn(d_ff_1_qn), .preset(1'b0), .reset(1'b0));
  D_Flip_Flop d_ff_2 (.clk(btRun), .D(d_ff_2_qn), .Q(d_ff_2_q), .Qn(d_ff_2_qn), .preset(1'b0), .reset(btStep));
  assign controlled_buffer_1_out = d_ff_2_q ? clock_1_out : 1'bz;  // Controlled_Buffer controlled_buffer_1
  Clock clock_1 (.out(clock_1_out));
  MUX_funct_32b mux_funct_32b_1 (
    .in_1(n4_letters_merge_interface_5_word_4_letters), .in_2(n4_letters_merge_interface_17_word_4_letters),
    .in_3(n4_letters_merge_interface_6_word_4_letters), .in_4(n4_letters_merge_interface_17_word_4_letters),
    .in_5(n4_letters_merge_interface_17_word_4_letters), .in_6(n4_letters_merge_interface_17_word_4_letters),
    .in_7(n4_letters_merge_interface_17_word_4_letters), .in_8(n4_letters_merge_interface_17_word_4_letters),
    .in_9(n4_letters_merge_interface_7_word_4_letters), .in_10(n4_letters_merge_interface_17_word_4_letters),
    .in_11(n4_letters_merge_interface_17_word_4_letters),
    .in_12(n4_letters_merge_interface_17_word_4_letters),
    .in_13(n4_letters_merge_interface_17_word_4_letters),
    .in_14(n4_letters_merge_interface_17_word_4_letters),
    .in_15(n4_letters_merge_interface_17_word_4_letters),
    .in_16(n4_letters_merge_interface_17_word_4_letters),
    .in_17(n4_letters_merge_interface_8_word_4_letters),
    .in_18(n4_letters_merge_interface_17_word_4_letters),
    .in_19(n4_letters_merge_interface_9_word_4_letters),
    .in_20(n4_letters_merge_interface_17_word_4_letters),
    .in_21(n4_letters_merge_interface_17_word_4_letters),
    .in_22(n4_letters_merge_interface_17_word_4_letters),
    .in_23(n4_letters_merge_interface_17_word_4_letters),
    .in_24(n4_letters_merge_interface_17_word_4_letters),
    .in_25(n4_letters_merge_interface_10_word_4_letters),
    .in_26(n4_letters_merge_interface_17_word_4_letters),
    .in_27(n4_letters_merge_interface_17_word_4_letters),
    .in_28(n4_letters_merge_interface_17_word_4_letters),
    .in_29(n4_letters_merge_interface_17_word_4_letters),
    .in_30(n4_letters_merge_interface_17_word_4_letters),
    .in_31(n4_letters_merge_interface_17_word_4_letters),
    .in_32(n4_letters_merge_interface_17_word_4_letters), .sel(IM[5:0]),
    .in_34(n4_letters_merge_interface_11_word_4_letters),
    .in_35(n4_letters_merge_interface_1_word_4_letters),
    .in_36(n4_letters_merge_interface_12_word_4_letters),
    .in_37(n4_letters_merge_interface_2_word_4_letters),
    .in_38(n4_letters_merge_interface_13_word_4_letters),
    .in_39(n4_letters_merge_interface_3_word_4_letters),
    .in_40(n4_letters_merge_interface_17_word_4_letters),
    .in_41(n4_letters_merge_interface_14_word_4_letters),
    .in_42(n4_letters_merge_interface_17_word_4_letters),
    .in_43(n4_letters_merge_interface_17_word_4_letters),
    .in_44(n4_letters_merge_interface_15_word_4_letters),
    .in_45(n4_letters_merge_interface_4_word_4_letters),
    .in_46(n4_letters_merge_interface_17_word_4_letters),
    .in_47(n4_letters_merge_interface_17_word_4_letters),
    .in_48(n4_letters_merge_interface_17_word_4_letters),
    .in_49(n4_letters_merge_interface_17_word_4_letters),
    .in_50(n4_letters_merge_interface_17_word_4_letters),
    .in_51(n4_letters_merge_interface_17_word_4_letters),
    .in_52(n4_letters_merge_interface_17_word_4_letters),
    .in_53(n4_letters_merge_interface_17_word_4_letters),
    .in_54(n4_letters_merge_interface_17_word_4_letters),
    .in_55(n4_letters_merge_interface_17_word_4_letters),
    .in_56(n4_letters_merge_interface_17_word_4_letters),
    .in_57(n4_letters_merge_interface_17_word_4_letters),
    .in_58(n4_letters_merge_interface_17_word_4_letters),
    .in_59(n4_letters_merge_interface_17_word_4_letters),
    .in_60(n4_letters_merge_interface_17_word_4_letters),
    .in_61(n4_letters_merge_interface_17_word_4_letters),
    .in_62(n4_letters_merge_interface_17_word_4_letters),
    .in_63(n4_letters_merge_interface_17_word_4_letters),
    .in_64(n4_letters_merge_interface_17_word_4_letters),
    .in_65(n4_letters_merge_interface_17_word_4_letters), .\output (mux_funct_32b_1_output));
  // Probe on IM[5:0]
  Multiplexer #(.select(5), .width(32), .enable("false")) multiplexer_3 (
    .in0(n4_letters_merge_interface_17_word_4_letters), .in1(n4_letters_merge_interface_17_word_4_letters),
    .in2(n4_letters_merge_interface_17_word_4_letters), .in3(n4_letters_merge_interface_17_word_4_letters),
    .in4(n4_letters_merge_interface_17_word_4_letters), .in5(n4_letters_merge_interface_17_word_4_letters),
    .in6(n4_letters_merge_interface_17_word_4_letters), .in7(n4_letters_merge_interface_17_word_4_letters),
    .in8(n4_letters_merge_interface_17_word_4_letters), .in9(n4_letters_merge_interface_17_word_4_letters),
    .in10(n4_letters_merge_interface_17_word_4_letters), .in11(n4_letters_merge_interface_17_word_4_letters),
    .in12(n4_letters_merge_interface_17_word_4_letters), .in13(n4_letters_merge_interface_17_word_4_letters),
    .in14(n4_letters_merge_interface_17_word_4_letters), .in15(n4_letters_merge_interface_17_word_4_letters),
    .in16(n4_letters_merge_interface_16_word_4_letters), .in17(n4_letters_merge_interface_17_word_4_letters),
    .in18(n4_letters_merge_interface_17_word_4_letters), .in19(n4_letters_merge_interface_17_word_4_letters),
    .in20(n4_letters_merge_interface_17_word_4_letters), .in21(n4_letters_merge_interface_17_word_4_letters),
    .in22(n4_letters_merge_interface_17_word_4_letters), .in23(n4_letters_merge_interface_17_word_4_letters),
    .in24(n4_letters_merge_interface_17_word_4_letters), .in25(n4_letters_merge_interface_17_word_4_letters),
    .in26(n4_letters_merge_interface_17_word_4_letters), .in27(n4_letters_merge_interface_17_word_4_letters),
    .in28(n4_letters_merge_interface_17_word_4_letters), .in29(n4_letters_merge_interface_17_word_4_letters),
    .in30(n4_letters_merge_interface_17_word_4_letters), .in31(n4_letters_merge_interface_17_word_4_letters),
    .out(multiplexer_3_out), .sel(IM[20:16]));
  MUX_funct_8b mux_funct_8b_1 (
    .in_1(8'h20), .in_2(8'h20), .in_3(8'h20), .in_4(8'h20), .in_5(8'h20), .in_6(8'h20), .in_7(8'h20),
    .in_8(8'h20), .in_9(8'h20), .in_10(8'h20), .in_11(8'h20), .in_12(8'h20), .in_13(8'h20), .in_14(8'h20),
    .in_15(8'h20), .in_16(8'h20), .in_17(8'h20), .in_18(8'h20), .in_19(8'h20), .in_20(8'h20), .in_21(8'h20),
    .in_22(8'h20), .in_23(8'h20), .in_24(8'h20), .in_25(8'h20), .in_26(8'h20), .in_27(8'h20), .in_28(8'h20),
    .in_29(8'h20), .in_30(8'h20), .in_31(8'h20), .in_32(8'h20), .sel(IM[5:0]), .in_34(8'h20), .in_35(8'h20),
    .in_36(8'h20), .in_37(8'h20), .in_38(8'h20), .in_39(8'h20), .in_40(8'h20), .in_41(8'h20), .in_42(8'h20),
    .in_43(8'h20), .in_44(8'h20), .in_45(8'h20), .in_46(8'h20), .in_47(8'h20), .in_48(8'h20), .in_49(8'h20),
    .in_50(8'h20), .in_51(8'h20), .in_52(8'h20), .in_53(8'h20), .in_54(8'h20), .in_55(8'h20), .in_56(8'h20),
    .in_57(8'h20), .in_58(8'h20), .in_59(8'h20), .in_60(8'h20), .in_61(8'h20), .in_62(8'h20), .in_63(8'h20),
    .in_64(8'h20), .\output (mux_funct_8b_1_output));  // open: in_65
  Multiplexer #(.select(5), .width(8), .enable("false")) multiplexer_4 (
    .in0(8'h20), .in1(8'h20), .in2(8'h20), .in3(8'h20), .in4(8'h20), .in5(8'h20), .in6(8'h20), .in7(8'h20),
    .in8(8'h20), .in9(8'h20), .in10(8'h20), .in11(8'h20), .in12(8'h20), .in13(8'h20), .in14(8'h20),
    .in15(8'h20), .in16(8'h4c), .in17(8'h20), .in18(8'h20), .in19(8'h20), .in20(8'h20), .in21(8'h20),
    .in22(8'h20), .in23(8'h20), .in24(8'h20), .in25(8'h20), .in26(8'h20), .in27(8'h20), .in28(8'h20),
    .in29(8'h20), .in30(8'h20), .in31(8'h20), .out(multiplexer_4_out), .sel(IM[20:16]));
  or or_1 (or_1_out, comparator_1_eq, comparator_2_eq);
  and and_1 (and_1_out, or_1_out, comparator_3_eq);
  assign out_15 = out_14 ? d_ff_2_q : 1'bz;  // Controlled_Buffer controlled_buffer_2
  assign out_16 = out_14 ? btStep : 1'bz;  // Controlled_Buffer controlled_buffer_3
  assign out_17 = out_14 ? btReset : 1'bz;  // Controlled_Buffer controlled_buffer_4
  assign out_18 = out_14 ? btExtra : 1'bz;  // Controlled_Buffer controlled_buffer_5
  assign out_19 = ~out_14 ? clk : 1'bz;  // Controlled_Buffer controlled_buffer_6
  assign out_20 = ~out_14 ? rst : 1'bz;  // Controlled_Buffer controlled_buffer_7
  // Probe on multiplexer_3_out
  Multiplexer #(.width(8), .enable("false")) multiplexer_5 (
    .in0(8'h2d), .in1(multiplexer_1_out), .out(multiplexer_5_out), .sel(and_1_out));
  Multiplexer #(.width(8), .enable("false")) multiplexer_6 (
    .in0(8'h2d), .in1(multiplexer_2_out), .out(multiplexer_6_out), .sel(and_1_out));
  _4_letters_merge_interface u_4_letters_merge_interface_18 (
    .letter_1(8'h4c), .letter_2(8'h41), .word_4_letters(n4_letters_merge_interface_18_word_4_letters),
    .letter_3(8'h4a), .letter_0(8'h20));
  _4_letters_merge_interface u_4_letters_merge_interface_19 (
    .letter_1(8'h45), .letter_2(8'h4e), .word_4_letters(n4_letters_merge_interface_19_word_4_letters),
    .letter_3(8'h42), .letter_0(8'h20));
  _4_letters_merge_interface u_4_letters_merge_interface_20 (
    .letter_1(8'h44), .letter_2(8'h44), .word_4_letters(n4_letters_merge_interface_20_word_4_letters),
    .letter_3(8'h41), .letter_0(8'h49));
  _4_letters_merge_interface u_4_letters_merge_interface_21 (
    .letter_1(8'h54), .letter_2(8'h4c), .word_4_letters(n4_letters_merge_interface_21_word_4_letters),
    .letter_3(8'h53), .letter_0(8'h49));
  _4_letters_merge_interface u_4_letters_merge_interface_22 (
    .letter_1(8'h49), .letter_2(8'h52), .word_4_letters(n4_letters_merge_interface_22_word_4_letters),
    .letter_3(8'h4f), .letter_0(8'h20));
  _4_letters_merge_interface u_4_letters_merge_interface_23 (
    .letter_1(8'h43), .letter_2(8'h46), .word_4_letters(n4_letters_merge_interface_23_word_4_letters),
    .letter_3(8'h4d), .letter_0(8'h30));
  _4_letters_merge_interface u_4_letters_merge_interface_24 (
    .letter_1(8'h55), .letter_2(8'h42), .word_4_letters(n4_letters_merge_interface_24_word_4_letters),
    .letter_3(8'h20), .letter_0(8'h20));
  _4_letters_merge_interface u_4_letters_merge_interface_25 (
    .letter_1(8'h48), .letter_2(8'h53), .word_4_letters(n4_letters_merge_interface_25_word_4_letters),
    .letter_3(8'h20), .letter_0(8'h20));
  Multiplexer #(.enable("false")) multiplexer_7 (
    .in0(btStep), .in1(controlled_buffer_1_out), .out(multiplexer_7_out), .sel(d_ff_2_q));
  not not_1 (not_1_out, out_14);
  Multiplexer #(.enable("false")) multiplexer_8 (.in0(multiplexer_7_out), .in1(clk), .out(clkO), .sel(not_1_out));
  Multiplexer #(.enable("false")) multiplexer_9 (.in0(btReset), .in1(rst), .out(rstO), .sel(not_1_out));
  _4_letters_merge_interface u_4_letters_merge_interface_26 (
    .letter_1(8'h20), .letter_2(8'h4a), .word_4_letters(n4_letters_merge_interface_26_word_4_letters),
    .letter_3(8'h20), .letter_0(8'h20));
  _4_letters_merge_interface u_4_letters_merge_interface_27 (
    .letter_1(8'h51), .letter_2(8'h45), .word_4_letters(n4_letters_merge_interface_27_word_4_letters),
    .letter_3(8'h42), .letter_0(8'h20));
  _4_letters_merge_interface u_4_letters_merge_interface_28 (
    .letter_1(8'h44), .letter_2(8'h44), .word_4_letters(n4_letters_merge_interface_28_word_4_letters),
    .letter_3(8'h41), .letter_0(8'h49));
  _4_letters_merge_interface u_4_letters_merge_interface_29 (
    .letter_1(8'h54), .letter_2(8'h4c), .word_4_letters(n4_letters_merge_interface_29_word_4_letters),
    .letter_3(8'h53), .letter_0(8'h49));
  _4_letters_merge_interface u_4_letters_merge_interface_30 (
    .letter_1(8'h44), .letter_2(8'h4e), .word_4_letters(n4_letters_merge_interface_30_word_4_letters),
    .letter_3(8'h41), .letter_0(8'h49));
  _4_letters_merge_interface u_4_letters_merge_interface_31 (
    .letter_1(8'h49), .letter_2(8'h55), .word_4_letters(n4_letters_merge_interface_31_word_4_letters),
    .letter_3(8'h4c), .letter_0(8'h20));
  _4_letters_merge_interface u_4_letters_merge_interface_32 (
    .letter_1(8'h57), .letter_2(8'h4c), .word_4_letters(n4_letters_merge_interface_32_word_4_letters),
    .letter_3(8'h20), .letter_0(8'h20));
  _4_letters_merge_interface u_4_letters_merge_interface_33 (
    .letter_1(8'h55), .letter_2(8'h48), .word_4_letters(n4_letters_merge_interface_33_word_4_letters),
    .letter_3(8'h20), .letter_0(8'h20));
  _4_letters_merge_interface u_4_letters_merge_interface_34 (
    .letter_1(8'h42), .letter_2(8'h53), .word_4_letters(n4_letters_merge_interface_34_word_4_letters),
    .letter_3(8'h20), .letter_0(8'h20));
  _4_letters_merge_interface u_4_letters_merge_interface_35 (
    .letter_1(8'h57), .letter_2(8'h53), .word_4_letters(n4_letters_merge_interface_35_word_4_letters),
    .letter_3(8'h20), .letter_0(8'h20));
  _4_letters_merge_interface u_4_letters_merge_interface_36 (
    .letter_1(8'h4c), .letter_2(8'h4c), .word_4_letters(n4_letters_merge_interface_36_word_4_letters),
    .letter_3(8'h20), .letter_0(8'h20));
  _4_letters_merge_interface u_4_letters_merge_interface_37 (
    .letter_1(8'h43), .letter_2(8'h53), .word_4_letters(n4_letters_merge_interface_37_word_4_letters),
    .letter_3(8'h20), .letter_0(8'h20));
  ROM #(.dataWidth(32), .Select("low")) rom_1 (.addr(multiplexer_5_out), .data(rom_1_data));
  ROM #(.dataWidth(32), .Select("low")) rom_2 (.addr(multiplexer_6_out), .data(rom_2_data));
  _4_letters_merge_interface u_4_letters_merge_interface_38 (
    .letter_1(8'h50), .letter_2(8'h4f), .word_4_letters(n4_letters_merge_interface_38_word_4_letters),
    .letter_3(8'h4e), .letter_0(8'h20));
  assign buffer_1_out = IM[31:26];  // Buffer buffer_1, 6 bits wide
  // Probe on IM[31:26]
  DotMatrix #(.matrixcols(4), .matrixrows(5)) dotmatrix_1 (
    .col0(SH0___L0), .col1(SH1___L0), .col2(SH2___L0), .col3(SH3___L0));
  letter_matriz_decode letter_matriz_decode_1 (
    .\input (rom_1_data), .output_3(SH3___L0), .output_2(SH2___L0), .output_0(SH0___L0), .output_1(SH1___L0));
  DotMatrix #(.matrixcols(4), .matrixrows(5)) dotmatrix_2 (
    .col0(SH4___L1), .col1(SH5___L1), .col2(SH6___L1), .col3(SH7___L1));
  letter_matriz_decode letter_matriz_decode_2 (
    .\input (rom_2_data), .output_3(SH7___L1), .output_2(SH6___L1), .output_0(SH4___L1), .output_1(SH5___L1));
  Button button_1 (.out(button_1_out));
  MUX_opCode_32b mux_opcode_32b_1 (
    .in_1(mux_funct_32b_1_output), .in_2(multiplexer_3_out),
    .in_3(n4_letters_merge_interface_26_word_4_letters), .in_4(n4_letters_merge_interface_18_word_4_letters),
    .in_5(n4_letters_merge_interface_27_word_4_letters), .in_6(n4_letters_merge_interface_19_word_4_letters),
    .in_7(n4_letters_merge_interface_38_word_4_letters), .in_8(n4_letters_merge_interface_38_word_4_letters),
    .in_9(n4_letters_merge_interface_28_word_4_letters),
    .in_10(n4_letters_merge_interface_20_word_4_letters),
    .in_11(n4_letters_merge_interface_29_word_4_letters),
    .in_12(n4_letters_merge_interface_21_word_4_letters),
    .in_13(n4_letters_merge_interface_30_word_4_letters),
    .in_14(n4_letters_merge_interface_22_word_4_letters),
    .in_15(n4_letters_merge_interface_38_word_4_letters),
    .in_16(n4_letters_merge_interface_31_word_4_letters),
    .in_17(n4_letters_merge_interface_23_word_4_letters),
    .in_18(n4_letters_merge_interface_38_word_4_letters),
    .in_19(n4_letters_merge_interface_38_word_4_letters),
    .in_20(n4_letters_merge_interface_38_word_4_letters),
    .in_21(n4_letters_merge_interface_38_word_4_letters),
    .in_22(n4_letters_merge_interface_38_word_4_letters),
    .in_23(n4_letters_merge_interface_38_word_4_letters),
    .in_24(n4_letters_merge_interface_38_word_4_letters),
    .in_25(n4_letters_merge_interface_38_word_4_letters),
    .in_26(n4_letters_merge_interface_38_word_4_letters),
    .in_27(n4_letters_merge_interface_38_word_4_letters),
    .in_28(n4_letters_merge_interface_38_word_4_letters),
    .in_29(n4_letters_merge_interface_38_word_4_letters),
    .in_30(n4_letters_merge_interface_38_word_4_letters),
    .in_31(n4_letters_merge_interface_38_word_4_letters),
    .in_32(n4_letters_merge_interface_38_word_4_letters), .sel(buffer_1_out),
    .in_34(n4_letters_merge_interface_38_word_4_letters),
    .in_35(n4_letters_merge_interface_38_word_4_letters),
    .in_36(n4_letters_merge_interface_38_word_4_letters),
    .in_37(n4_letters_merge_interface_32_word_4_letters),
    .in_38(n4_letters_merge_interface_24_word_4_letters),
    .in_39(n4_letters_merge_interface_33_word_4_letters),
    .in_40(n4_letters_merge_interface_38_word_4_letters),
    .in_41(n4_letters_merge_interface_38_word_4_letters),
    .in_42(n4_letters_merge_interface_34_word_4_letters),
    .in_43(n4_letters_merge_interface_25_word_4_letters),
    .in_44(n4_letters_merge_interface_38_word_4_letters),
    .in_45(n4_letters_merge_interface_35_word_4_letters),
    .in_46(n4_letters_merge_interface_38_word_4_letters),
    .in_47(n4_letters_merge_interface_38_word_4_letters),
    .in_48(n4_letters_merge_interface_38_word_4_letters),
    .in_49(n4_letters_merge_interface_38_word_4_letters),
    .in_50(n4_letters_merge_interface_36_word_4_letters),
    .in_51(n4_letters_merge_interface_38_word_4_letters),
    .in_52(n4_letters_merge_interface_38_word_4_letters),
    .in_53(n4_letters_merge_interface_38_word_4_letters),
    .in_54(n4_letters_merge_interface_38_word_4_letters),
    .in_55(n4_letters_merge_interface_38_word_4_letters),
    .in_56(n4_letters_merge_interface_38_word_4_letters),
    .in_57(n4_letters_merge_interface_38_word_4_letters),
    .in_58(n4_letters_merge_interface_37_word_4_letters),
    .in_59(n4_letters_merge_interface_38_word_4_letters),
    .in_60(n4_letters_merge_interface_38_word_4_letters),
    .in_61(n4_letters_merge_interface_38_word_4_letters),
    .in_62(n4_letters_merge_interface_38_word_4_letters),
    .in_63(n4_letters_merge_interface_38_word_4_letters),
    .in_64(n4_letters_merge_interface_38_word_4_letters),
    .in_65(n4_letters_merge_interface_38_word_4_letters), .\output (mux_opcode_32b_1_output));
  // Probe on mux_opcode_8b_1_output
  MUX_opCode_8b mux_opcode_8b_1 (
    .in_1(mux_funct_8b_1_output), .in_2(multiplexer_4_out), .in_3(8'h20), .in_4(8'h20), .in_5(8'h20),
    .in_6(8'h20), .in_7(8'h20), .in_8(8'h20), .in_9(8'h20), .in_10(8'h55), .in_11(8'h20), .in_12(8'h55),
    .in_13(8'h20), .in_14(8'h20), .in_15(8'h20), .in_16(8'h20), .in_17(8'h20), .in_18(8'h20), .in_19(8'h20),
    .in_20(8'h20), .in_21(8'h20), .in_22(8'h20), .in_23(8'h20), .in_24(8'h20), .in_25(8'h20), .in_26(8'h20),
    .in_27(8'h20), .in_28(8'h20), .in_29(8'h20), .in_30(8'h20), .in_31(8'h20), .in_32(8'h20),
    .sel(IM[31:26]), .in_34(8'h20), .in_35(8'h20), .in_36(8'h20), .in_37(8'h20), .in_38(8'h20),
    .in_39(8'h20), .in_40(8'h20), .in_41(8'h20), .in_42(8'h20), .in_43(8'h20), .in_44(8'h20), .in_45(8'h20),
    .in_46(8'h20), .in_47(8'h20), .in_48(8'h20), .in_49(8'h20), .in_50(8'h20), .in_51(8'h20), .in_52(8'h20),
    .in_53(8'h20), .in_54(8'h20), .in_55(8'h20), .in_56(8'h20), .in_57(8'h20), .in_58(8'h20), .in_59(8'h20),
    .in_60(8'h20), .in_61(8'h20), .in_62(8'h20), .in_63(8'h20), .in_64(8'h20), .in_65(8'h20),
    .\output (mux_opcode_8b_1_output));
  Counter counter_1 (
    .Q(counter_1_q), .clk(xor_1_out), .down(button_1_out));  // open: load, D, count, carry, clr, preset
  xor xor_1 (xor_1_out, button_1_out, button_2_out);
  Button button_2 (.out(button_2_out));
  // Probe on IM[31:26]
  ROM #(.dataWidth(32), .Select("low")) rom_3 (.addr(mux_opcode_32b_1_output[31:24]), .data(rom_3_data));
  ROM #(.dataWidth(32), .Select("low")) rom_4 (.addr(mux_opcode_32b_1_output[23:16]), .data(rom_4_data));
  ROM #(.dataWidth(32), .Select("low")) rom_5 (.addr(mux_opcode_32b_1_output[15:8]), .data(rom_5_data));
  ROM #(.dataWidth(32), .simpleMode("false"), .Select("low")) rom_6 (
    .addr(mux_opcode_32b_1_output[7:0]), .data(rom_6_data));
  ROM #(.dataWidth(32), .Select("low")) rom_7 (.addr(mux_opcode_8b_1_output), .data(rom_7_data));
  Counter #(.width(3), .max('h4)) counter_2 (
    .Q(counter_2_q), .clk(clk), .clr(rst_t));  // open: load, D, count, carry, preset, down
  ROM #(.dataWidth(32), .Select("low")) rom_8 (.addr(counter_1_q), .data(rom_8_data));
  DotMatrix #(.matrixcols(4), .matrixrows(5)) dotmatrix_3 (
    .col0(I0___L0), .col1(I1___L0), .col2(I2___L0), .col3(I3___L0));
  letter_matriz_decode letter_matriz_decode_3 (
    .\input (rom_3_data), .output_3(I3___L0), .output_2(I2___L0), .output_0(I0___L0), .output_1(I1___L0));
  DotMatrix #(.matrixcols(4), .matrixrows(5)) dotmatrix_4 (
    .col0(I4___L1), .col1(I5___L1), .col2(I6___L1), .col3(I7___L1));
  letter_matriz_decode letter_matriz_decode_4 (
    .\input (rom_4_data), .output_3(I7___L1), .output_2(I6___L1), .output_0(I4___L1), .output_1(I5___L1));
  // Probe on I7___L1
  DotMatrix #(.matrixcols(4), .matrixrows(5)) dotmatrix_5 (
    .col0(I9___L2), .col1(I10___L2), .col2(I11___L3), .col3(I12___L2));
  letter_matriz_decode letter_matriz_decode_5 (
    .\input (rom_5_data), .output_3(I12___L2), .output_2(I11___L3), .output_0(I9___L2), .output_1(I10___L2));
  DotMatrix #(.matrixcols(4), .matrixrows(5)) dotmatrix_6 (
    .col0(I13___L3_2), .col1(I14___L3_2), .col2(I15___L3_2), .col3(I16___L3_2));
  letter_matriz_decode letter_matriz_decode_6 (
    .\input (rom_6_data), .output_3(I16___L3_2), .output_2(I15___L3_2), .output_0(I13___L3_2),
    .output_1(I14___L3_2));
  // Probe on I13___L3_2
  DotMatrix #(.matrixcols(4), .matrixrows(5)) dotmatrix_7 (
    .col0(I17___L5), .col1(I17___L5), .col2(I19___L5), .col3(I20___L4));
  letter_matriz_decode letter_matriz_decode_7 (
    .\input (rom_7_data), .output_3(I20___L4), .output_2(I19___L5), .output_0(I17___L5), .output_1(I17___L5));
  Decoder #(.select(3), .enable("false")) decoder_1 (
    .out0(IF), .out1(ID), .out2(EX), .out3(MEM), .out4(WB), .sel(counter_2_q));  // open: out5, out6, out7
  // Probe on IM[25:21]
  // Probe on IM[20:16]
  // Probe on IM[15:11]
  DotMatrix #(.matrixcols(4), .matrixrows(5)) dotmatrix_8 (
    .col0(letter_matriz_decode_8_output_0), .col1(letter_matriz_decode_8_output_1),
    .col2(letter_matriz_decode_8_output_2), .col3(letter_matriz_decode_8_output_3));
  letter_matriz_decode letter_matriz_decode_8 (
    .\input (rom_8_data), .output_3(letter_matriz_decode_8_output_3),
    .output_2(letter_matriz_decode_8_output_2), .output_0(letter_matriz_decode_8_output_0),
    .output_1(letter_matriz_decode_8_output_1));
  MUX_funct_1b mux_funct_1b_1 (
    .in_1(1'b1), .in_2(1'b0), .in_3(1'b1), .in_4(1'b0), .in_5(1'b0), .in_6(1'b0), .in_7(1'b0), .in_8(1'b0),
    .in_9(1'b0), .in_10(1'b0), .in_11(1'b0), .in_12(1'b0), .in_13(1'b0), .in_14(1'b0), .in_15(1'b0),
    .in_16(1'b0), .in_17(1'b1), .in_18(1'b0), .in_19(1'b1), .in_20(1'b0), .in_21(1'b0), .in_22(1'b0),
    .in_23(1'b0), .in_24(1'b0), .in_25(1'b1), .in_26(1'b0), .in_27(1'b0), .in_28(1'b0), .in_29(1'b0),
    .in_30(1'b0), .in_31(1'b0), .in_32(1'b0), .sel(IM[5:0]), .in_34(1'b1), .in_35(1'b1), .in_36(1'b1),
    .in_37(1'b1), .in_38(1'b1), .in_39(1'b1), .in_40(1'b0), .in_41(1'b1), .in_42(1'b0), .in_43(1'b0),
    .in_44(1'b1), .in_45(1'b1), .in_46(1'b0), .in_47(1'b0), .in_48(1'b0), .in_49(1'b0), .in_50(1'b0),
    .in_51(1'b0), .in_52(1'b0), .in_53(1'b0), .in_54(1'b0), .in_55(1'b0), .in_56(1'b0), .in_57(1'b0),
    .in_58(1'b0), .in_59(1'b0), .in_60(1'b0), .in_61(1'b0), .in_62(1'b0), .in_63(1'b0), .in_64(1'b0),
    .in_65(1'b0), .\output (mux_funct_1b_1_output));
  MUX_funct_1b mux_funct_1b_2 (
    .in_1(1'b0), .in_2(1'b0), .in_3(1'b0), .in_4(1'b0), .in_5(1'b0), .in_6(1'b0), .in_7(1'b0), .in_8(1'b0),
    .in_9(1'b1), .in_10(1'b0), .in_11(1'b0), .in_12(1'b0), .in_13(1'b0), .in_14(1'b0), .in_15(1'b0),
    .in_16(1'b0), .in_17(1'b0), .in_18(1'b0), .in_19(1'b0), .in_20(1'b0), .in_21(1'b0), .in_22(1'b0),
    .in_23(1'b0), .in_24(1'b0), .in_25(1'b0), .in_26(1'b0), .in_27(1'b0), .in_28(1'b0), .in_29(1'b0),
    .in_30(1'b0), .in_31(1'b0), .in_32(1'b0), .sel(IM[5:0]), .in_34(1'b1), .in_35(1'b1), .in_36(1'b1),
    .in_37(1'b1), .in_38(1'b1), .in_39(1'b1), .in_40(1'b0), .in_41(1'b1), .in_42(1'b0), .in_43(1'b0),
    .in_44(1'b1), .in_45(1'b1), .in_46(1'b0), .in_47(1'b0), .in_48(1'b0), .in_49(1'b0), .in_50(1'b0),
    .in_51(1'b0), .in_52(1'b0), .in_53(1'b0), .in_54(1'b0), .in_55(1'b0), .in_56(1'b0), .in_57(1'b0),
    .in_58(1'b0), .in_59(1'b0), .in_60(1'b0), .in_61(1'b0), .in_62(1'b0), .in_63(1'b0), .in_64(1'b0),
    .in_65(1'b0), .\output (mux_funct_1b_2_output));
  MUX_funct_1b mux_funct_1b_3 (
    .in_1(1'b1), .in_2(1'b0), .in_3(1'b1), .in_4(1'b0), .in_5(1'b0), .in_6(1'b0), .in_7(1'b0), .in_8(1'b0),
    .in_9(1'b0), .in_10(1'b0), .in_11(1'b0), .in_12(1'b0), .in_13(1'b0), .in_14(1'b0), .in_15(1'b0),
    .in_16(1'b0), .in_17(1'b0), .in_18(1'b0), .in_19(1'b0), .in_20(1'b0), .in_21(1'b0), .in_22(1'b0),
    .in_23(1'b0), .in_24(1'b0), .in_25(1'b0), .in_26(1'b0), .in_27(1'b0), .in_28(1'b0), .in_29(1'b0),
    .in_30(1'b0), .in_31(1'b0), .in_32(1'b0), .sel(IM[5:0]), .in_34(1'b1), .in_35(1'b1), .in_36(1'b1),
    .in_37(1'b1), .in_38(1'b1), .in_39(1'b1), .in_40(1'b0), .in_41(1'b1), .in_42(1'b0), .in_43(1'b0),
    .in_44(1'b1), .in_45(1'b1), .in_46(1'b0), .in_47(1'b0), .in_48(1'b0), .in_49(1'b0), .in_50(1'b0),
    .in_51(1'b0), .in_52(1'b0), .in_53(1'b0), .in_54(1'b0), .in_55(1'b0), .in_56(1'b0), .in_57(1'b0),
    .in_58(1'b0), .in_59(1'b0), .in_60(1'b0), .in_61(1'b0), .in_62(1'b0), .in_63(1'b0), .in_64(1'b0),
    .in_65(1'b0), .\output (mux_funct_1b_3_output));
  MUX_opCode_1b mux_opcode_1b_1 (
    .in_1(mux_funct_1b_1_output), .in_2(1'b1), .in_3(1'b0), .in_4(1'b0), .in_5(1'b1), .in_6(1'b1),
    .in_7(1'b0), .in_8(1'b0), .in_9(1'b1), .in_10(1'b1), .in_11(1'b1), .in_12(1'b1), .in_13(1'b1),
    .in_14(1'b1), .in_15(1'b0), .in_16(1'b0), .in_17(1'b1), .in_18(1'b0), .in_19(1'b0), .in_20(1'b0),
    .in_21(1'b0), .in_22(1'b0), .in_23(1'b0), .in_24(1'b0), .in_25(1'b0), .in_26(1'b0), .in_27(1'b0),
    .in_28(1'b0), .in_29(1'b0), .in_30(1'b0), .in_31(1'b0), .in_32(1'b0), .sel(IM[31:26]), .in_34(1'b0),
    .in_35(1'b0), .in_36(1'b0), .in_37(1'b1), .in_38(1'b1), .in_39(1'b1), .in_40(1'b0), .in_41(1'b0),
    .in_42(1'b1), .in_43(1'b1), .in_44(1'b0), .in_45(1'b1), .in_46(1'b0), .in_47(1'b0), .in_48(1'b0),
    .in_49(1'b0), .in_50(1'b1), .in_51(1'b0), .in_52(1'b0), .in_53(1'b0), .in_54(1'b0), .in_55(1'b0),
    .in_56(1'b0), .in_57(1'b0), .in_58(1'b1), .in_59(1'b0), .in_60(1'b0), .in_61(1'b0), .in_62(1'b0),
    .in_63(1'b0), .in_64(1'b0), .in_65(1'b0), .\output (mux_opcode_1b_1_output));
  // Probe on IM[31:26]
  MUX_opCode_1b mux_opcode_1b_2 (
    .in_1(mux_funct_1b_2_output), .in_2(1'b1), .in_3(1'b0), .in_4(1'b0), .in_5(1'b1), .in_6(1'b1),
    .in_7(1'b0), .in_8(1'b0), .in_9(1'b1), .in_10(1'b1), .in_11(1'b1), .in_12(1'b1), .in_13(1'b1),
    .in_14(1'b1), .in_15(1'b0), .in_16(1'b0), .in_17(1'b1), .in_18(1'b0), .in_19(1'b0), .in_20(1'b0),
    .in_21(1'b0), .in_22(1'b0), .in_23(1'b0), .in_24(1'b0), .in_25(1'b0), .in_26(1'b0), .in_27(1'b0),
    .in_28(1'b0), .in_29(1'b0), .in_30(1'b0), .in_31(1'b0), .in_32(1'b0), .sel(IM[31:26]), .in_34(1'b0),
    .in_35(1'b0), .in_36(1'b0), .in_37(1'b1), .in_38(1'b1), .in_39(1'b1), .in_40(1'b0), .in_41(1'b0),
    .in_42(1'b1), .in_43(1'b1), .in_44(1'b0), .in_45(1'b1), .in_46(1'b0), .in_47(1'b0), .in_48(1'b0),
    .in_49(1'b0), .in_50(1'b1), .in_51(1'b0), .in_52(1'b0), .in_53(1'b0), .in_54(1'b0), .in_55(1'b0),
    .in_56(1'b0), .in_57(1'b0), .in_58(1'b1), .in_59(1'b0), .in_60(1'b0), .in_61(1'b0), .in_62(1'b0),
    .in_63(1'b0), .in_64(1'b0), .in_65(1'b0), .\output (mux_opcode_1b_2_output));
  // Probe on IM[31:26]
  MUX_opCode_1b mux_opcode_1b_3 (
    .in_1(mux_funct_1b_3_output), .in_2(1'b1), .in_3(1'b0), .in_4(1'b0), .in_5(1'b1), .in_6(1'b1),
    .in_7(1'b0), .in_8(1'b0), .in_9(1'b1), .in_10(1'b1), .in_11(1'b1), .in_12(1'b1), .in_13(1'b1),
    .in_14(1'b1), .in_15(1'b0), .in_16(1'b0), .in_17(1'b1), .in_18(1'b0), .in_19(1'b0), .in_20(1'b0),
    .in_21(1'b0), .in_22(1'b0), .in_23(1'b0), .in_24(1'b0), .in_25(1'b0), .in_26(1'b0), .in_27(1'b0),
    .in_28(1'b0), .in_29(1'b0), .in_30(1'b0), .in_31(1'b0), .in_32(1'b0), .sel(IM[31:26]), .in_34(1'b0),
    .in_35(1'b0), .in_36(1'b0), .in_37(1'b1), .in_38(1'b1), .in_39(1'b1), .in_40(1'b0), .in_41(1'b0),
    .in_42(1'b1), .in_43(1'b1), .in_44(1'b0), .in_45(1'b1), .in_46(1'b0), .in_47(1'b0), .in_48(1'b0),
    .in_49(1'b0), .in_50(1'b1), .in_51(1'b0), .in_52(1'b0), .in_53(1'b0), .in_54(1'b0), .in_55(1'b0),
    .in_56(1'b0), .in_57(1'b0), .in_58(1'b1), .in_59(1'b0), .in_60(1'b0), .in_61(1'b0), .in_62(1'b0),
    .in_63(1'b0), .in_64(1'b0), .in_65(1'b0), .\output (mux_opcode_1b_3_output));
  // Probe on IM[31:26]
  _2_letters_merge_interface u_2_letters_merge_interface_1 (
    .letter_0(8'h54), .letter_1(8'h41), .word_4_letters(n2_letters_merge_interface_1_word_4_letters));
  _2_letters_merge_interface u_2_letters_merge_interface_2 (
    .letter_0(8'h31), .letter_1(8'h56), .word_4_letters(n2_letters_merge_interface_2_word_4_letters));
  _2_letters_merge_interface u_2_letters_merge_interface_3 (
    .letter_0(8'h31), .letter_1(8'h41), .word_4_letters(n2_letters_merge_interface_3_word_4_letters));
  _2_letters_merge_interface u_2_letters_merge_interface_4 (
    .letter_0(8'h33), .letter_1(8'h41), .word_4_letters(n2_letters_merge_interface_4_word_4_letters));
  _2_letters_merge_interface u_2_letters_merge_interface_5 (
    .letter_0(8'h31), .letter_1(8'h54), .word_4_letters(n2_letters_merge_interface_5_word_4_letters));
  _2_letters_merge_interface u_2_letters_merge_interface_6 (
    .letter_0(8'h33), .letter_1(8'h54), .word_4_letters(n2_letters_merge_interface_6_word_4_letters));
  _2_letters_merge_interface u_2_letters_merge_interface_7 (
    .letter_0(8'h35), .letter_1(8'h54), .word_4_letters(n2_letters_merge_interface_7_word_4_letters));
  _2_letters_merge_interface u_2_letters_merge_interface_8 (
    .letter_0(8'h37), .letter_1(8'h54), .word_4_letters(n2_letters_merge_interface_8_word_4_letters));
  _2_letters_merge_interface u_2_letters_merge_interface_9 (
    .letter_0(8'h31), .letter_1(8'h53), .word_4_letters(n2_letters_merge_interface_9_word_4_letters));
  _2_letters_merge_interface u_2_letters_merge_interface_10 (
    .letter_0(8'h33), .letter_1(8'h53), .word_4_letters(n2_letters_merge_interface_10_word_4_letters));
  _2_letters_merge_interface u_2_letters_merge_interface_11 (
    .letter_0(8'h35), .letter_1(8'h53), .word_4_letters(n2_letters_merge_interface_11_word_4_letters));
  _2_letters_merge_interface u_2_letters_merge_interface_12 (
    .letter_0(8'h37), .letter_1(8'h53), .word_4_letters(n2_letters_merge_interface_12_word_4_letters));
  _2_letters_merge_interface u_2_letters_merge_interface_13 (
    .letter_0(8'h39), .letter_1(8'h54), .word_4_letters(n2_letters_merge_interface_13_word_4_letters));
  _2_letters_merge_interface u_2_letters_merge_interface_14 (
    .letter_0(8'h31), .letter_1(8'h4b), .word_4_letters(n2_letters_merge_interface_14_word_4_letters));
  _2_letters_merge_interface u_2_letters_merge_interface_15 (
    .letter_0(8'h50), .letter_1(8'h46), .word_4_letters(n2_letters_merge_interface_15_word_4_letters));
  _2_letters_merge_interface u_2_letters_merge_interface_16 (
    .letter_0(8'h41), .letter_1(8'h52), .word_4_letters(n2_letters_merge_interface_16_word_4_letters));
  _2_letters_merge_interface u_2_letters_merge_interface_17 (
    .letter_0(8'h54), .letter_1(8'h41), .word_4_letters(n2_letters_merge_interface_17_word_4_letters));
  _2_letters_merge_interface u_2_letters_merge_interface_18 (
    .letter_0(8'h31), .letter_1(8'h56), .word_4_letters(n2_letters_merge_interface_18_word_4_letters));
  _2_letters_merge_interface u_2_letters_merge_interface_19 (
    .letter_0(8'h31), .letter_1(8'h41), .word_4_letters(n2_letters_merge_interface_19_word_4_letters));
  _2_letters_merge_interface u_2_letters_merge_interface_20 (
    .letter_0(8'h33), .letter_1(8'h41), .word_4_letters(n2_letters_merge_interface_20_word_4_letters));
  _2_letters_merge_interface u_2_letters_merge_interface_21 (
    .letter_0(8'h31), .letter_1(8'h54), .word_4_letters(n2_letters_merge_interface_21_word_4_letters));
  _2_letters_merge_interface u_2_letters_merge_interface_22 (
    .letter_0(8'h33), .letter_1(8'h54), .word_4_letters(n2_letters_merge_interface_22_word_4_letters));
  _2_letters_merge_interface u_2_letters_merge_interface_23 (
    .letter_0(8'h35), .letter_1(8'h54), .word_4_letters(n2_letters_merge_interface_23_word_4_letters));
  _2_letters_merge_interface u_2_letters_merge_interface_24 (
    .letter_0(8'h37), .letter_1(8'h54), .word_4_letters(n2_letters_merge_interface_24_word_4_letters));
  _2_letters_merge_interface u_2_letters_merge_interface_25 (
    .letter_0(8'h31), .letter_1(8'h53), .word_4_letters(n2_letters_merge_interface_25_word_4_letters));
  _2_letters_merge_interface u_2_letters_merge_interface_26 (
    .letter_0(8'h33), .letter_1(8'h53), .word_4_letters(n2_letters_merge_interface_26_word_4_letters));
  _2_letters_merge_interface u_2_letters_merge_interface_27 (
    .letter_0(8'h35), .letter_1(8'h53), .word_4_letters(n2_letters_merge_interface_27_word_4_letters));
  _2_letters_merge_interface u_2_letters_merge_interface_28 (
    .letter_0(8'h37), .letter_1(8'h53), .word_4_letters(n2_letters_merge_interface_28_word_4_letters));
  _2_letters_merge_interface u_2_letters_merge_interface_29 (
    .letter_0(8'h39), .letter_1(8'h54), .word_4_letters(n2_letters_merge_interface_29_word_4_letters));
  _2_letters_merge_interface u_2_letters_merge_interface_30 (
    .letter_0(8'h31), .letter_1(8'h4b), .word_4_letters(n2_letters_merge_interface_30_word_4_letters));
  _2_letters_merge_interface u_2_letters_merge_interface_31 (
    .letter_0(8'h50), .letter_1(8'h46), .word_4_letters(n2_letters_merge_interface_31_word_4_letters));
  _2_letters_merge_interface u_2_letters_merge_interface_32 (
    .letter_0(8'h41), .letter_1(8'h52), .word_4_letters(n2_letters_merge_interface_32_word_4_letters));
  _2_letters_merge_interface u_2_letters_merge_interface_33 (
    .letter_0(8'h54), .letter_1(8'h41), .word_4_letters(n2_letters_merge_interface_33_word_4_letters));
  _2_letters_merge_interface u_2_letters_merge_interface_34 (
    .letter_0(8'h31), .letter_1(8'h56), .word_4_letters(n2_letters_merge_interface_34_word_4_letters));
  _2_letters_merge_interface u_2_letters_merge_interface_35 (
    .letter_0(8'h31), .letter_1(8'h41), .word_4_letters(n2_letters_merge_interface_35_word_4_letters));
  _2_letters_merge_interface u_2_letters_merge_interface_36 (
    .letter_0(8'h33), .letter_1(8'h41), .word_4_letters(n2_letters_merge_interface_36_word_4_letters));
  _2_letters_merge_interface u_2_letters_merge_interface_37 (
    .letter_0(8'h31), .letter_1(8'h54), .word_4_letters(n2_letters_merge_interface_37_word_4_letters));
  _2_letters_merge_interface u_2_letters_merge_interface_38 (
    .letter_0(8'h33), .letter_1(8'h54), .word_4_letters(n2_letters_merge_interface_38_word_4_letters));
  _2_letters_merge_interface u_2_letters_merge_interface_39 (
    .letter_0(8'h35), .letter_1(8'h54), .word_4_letters(n2_letters_merge_interface_39_word_4_letters));
  _2_letters_merge_interface u_2_letters_merge_interface_40 (
    .letter_0(8'h37), .letter_1(8'h54), .word_4_letters(n2_letters_merge_interface_40_word_4_letters));
  _2_letters_merge_interface u_2_letters_merge_interface_41 (
    .letter_0(8'h31), .letter_1(8'h53), .word_4_letters(n2_letters_merge_interface_41_word_4_letters));
  _2_letters_merge_interface u_2_letters_merge_interface_42 (
    .letter_0(8'h33), .letter_1(8'h53), .word_4_letters(n2_letters_merge_interface_42_word_4_letters));
  _2_letters_merge_interface u_2_letters_merge_interface_43 (
    .letter_0(8'h35), .letter_1(8'h53), .word_4_letters(n2_letters_merge_interface_43_word_4_letters));
  _2_letters_merge_interface u_2_letters_merge_interface_44 (
    .letter_0(8'h37), .letter_1(8'h53), .word_4_letters(n2_letters_merge_interface_44_word_4_letters));
  _2_letters_merge_interface u_2_letters_merge_interface_45 (
    .letter_0(8'h39), .letter_1(8'h54), .word_4_letters(n2_letters_merge_interface_45_word_4_letters));
  _2_letters_merge_interface u_2_letters_merge_interface_46 (
    .letter_0(8'h31), .letter_1(8'h4b), .word_4_letters(n2_letters_merge_interface_46_word_4_letters));
  _2_letters_merge_interface u_2_letters_merge_interface_47 (
    .letter_0(8'h50), .letter_1(8'h46), .word_4_letters(n2_letters_merge_interface_47_word_4_letters));
  _2_letters_merge_interface u_2_letters_merge_interface_48 (
    .letter_0(8'h41), .letter_1(8'h52), .word_4_letters(n2_letters_merge_interface_48_word_4_letters));
  _2_letters_merge_interface u_2_letters_merge_interface_49 (
    .letter_0(8'h52), .letter_1(8'h5a), .word_4_letters(n2_letters_merge_interface_49_word_4_letters));
  _2_letters_merge_interface u_2_letters_merge_interface_50 (
    .letter_0(8'h30), .letter_1(8'h56), .word_4_letters(n2_letters_merge_interface_50_word_4_letters));
  _2_letters_merge_interface u_2_letters_merge_interface_51 (
    .letter_0(8'h30), .letter_1(8'h41), .word_4_letters(n2_letters_merge_interface_51_word_4_letters));
  _2_letters_merge_interface u_2_letters_merge_interface_52 (
    .letter_0(8'h32), .letter_1(8'h41), .word_4_letters(n2_letters_merge_interface_52_word_4_letters));
  _2_letters_merge_interface u_2_letters_merge_interface_53 (
    .letter_0(8'h30), .letter_1(8'h54), .word_4_letters(n2_letters_merge_interface_53_word_4_letters));
  _2_letters_merge_interface u_2_letters_merge_interface_54 (
    .letter_0(8'h32), .letter_1(8'h54), .word_4_letters(n2_letters_merge_interface_54_word_4_letters));
  _2_letters_merge_interface u_2_letters_merge_interface_55 (
    .letter_0(8'h34), .letter_1(8'h54), .word_4_letters(n2_letters_merge_interface_55_word_4_letters));
  _2_letters_merge_interface u_2_letters_merge_interface_56 (
    .letter_0(8'h36), .letter_1(8'h54), .word_4_letters(n2_letters_merge_interface_56_word_4_letters));
  _2_letters_merge_interface u_2_letters_merge_interface_57 (
    .letter_0(8'h30), .letter_1(8'h53), .word_4_letters(n2_letters_merge_interface_57_word_4_letters));
  _2_letters_merge_interface u_2_letters_merge_interface_58 (
    .letter_0(8'h32), .letter_1(8'h53), .word_4_letters(n2_letters_merge_interface_58_word_4_letters));
  _2_letters_merge_interface u_2_letters_merge_interface_59 (
    .letter_0(8'h34), .letter_1(8'h53), .word_4_letters(n2_letters_merge_interface_59_word_4_letters));
  _2_letters_merge_interface u_2_letters_merge_interface_60 (
    .letter_0(8'h36), .letter_1(8'h53), .word_4_letters(n2_letters_merge_interface_60_word_4_letters));
  _2_letters_merge_interface u_2_letters_merge_interface_61 (
    .letter_0(8'h38), .letter_1(8'h54), .word_4_letters(n2_letters_merge_interface_61_word_4_letters));
  _2_letters_merge_interface u_2_letters_merge_interface_62 (
    .letter_0(8'h30), .letter_1(8'h4b), .word_4_letters(n2_letters_merge_interface_62_word_4_letters));
  _2_letters_merge_interface u_2_letters_merge_interface_63 (
    .letter_0(8'h50), .letter_1(8'h53), .word_4_letters(n2_letters_merge_interface_63_word_4_letters));
  _2_letters_merge_interface u_2_letters_merge_interface_64 (
    .letter_0(8'h50), .letter_1(8'h46), .word_4_letters(n2_letters_merge_interface_64_word_4_letters));
  _2_letters_merge_interface u_2_letters_merge_interface_65 (
    .letter_0(8'h52), .letter_1(8'h5a), .word_4_letters(n2_letters_merge_interface_65_word_4_letters));
  _2_letters_merge_interface u_2_letters_merge_interface_66 (
    .letter_0(8'h30), .letter_1(8'h56), .word_4_letters(n2_letters_merge_interface_66_word_4_letters));
  _2_letters_merge_interface u_2_letters_merge_interface_67 (
    .letter_0(8'h30), .letter_1(8'h41), .word_4_letters(n2_letters_merge_interface_67_word_4_letters));
  _2_letters_merge_interface u_2_letters_merge_interface_68 (
    .letter_0(8'h32), .letter_1(8'h41), .word_4_letters(n2_letters_merge_interface_68_word_4_letters));
  _2_letters_merge_interface u_2_letters_merge_interface_69 (
    .letter_0(8'h30), .letter_1(8'h54), .word_4_letters(n2_letters_merge_interface_69_word_4_letters));
  _2_letters_merge_interface u_2_letters_merge_interface_70 (
    .letter_0(8'h32), .letter_1(8'h54), .word_4_letters(n2_letters_merge_interface_70_word_4_letters));
  _2_letters_merge_interface u_2_letters_merge_interface_71 (
    .letter_0(8'h34), .letter_1(8'h54), .word_4_letters(n2_letters_merge_interface_71_word_4_letters));
  _2_letters_merge_interface u_2_letters_merge_interface_72 (
    .letter_0(8'h36), .letter_1(8'h54), .word_4_letters(n2_letters_merge_interface_72_word_4_letters));
  _2_letters_merge_interface u_2_letters_merge_interface_73 (
    .letter_0(8'h30), .letter_1(8'h53), .word_4_letters(n2_letters_merge_interface_73_word_4_letters));
  _2_letters_merge_interface u_2_letters_merge_interface_74 (
    .letter_0(8'h32), .letter_1(8'h53), .word_4_letters(n2_letters_merge_interface_74_word_4_letters));
  _2_letters_merge_interface u_2_letters_merge_interface_75 (
    .letter_0(8'h34), .letter_1(8'h53), .word_4_letters(n2_letters_merge_interface_75_word_4_letters));
  _2_letters_merge_interface u_2_letters_merge_interface_76 (
    .letter_0(8'h36), .letter_1(8'h53), .word_4_letters(n2_letters_merge_interface_76_word_4_letters));
  _2_letters_merge_interface u_2_letters_merge_interface_77 (
    .letter_0(8'h38), .letter_1(8'h54), .word_4_letters(n2_letters_merge_interface_77_word_4_letters));
  _2_letters_merge_interface u_2_letters_merge_interface_78 (
    .letter_0(8'h30), .letter_1(8'h4b), .word_4_letters(n2_letters_merge_interface_78_word_4_letters));
  _2_letters_merge_interface u_2_letters_merge_interface_79 (
    .letter_0(8'h50), .letter_1(8'h53), .word_4_letters(n2_letters_merge_interface_79_word_4_letters));
  _2_letters_merge_interface u_2_letters_merge_interface_80 (
    .letter_0(8'h50), .letter_1(8'h46), .word_4_letters(n2_letters_merge_interface_80_word_4_letters));
  _2_letters_merge_interface u_2_letters_merge_interface_81 (
    .letter_0(8'h52), .letter_1(8'h5a), .word_4_letters(n2_letters_merge_interface_81_word_4_letters));
  _2_letters_merge_interface u_2_letters_merge_interface_82 (
    .letter_0(8'h30), .letter_1(8'h56), .word_4_letters(n2_letters_merge_interface_82_word_4_letters));
  _2_letters_merge_interface u_2_letters_merge_interface_83 (
    .letter_0(8'h30), .letter_1(8'h41), .word_4_letters(n2_letters_merge_interface_83_word_4_letters));
  _2_letters_merge_interface u_2_letters_merge_interface_84 (
    .letter_0(8'h32), .letter_1(8'h41), .word_4_letters(n2_letters_merge_interface_84_word_4_letters));
  _2_letters_merge_interface u_2_letters_merge_interface_85 (
    .letter_0(8'h30), .letter_1(8'h54), .word_4_letters(n2_letters_merge_interface_85_word_4_letters));
  _2_letters_merge_interface u_2_letters_merge_interface_86 (
    .letter_0(8'h32), .letter_1(8'h54), .word_4_letters(n2_letters_merge_interface_86_word_4_letters));
  _2_letters_merge_interface u_2_letters_merge_interface_87 (
    .letter_0(8'h34), .letter_1(8'h54), .word_4_letters(n2_letters_merge_interface_87_word_4_letters));
  _2_letters_merge_interface u_2_letters_merge_interface_88 (
    .letter_0(8'h36), .letter_1(8'h54), .word_4_letters(n2_letters_merge_interface_88_word_4_letters));
  Multiplexer #(.select(5), .width(16), .enable("false")) multiplexer_10 (
    .in0(n2_letters_merge_interface_81_word_4_letters), .in1(n2_letters_merge_interface_33_word_4_letters),
    .in2(n2_letters_merge_interface_82_word_4_letters), .in3(n2_letters_merge_interface_34_word_4_letters),
    .in4(n2_letters_merge_interface_83_word_4_letters), .in5(n2_letters_merge_interface_35_word_4_letters),
    .in6(n2_letters_merge_interface_84_word_4_letters), .in7(n2_letters_merge_interface_36_word_4_letters),
    .in8(n2_letters_merge_interface_85_word_4_letters), .in9(n2_letters_merge_interface_37_word_4_letters),
    .in10(n2_letters_merge_interface_86_word_4_letters), .in11(n2_letters_merge_interface_38_word_4_letters),
    .in12(n2_letters_merge_interface_87_word_4_letters), .in13(n2_letters_merge_interface_39_word_4_letters),
    .in14(n2_letters_merge_interface_88_word_4_letters), .in15(n2_letters_merge_interface_40_word_4_letters),
    .in16(n2_letters_merge_interface_89_word_4_letters), .in17(n2_letters_merge_interface_41_word_4_letters),
    .in18(n2_letters_merge_interface_90_word_4_letters), .in19(n2_letters_merge_interface_42_word_4_letters),
    .in20(n2_letters_merge_interface_91_word_4_letters), .in21(n2_letters_merge_interface_43_word_4_letters),
    .in22(n2_letters_merge_interface_92_word_4_letters), .in23(n2_letters_merge_interface_44_word_4_letters),
    .in24(n2_letters_merge_interface_93_word_4_letters), .in25(n2_letters_merge_interface_45_word_4_letters),
    .in26(n2_letters_merge_interface_94_word_4_letters), .in27(n2_letters_merge_interface_46_word_4_letters),
    .in28(n2_letters_merge_interface_95_word_4_letters), .in29(n2_letters_merge_interface_47_word_4_letters),
    .in30(n2_letters_merge_interface_96_word_4_letters), .in31(n2_letters_merge_interface_48_word_4_letters),
    .out(multiplexer_10_out), .sel(IM[15:11]));
  _2_letters_merge_interface u_2_letters_merge_interface_89 (
    .letter_0(8'h30), .letter_1(8'h53), .word_4_letters(n2_letters_merge_interface_89_word_4_letters));
  _2_letters_merge_interface u_2_letters_merge_interface_90 (
    .letter_0(8'h32), .letter_1(8'h53), .word_4_letters(n2_letters_merge_interface_90_word_4_letters));
  _2_letters_merge_interface u_2_letters_merge_interface_91 (
    .letter_0(8'h34), .letter_1(8'h53), .word_4_letters(n2_letters_merge_interface_91_word_4_letters));
  _2_letters_merge_interface u_2_letters_merge_interface_92 (
    .letter_0(8'h36), .letter_1(8'h53), .word_4_letters(n2_letters_merge_interface_92_word_4_letters));
  _2_letters_merge_interface u_2_letters_merge_interface_93 (
    .letter_0(8'h38), .letter_1(8'h54), .word_4_letters(n2_letters_merge_interface_93_word_4_letters));
  _2_letters_merge_interface u_2_letters_merge_interface_94 (
    .letter_0(8'h30), .letter_1(8'h4b), .word_4_letters(n2_letters_merge_interface_94_word_4_letters));
  _2_letters_merge_interface u_2_letters_merge_interface_95 (
    .letter_0(8'h50), .letter_1(8'h53), .word_4_letters(n2_letters_merge_interface_95_word_4_letters));
  _2_letters_merge_interface u_2_letters_merge_interface_96 (
    .letter_0(8'h50), .letter_1(8'h46), .word_4_letters(n2_letters_merge_interface_96_word_4_letters));
  Multiplexer #(.select(5), .width(16), .enable("false")) multiplexer_11 (
    .in0(n2_letters_merge_interface_49_word_4_letters), .in1(n2_letters_merge_interface_1_word_4_letters),
    .in2(n2_letters_merge_interface_50_word_4_letters), .in3(n2_letters_merge_interface_2_word_4_letters),
    .in4(n2_letters_merge_interface_51_word_4_letters), .in5(n2_letters_merge_interface_3_word_4_letters),
    .in6(n2_letters_merge_interface_52_word_4_letters), .in7(n2_letters_merge_interface_4_word_4_letters),
    .in8(n2_letters_merge_interface_53_word_4_letters), .in9(n2_letters_merge_interface_5_word_4_letters),
    .in10(n2_letters_merge_interface_54_word_4_letters), .in11(n2_letters_merge_interface_6_word_4_letters),
    .in12(n2_letters_merge_interface_55_word_4_letters), .in13(n2_letters_merge_interface_7_word_4_letters),
    .in14(n2_letters_merge_interface_56_word_4_letters), .in15(n2_letters_merge_interface_8_word_4_letters),
    .in16(n2_letters_merge_interface_57_word_4_letters), .in17(n2_letters_merge_interface_9_word_4_letters),
    .in18(n2_letters_merge_interface_58_word_4_letters), .in19(n2_letters_merge_interface_10_word_4_letters),
    .in20(n2_letters_merge_interface_59_word_4_letters), .in21(n2_letters_merge_interface_11_word_4_letters),
    .in22(n2_letters_merge_interface_60_word_4_letters), .in23(n2_letters_merge_interface_12_word_4_letters),
    .in24(n2_letters_merge_interface_61_word_4_letters), .in25(n2_letters_merge_interface_13_word_4_letters),
    .in26(n2_letters_merge_interface_62_word_4_letters), .in27(n2_letters_merge_interface_14_word_4_letters),
    .in28(n2_letters_merge_interface_63_word_4_letters), .in29(n2_letters_merge_interface_15_word_4_letters),
    .in30(n2_letters_merge_interface_64_word_4_letters), .in31(n2_letters_merge_interface_16_word_4_letters),
    .out(multiplexer_11_out), .sel(IM[25:21]));
  Multiplexer #(.select(5), .width(16), .enable("false")) multiplexer_12 (
    .in0(n2_letters_merge_interface_65_word_4_letters), .in1(n2_letters_merge_interface_17_word_4_letters),
    .in2(n2_letters_merge_interface_66_word_4_letters), .in3(n2_letters_merge_interface_18_word_4_letters),
    .in4(n2_letters_merge_interface_67_word_4_letters), .in5(n2_letters_merge_interface_19_word_4_letters),
    .in6(n2_letters_merge_interface_68_word_4_letters), .in7(n2_letters_merge_interface_20_word_4_letters),
    .in8(n2_letters_merge_interface_69_word_4_letters), .in9(n2_letters_merge_interface_21_word_4_letters),
    .in10(n2_letters_merge_interface_70_word_4_letters), .in11(n2_letters_merge_interface_22_word_4_letters),
    .in12(n2_letters_merge_interface_71_word_4_letters), .in13(n2_letters_merge_interface_23_word_4_letters),
    .in14(n2_letters_merge_interface_72_word_4_letters), .in15(n2_letters_merge_interface_24_word_4_letters),
    .in16(n2_letters_merge_interface_73_word_4_letters), .in17(n2_letters_merge_interface_25_word_4_letters),
    .in18(n2_letters_merge_interface_74_word_4_letters), .in19(n2_letters_merge_interface_26_word_4_letters),
    .in20(n2_letters_merge_interface_75_word_4_letters), .in21(n2_letters_merge_interface_27_word_4_letters),
    .in22(n2_letters_merge_interface_76_word_4_letters), .in23(n2_letters_merge_interface_28_word_4_letters),
    .in24(n2_letters_merge_interface_77_word_4_letters), .in25(n2_letters_merge_interface_29_word_4_letters),
    .in26(n2_letters_merge_interface_78_word_4_letters), .in27(n2_letters_merge_interface_30_word_4_letters),
    .in28(n2_letters_merge_interface_79_word_4_letters), .in29(n2_letters_merge_interface_31_word_4_letters),
    .in30(n2_letters_merge_interface_80_word_4_letters), .in31(n2_letters_merge_interface_32_word_4_letters),
    .out(multiplexer_12_out), .sel(IM[20:16]));
  Multiplexer #(.width(8), .enable("false")) multiplexer_13 (
    .in0(8'h2d), .in1(multiplexer_12_out[15:8]), .out(multiplexer_13_out), .sel(mux_opcode_1b_3_output));
  Multiplexer #(.width(8), .enable("false")) multiplexer_14 (
    .in0(8'h2d), .in1(multiplexer_12_out[7:0]), .out(multiplexer_14_out), .sel(mux_opcode_1b_3_output));
  Multiplexer #(.width(8), .enable("false")) multiplexer_15 (
    .in0(8'h2d), .in1(multiplexer_10_out[15:8]), .out(multiplexer_15_out), .sel(mux_opcode_1b_1_output));
  Multiplexer #(.width(8), .enable("false")) multiplexer_16 (
    .in0(8'h2d), .in1(multiplexer_10_out[7:0]), .out(multiplexer_16_out), .sel(mux_opcode_1b_1_output));
  Multiplexer #(.width(8), .enable("false")) multiplexer_17 (
    .in0(8'h2d), .in1(multiplexer_11_out[15:8]), .out(multiplexer_17_out), .sel(mux_opcode_1b_2_output));
  Multiplexer #(.width(8), .enable("false")) multiplexer_18 (
    .in0(8'h2d), .in1(multiplexer_11_out[7:0]), .out(multiplexer_18_out), .sel(mux_opcode_1b_2_output));
  letter_matriz_decode letter_matriz_decode_9 (
    .\input (RS_L0), .output_3(RS3___L0), .output_2(RS2___L0), .output_0(RS0___L0), .output_1(RS1___L0));
  ROM #(.dataWidth(32), .Select("low")) rom_9 (.addr(multiplexer_17_out), .data(RS_L0), .sel(1'b0));
  letter_matriz_decode letter_matriz_decode_10 (
    .\input (RS_L1), .output_3(RS7___L1), .output_2(RS6___L1), .output_0(RS4___L1), .output_1(RS5___L1));
  ROM #(.dataWidth(32), .Select("low")) rom_10 (.addr(multiplexer_18_out), .data(RS_L1), .sel(1'b0));
  DotMatrix #(.matrixcols(4), .matrixrows(5)) dotmatrix_9 (
    .col0(RT___L0), .col1(RT1___L0), .col2(RT2___L0), .col3(RT3___L0));
  letter_matriz_decode letter_matriz_decode_11 (
    .\input (RT_L0), .output_3(RT3___L0), .output_2(RT2___L0), .output_0(RT___L0), .output_1(RT1___L0));
  ROM #(.dataWidth(32), .Select("low")) rom_11 (.addr(multiplexer_13_out), .data(RT_L0));
  DotMatrix #(.matrixcols(4), .matrixrows(5)) dotmatrix_10 (
    .col0(RT4___L1), .col1(RT5___L1), .col2(RT6___L1), .col3(RT7___L1));
  letter_matriz_decode letter_matriz_decode_12 (
    .\input (RT_L1), .output_3(RT7___L1), .output_2(RT6___L1), .output_0(RT4___L1), .output_1(RT5___L1));
  ROM #(.dataWidth(32), .Select("low")) rom_12 (.addr(multiplexer_14_out), .data(RT_L1));
  DotMatrix #(.matrixcols(4), .matrixrows(5)) dotmatrix_11 (
    .col0(RD0___L0), .col1(RD1___L0), .col2(RD2___L0), .col3(RD3___L0));
  letter_matriz_decode letter_matriz_decode_13 (
    .\input (RD_L0), .output_3(RD3___L0), .output_2(RD2___L0), .output_0(RD0___L0), .output_1(RD1___L0));
  ROM #(.dataWidth(32), .Select("low")) rom_13 (.addr(multiplexer_15_out), .data(RD_L0));
  DotMatrix #(.matrixcols(4), .matrixrows(5)) dotmatrix_12 (
    .col0(RD4___L1), .col1(RD5___L1), .col2(RD6___L1), .col3(RD7___L1));
  letter_matriz_decode letter_matriz_decode_14 (
    .\input (RD_L1), .output_3(RD7___L1), .output_2(RD6___L1), .output_0(RD4___L1), .output_1(RD5___L1));
  ROM #(.dataWidth(32), .Select("low")) rom_14 (.addr(multiplexer_16_out), .data(RD_L1));
  DotMatrix #(.matrixcols(4), .matrixrows(5)) dotmatrix_13 (
    .col0(RS0___L0), .col1(RS1___L0), .col2(RS2___L0), .col3(RS3___L0));
  DotMatrix #(.matrixcols(4), .matrixrows(5)) dotmatrix_14 (
    .col0(RS4___L1), .col1(RS5___L1), .col2(RS6___L1), .col3(RS7___L1));
  Multiplexer #(.select(4), .width(8), .enable("false")) multiplexer_19 (
    .in0(8'h30), .in1(8'h31), .in2(8'h32), .in3(8'h33), .in4(8'h34), .in5(8'h35), .in6(8'h36), .in7(8'h37),
    .in8(8'h38), .in9(8'h39), .in10(8'h41), .in11(8'h42), .in12(8'h43), .in13(8'h44), .in14(8'h45),
    .in15(8'h46), .out(multiplexer_19_out), .sel(IM[15:12]));
  Multiplexer #(.select(4), .width(8), .enable("false")) multiplexer_20 (
    .in0(8'h30), .in1(8'h31), .in2(8'h32), .in3(8'h33), .in4(8'h34), .in5(8'h35), .in6(8'h36), .in7(8'h37),
    .in8(8'h38), .in9(8'h39), .in10(8'h41), .in11(8'h42), .in12(8'h43), .in13(8'h44), .in14(8'h45),
    .in15(8'h46), .out(multiplexer_20_out), .sel(IM[11:8]));
  Multiplexer #(.select(4), .width(8), .enable("false")) multiplexer_21 (
    .in0(8'h30), .in1(8'h31), .in2(8'h32), .in3(8'h33), .in4(8'h34), .in5(8'h35), .in6(8'h36), .in7(8'h37),
    .in8(8'h38), .in9(8'h39), .in10(8'h41), .in11(8'h42), .in12(8'h43), .in13(8'h44), .in14(8'h45),
    .in15(8'h46), .out(multiplexer_21_out), .sel(IM[7:4]));
  Multiplexer #(.select(4), .width(8), .enable("false")) multiplexer_22 (
    .in0(8'h30), .in1(8'h31), .in2(8'h32), .in3(8'h33), .in4(8'h34), .in5(8'h35), .in6(8'h36), .in7(8'h37),
    .in8(8'h38), .in9(8'h39), .in10(8'h41), .in11(8'h42), .in12(8'h43), .in13(8'h44), .in14(8'h45),
    .in15(8'h46), .out(multiplexer_22_out), .sel(IM[3:0]));
  MUX_opCode_1b mux_opcode_1b_4 (
    .in_1(1'b0), .in_2(1'b0), .in_3(1'b0), .in_4(1'b0), .in_5(1'b0), .in_6(1'b0), .in_7(1'b0), .in_8(1'b0),
    .in_9(mux_opcode_1b_4_output), .in_10(mux_opcode_1b_4_output), .in_11(mux_opcode_1b_4_output),
    .in_12(mux_opcode_1b_4_output), .in_13(mux_opcode_1b_4_output), .in_14(mux_opcode_1b_4_output),
    .in_15(1'b0), .in_16(mux_opcode_1b_4_output), .in_17(1'b0), .in_18(1'b0), .in_19(1'b0), .in_20(1'b0),
    .in_21(1'b0), .in_22(1'b0), .in_23(1'b0), .in_24(1'b0), .in_25(1'b0), .in_26(1'b0), .in_27(1'b0),
    .in_28(1'b0), .in_29(1'b0), .in_30(1'b0), .in_31(1'b0), .in_32(1'b0), .sel(IM[31:26]), .in_34(1'b0),
    .in_35(1'b0), .in_36(1'b0), .in_37(1'b0), .in_38(1'b0), .in_39(1'b0), .in_40(1'b0), .in_41(1'b0),
    .in_42(1'b0), .in_43(1'b0), .in_44(1'b0), .in_45(1'b0), .in_46(1'b0), .in_47(1'b0), .in_48(1'b0),
    .in_49(1'b0), .in_50(1'b0), .in_51(1'b0), .in_52(1'b0), .in_53(1'b0), .in_54(1'b0), .in_55(1'b0),
    .in_56(1'b0), .in_57(1'b0), .in_58(1'b0), .in_59(1'b0), .in_60(1'b0), .in_61(1'b0), .in_62(1'b0),
    .in_63(1'b0), .in_64(1'b0), .in_65(1'b0), .\output (mux_opcode_1b_4_output));
  // Probe on IM[31:26]
  Multiplexer #(.width(8), .enable("false")) multiplexer_23 (
    .in0(8'h2d), .in1(multiplexer_19_out), .out(multiplexer_23_out), .sel(mux_opcode_1b_4_output));
  Multiplexer #(.width(8), .enable("false")) multiplexer_24 (
    .in0(8'h2d), .in1(multiplexer_20_out), .out(multiplexer_24_out), .sel(mux_opcode_1b_4_output));
  Multiplexer #(.width(8), .enable("false")) multiplexer_25 (
    .in0(8'h2d), .in1(multiplexer_21_out), .out(multiplexer_25_out), .sel(mux_opcode_1b_4_output));
  Multiplexer #(.width(8), .enable("false")) multiplexer_26 (
    .in0(8'h2d), .in1(multiplexer_22_out), .out(multiplexer_26_out), .sel(mux_opcode_1b_4_output));
  ROM #(.dataWidth(32), .Select("low")) rom_15 (.addr(multiplexer_23_out), .data(rom_15_data));
  ROM #(.dataWidth(32), .Select("low")) rom_16 (.addr(multiplexer_24_out), .data(rom_16_data));
  ROM #(.dataWidth(32), .Select("low")) rom_17 (.addr(multiplexer_25_out), .data(rom_17_data));
  ROM #(.dataWidth(32), .Select("low")) rom_18 (.addr(multiplexer_26_out), .data(rom_18_data));
  DotMatrix #(.matrixcols(4), .matrixrows(5)) dotmatrix_15 (
    .col0(IM0___L0), .col1(IM1___L0), .col2(IM2___L0), .col3(IM3___L0));
  letter_matriz_decode letter_matriz_decode_15 (
    .\input (rom_15_data), .output_3(IM3___L0), .output_2(IM2___L0), .output_0(IM0___L0), .output_1(IM1___L0));
  DotMatrix #(.matrixcols(4), .matrixrows(5)) dotmatrix_16 (
    .col0(IM4___L1), .col1(IM5___L1), .col2(IM6___L1), .col3(IM7___L1));
  letter_matriz_decode letter_matriz_decode_16 (
    .\input (rom_16_data), .output_3(IM7___L1), .output_2(IM6___L1), .output_0(IM4___L1), .output_1(IM5___L1));
  DotMatrix #(.matrixcols(4), .matrixrows(5)) dotmatrix_17 (
    .col0(IM9___L2), .col1(IM10___L2), .col2(IM11___L3), .col3(IM12___L2));
  letter_matriz_decode letter_matriz_decode_17 (
    .\input (rom_17_data), .output_3(IM12___L2), .output_2(IM11___L3), .output_0(IM9___L2),
    .output_1(IM10___L2));
  DotMatrix #(.matrixcols(4), .matrixrows(5)) dotmatrix_18 (
    .col0(I13___L3), .col1(I14___L3), .col2(I15___L3), .col3(I16___L3));
  letter_matriz_decode letter_matriz_decode_18 (
    .\input (rom_18_data), .output_3(I16___L3), .output_2(I15___L3), .output_0(I13___L3), .output_1(I14___L3));
  // Probe on IM[31:26]
  Multiplexer #(.width(32), .enable("false")) multiplexer_27 (
    .in0(undriven), .in1(32'h11f11100), .out(multiplexer_27_out), .sel(1'b0));
  MUX_opCode_2b mux_opcode_2b_1 (
    .in_1(2'b00), .in_9(2'b01), .in_10(2'b01), .in_11(2'b01), .in_12(2'b01), .in_13(2'b01), .in_14(2'b01),
    .sel(IM[31:26]), .\output (mux_opcode_2b_1_output));  // open: in_2, in_3, in_4, in_5, in_6, in_7, in_8, in_15, in_16, in_17, in_18, in_19, in_20, in_21, in_22, in_23, in_24, in_25, in_26, in_27, in_28, in_29, in_30, in_31, in_32, in_34, in_35, in_36, in_37, in_38, in_39, in_40, in_41, in_42, in_43, in_44, in_45, in_46, in_47, in_48, in_49, in_50, in_51, in_52, in_53, in_54, in_55, in_56, in_57, in_58, in_59, in_60, in_61, in_62, in_63, in_64, in_65
  Multiplexer #(.select(2), .width(32), .enable("false")) multiplexer_28 (
    .in0(RD_L0), .in1(RT_L0), .out(multiplexer_28_out), .sel(undriven_2));  // open: in2, in3
  Multiplexer #(.select(2), .width(32), .enable("false")) multiplexer_29 (
    .in0(RD_L1), .in1(RT_L1), .out(multiplexer_29_out), .sel(mux_opcode_2b_1_output));  // open: in2, in3
  Multiplexer #(.select(2), .width(32), .enable("false")) multiplexer_30 (
    .in0(32'h100000), .in1(32'h100000), .out(multiplexer_30_out), .sel(mux_opcode_2b_1_output));  // open: in2, in3
  Multiplexer #(.select(2), .width(32), .enable("false")) multiplexer_31 (
    .in0(RS_L0), .in1(RS_L0), .out(multiplexer_31_out), .sel(mux_opcode_2b_1_output));  // open: in2, in3
  Multiplexer #(.select(2), .width(32), .enable("false")) multiplexer_32 (
    .in0(RS_L1), .in1(RS_L1), .out(multiplexer_32_out), .sel(mux_opcode_2b_1_output));  // open: in2, in3
  Multiplexer #(.select(2), .width(32), .enable("false")) multiplexer_33 (
    .in0(32'h100000), .in1(32'h100000), .out(multiplexer_33_out), .sel(mux_opcode_2b_1_output));  // open: in2, in3
  Multiplexer #(.select(2), .width(32), .enable("false")) multiplexer_34 (
    .in0(RT_L0), .in1(multiplexer_27_out), .out(multiplexer_34_out), .sel(mux_opcode_2b_1_output));  // open: in2, in3
  Multiplexer #(.select(2), .width(32), .enable("false")) multiplexer_35 (
    .in0(RT_L1), .out(multiplexer_35_out), .sel(mux_opcode_2b_1_output));  // open: in1, in2, in3
  DotMatrix #(.matrixcols(4), .matrixrows(5)) dotmatrix_19 (.col0(A0_L0), .col1(A1_L0), .col2(A2_L0), .col3(A3_L0));
  letter_matriz_decode letter_matriz_decode_19 (
    .\input (multiplexer_28_out), .output_3(A3_L0), .output_2(A2_L0), .output_0(A0_L0), .output_1(A1_L0));
  DotMatrix #(.matrixcols(4), .matrixrows(5)) dotmatrix_20 (.col0(A4_L1), .col1(A5_L1), .col2(A6_L1), .col3(A7_L1));
  letter_matriz_decode letter_matriz_decode_20 (
    .\input (multiplexer_29_out), .output_3(A7_L1), .output_2(A6_L1), .output_0(A4_L1), .output_1(A5_L1));
  DotMatrix #(.matrixcols(4), .matrixrows(5)) dotmatrix_21 (.col0(A8_L2), .col1(A9_L2), .col2(A10_L2), .col3(A11_L2));
  letter_matriz_decode letter_matriz_decode_21 (
    .\input (multiplexer_30_out), .output_3(A11_L2), .output_2(A10_L2), .output_0(A8_L2), .output_1(A9_L2));
  DotMatrix #(.matrixcols(4), .matrixrows(5)) dotmatrix_22 (.col0(A12_L3), .col1(A13_L3), .col2(A14_L3), .col3(A15_L3));
  letter_matriz_decode letter_matriz_decode_22 (
    .\input (multiplexer_31_out), .output_3(A15_L3), .output_2(A14_L3), .output_0(A12_L3), .output_1(A13_L3));
  DotMatrix #(.matrixcols(4), .matrixrows(5)) dotmatrix_23 (
    .col0(A16_L4), .col1(A17_L4), .col2(A18_L4), .col3(A19__L4));
  letter_matriz_decode letter_matriz_decode_23 (
    .\input (multiplexer_32_out), .output_3(A19__L4), .output_2(A18_L4), .output_0(A16_L4), .output_1(A17_L4));
  DotMatrix #(.matrixcols(4), .matrixrows(5)) dotmatrix_24 (.col0(A20_L5), .col1(A21_L5), .col2(A22_L5), .col3(A23_L5));
  letter_matriz_decode letter_matriz_decode_24 (
    .\input (multiplexer_33_out), .output_3(A23_L5), .output_2(A22_L5), .output_0(A20_L5), .output_1(A21_L5));
  DotMatrix #(.matrixcols(4), .matrixrows(5)) dotmatrix_25 (.col0(A24_L5), .col1(A25_L5), .col2(A26_L5), .col3(A27_L5));
  letter_matriz_decode letter_matriz_decode_25 (
    .\input (multiplexer_34_out), .output_3(A27_L5), .output_2(A26_L5), .output_0(A24_L5), .output_1(A25_L5));
  DotMatrix #(.matrixcols(4), .matrixrows(5)) dotmatrix_26 (.col0(A28_L5), .col1(A29_L5), .col2(A30_L5), .col3(A31_L5));
  letter_matriz_decode letter_matriz_decode_26 (
    .\input (multiplexer_35_out), .output_3(A31_L5), .output_2(A30_L5), .output_0(A28_L5), .output_1(A29_L5));

  assign I18___L4 = I17___L5;
  // also tied to VCC on the sheet: mux_opcode_1b_4_output

  // Other names for the same wires on the sheet: adressJM[25:0] = IM[25:0]; funct[5:0] = IM[5:0];
  //   immd[15:0] = IM[15:0]; shamt[4:0] = IM[10:6]; rd[4:0] = IM[15:11]; rt[4:0] = IM[20:16]; rs[4:0] = IM[25:21];
  //   opCode[5:0] = IM[31:26]

  // Notes on the sheet:
  //   SHAMT
  //   contents of rom_1 (hex, n*v repeats v):
  //   32*151c100 0 d10000 81008100 4*151c100 810000 e0110000 11e00000 50205000 40e04000 300000 40404000
  //   100000 10400100 f111f100 80f10000 7151d100 1151b100 c140f100 d1517100 f1517100 171c100 f151f100
  //   d151f100 a00000 a00000 40a00000 a0a00000 a0400000 151c100 151c100 f141f100 f151a000 f1111100
  //   f111e000 f1515100 f1414100 f1317100 f140f100 11f11100 3010f100 f140b100 f1101000 f1c0f100 f101f100
  //   f111f100 f141c100 c141f100 f141b000 d1517100 1f10100 f110f100 e110e100 f120f100 b140b100 81708100
  //   31519100 f1110000 1401000 11ff0000 40804000 10101000 80400000
  //   contents of rom_2 (hex, n*v repeats v):
  //   32*151c100 0 d10000 81008100 4*151c100 810000 e0110000 11e00000 50205000 40e04000 300000 40404000
  //   100000 10400100 f111f100 80f10000 7151d100 1151b100 c140f100 d1517100 f1517100 171c100 f151f100
  //   d151f100 a00000 a00000 40a00000 a0a00000 a0400000 151c100 151c100 f141f100 f151a000 f1111100
  //   f111e000 f1515100 f1414100 f1317100 f140f100 11f11100 3010f100 f140b100 f1101000 f1c0f100 f101f100
  //   f111f100 f141c100 c141f100 f141b000 d1517100 1f10100 f110f100 e110e100 f120f100 b140b100 81708100
  //   31519100 f1110000 1401000 11ff0000 40804000 10101000 80400000
  //   Actual Instruction
  //   contents of rom_3 (hex, n*v repeats v):
  //   32*151c100 0 d10000 81008100 4*151c100 810000 e0110000 11e00000 50205000 40e04000 300000 40404000
  //   100000 10400100 f111f100 80f10000 7151d100 1151b100 c140f100 d1517100 f1517100 171c100 f151f100
  //   d151f100 a00000 a00000 40a00000 a0a00000 a0400000 151c100 151c100 f141f100 f151a000 f1111100
  //   f111e000 f1515100 f1414100 f1317100 f140f100 11f11100 3010f100 f140b100 f1101000 f1c0f100 f101f100
  //   f111f100 f141c100 c141f100 f141b000 d1517100 1f10100 f110f100 e110e100 f120f100 b140b100 81708100
  //   31519100 f1110000 1401000 11ff0000 40804000 10101000 80400000
  //   contents of rom_4 (hex, n*v repeats v):
  //   32*151c100 0 d10000 81008100 4*151c100 810000 e0110000 11e00000 50205000 40e04000 300000 40404000
  //   100000 10400100 f111f100 80f10000 7151d100 1151b100 c140f100 d1517100 f1517100 171c100 f151f100
  //   d151f100 a00000 a00000 40a00000 a0a00000 a0400000 151c100 151c100 f141f100 f151a000 f1111100
  //   f111e000 f1515100 f1414100 f1317100 f140f100 11f11100 3010f100 f140b100 f1101000 f1c0f100 f101f100
  //   f111f100 f141c100 c141f100 f141b000 d1517100 1f10100 f110f100 e110e100 f120f100 b140b100 81708100
  //   31519100 f1110000 1401000 11ff0000 40804000 10101000 80400000
  //   contents of rom_5 (hex, n*v repeats v):
  //   32*151c100 0 d10000 81008100 4*151c100 810000 e0110000 11e00000 50205000 40e04000 300000 40404000
  //   100000 10400100 f111f100 80f10000 7151d100 1151b100 c140f100 d1517100 f1517100 171c100 f151f100
  //   d151f100 a00000 a00000 40a00000 a0a00000 a0400000 151c100 151c100 f141f100 f151a000 f1111100
  //   f111e000 f1515100 f1414100 f1317100 f140f100 11f11100 3010f100 f140b100 f1101000 f1c0f100 f101f100
  //   f111f100 f141c100 c141f100 f141b000 d1517100 1f10100 f110f100 e110e100 f120f100 b140b100 81708100
  //   31519100 f1110000 1401000 11ff0000 40804000 10101000 80400000
  //   contents of rom_6 (hex, n*v repeats v):
  //   32*151c100 0 d10000 81008100 4*151c100 810000 e0110000 11e00000 50205000 40e04000 300000 40404000
  //   100000 10400100 f111f100 80f10000 7151d100 1151b100 c140f100 d1517100 f1517100 171c100 f151f100
  //   d151f100 a00000 a00000 40a00000 a0a00000 a0400000 151c100 151c100 f141f100 f151a000 f1111100
  //   f111e000 f1515100 f1414100 f1317100 f140f100 11f11100 3010f100 f140b100 f1101000 f1c0f100 f101f100
  //   f111f100 f141c100 c141f100 f141b000 d1517100 1f10100 f110f100 e110e100 f120f100 b140b100 81708100
  //   31519100 f1110000 1401000 11ff0000 40804000 10101000 80400000
  //   contents of rom_7 (hex, n*v repeats v):
  //   32*151c100 0 d10000 81008100 4*151c100 810000 e0110000 11e00000 50205000 40e04000 300000 40404000
  //   100000 10400100 f111f100 80f10000 7151d100 1151b100 c140f100 d1517100 f1517100 171c100 f151f100
  //   d151f100 a00000 a00000 40a00000 a0a00000 a0400000 151c100 151c100 f141f100 f151a000 f1111100
  //   f111e000 f1515100 f1414100 f1317100 f140f100 11f11100 3010f100 f140b100 f1101000 f1c0f100 f101f100
  //   f111f100 f141c100 c141f100 f141b000 d1517100 1f10100 f110f100 e110e100 f120f100 b140b100 81708100
  //   31519100 f1110000 1401000 11ff0000 40804000 10101000 80400000
  //   contents of rom_8 (hex, n*v repeats v):
  //   32*151c100 0 d10000 81008100 4*151c100 810000 e0110000 11e00000 50205000 40e04000 300000 40404000
  //   100000 10400100 f111f100 80f10000 7151d100 1151b100 c140f100 d1517100 f1517100 171c100 f151f100
  //   d151f100 a00000 a00000 40a00000 a0a00000 a0400000 151c100 151c100 f141f100 f151a000 f1111100
  //   f111e000 f1515100 f1414100 f1317100 f140f100 11f11100 3010f100 f140b100 f1101000 f1c0f100 f101f100
  //   f111f100 f141c100 c141f100 f141b000 d1517100 1f10100 f110f100 e110e100 f120f100 b140b100 81708100
  //   31519100 f1110000 1401000 11ff0000 40804000 10101000 80400000
  //   Rs
  //   Rt
  //   Rd
  //   contents of rom_9 (hex, n*v repeats v):
  //   32*151c100 0 d10000 81008100 4*151c100 810000 e0110000 11e00000 50205000 40e04000 300000 40404000
  //   100000 10400100 f111f100 80f10000 7151d100 1151b100 c140f100 d1517100 f1517100 171c100 f151f100
  //   d151f100 a00000 a00000 40a00000 a0a00000 a0400000 151c100 151c100 f141f100 f151a000 f1111100
  //   f111e000 f1515100 f1414100 f1317100 f140f100 11f11100 3010f100 f140b100 f1101000 f1c0f100 f101f100
  //   f111f100 f141c100 c141f100 f141b000 d1517100 1f10100 f110f100 e110e100 f120f100 b140b100 81708100
  //   31519100 f1110000 1401000 11ff0000 40804000 10101000 80400000
  //   contents of rom_10 (hex, n*v repeats v):
  //   32*151c100 0 d10000 81008100 4*151c100 810000 e0110000 11e00000 50205000 40e04000 300000 40404000
  //   100000 10400100 f111f100 80f10000 7151d100 1151b100 c140f100 d1517100 f1517100 171c100 f151f100
  //   d151f100 a00000 a00000 40a00000 a0a00000 a0400000 151c100 151c100 f141f100 f151a000 f1111100
  //   f111e000 f1515100 f1414100 f1317100 f140f100 11f11100 3010f100 f140b100 f1101000 f1c0f100 f101f100
  //   f111f100 f141c100 c141f100 f141b000 d1517100 1f10100 f110f100 e110e100 f120f100 b140b100 81708100
  //   31519100 f1110000 1401000 11ff0000 40804000 10101000 80400000
  //   contents of rom_11 (hex, n*v repeats v):
  //   32*151c100 0 d10000 81008100 4*151c100 810000 e0110000 11e00000 50205000 40e04000 300000 40404000
  //   100000 10400100 f111f100 80f10000 7151d100 1151b100 c140f100 d1517100 f1517100 171c100 f151f100
  //   d151f100 a00000 a00000 40a00000 a0a00000 a0400000 151c100 151c100 f141f100 f151a000 f1111100
  //   f111e000 f1515100 f1414100 f1317100 f140f100 11f11100 3010f100 f140b100 f1101000 f1c0f100 f101f100
  //   f111f100 f141c100 c141f100 f141b000 d1517100 1f10100 f110f100 e110e100 f120f100 b140b100 81708100
  //   31519100 f1110000 1401000 11ff0000 40804000 10101000 80400000
  //   contents of rom_12 (hex, n*v repeats v):
  //   32*151c100 0 d10000 81008100 4*151c100 810000 e0110000 11e00000 50205000 40e04000 300000 40404000
  //   100000 10400100 f111f100 80f10000 7151d100 1151b100 c140f100 d1517100 f1517100 171c100 f151f100
  //   d151f100 a00000 a00000 40a00000 a0a00000 a0400000 151c100 151c100 f141f100 f151a000 f1111100
  //   f111e000 f1515100 f1414100 f1317100 f140f100 11f11100 3010f100 f140b100 f1101000 f1c0f100 f101f100
  //   f111f100 f141c100 c141f100 f141b000 d1517100 1f10100 f110f100 e110e100 f120f100 b140b100 81708100
  //   31519100 f1110000 1401000 11ff0000 40804000 10101000 80400000
  //   contents of rom_13 (hex, n*v repeats v):
  //   32*151c100 0 d10000 81008100 4*151c100 810000 e0110000 11e00000 50205000 40e04000 300000 40404000
  //   100000 10400100 f111f100 80f10000 7151d100 1151b100 c140f100 d1517100 f1517100 171c100 f151f100
  //   d151f100 a00000 a00000 40a00000 a0a00000 a0400000 151c100 151c100 f141f100 f151a000 f1111100
  //   f111e000 f1515100 f1414100 f1317100 f140f100 11f11100 3010f100 f140b100 f1101000 f1c0f100 f101f100
  //   f111f100 f141c100 c141f100 f141b000 d1517100 1f10100 f110f100 e110e100 f120f100 b140b100 81708100
  //   31519100 f1110000 1401000 11ff0000 40804000 10101000 80400000
  //   contents of rom_14 (hex, n*v repeats v):
  //   32*151c100 0 d10000 81008100 4*151c100 810000 e0110000 11e00000 50205000 40e04000 300000 40404000
  //   100000 10400100 f111f100 80f10000 7151d100 1151b100 c140f100 d1517100 f1517100 171c100 f151f100
  //   d151f100 a00000 a00000 40a00000 a0a00000 a0400000 151c100 151c100 f141f100 f151a000 f1111100
  //   f111e000 f1515100 f1414100 f1317100 f140f100 11f11100 3010f100 f140b100 f1101000 f1c0f100 f101f100
  //   f111f100 f141c100 c141f100 f141b000 d1517100 1f10100 f110f100 e110e100 f120f100 b140b100 81708100
  //   31519100 f1110000 1401000 11ff0000 40804000 10101000 80400000
  //   Immediate
  //   contents of rom_15 (hex, n*v repeats v):
  //   32*151c100 0 d10000 81008100 4*151c100 810000 e0110000 11e00000 50205000 40e04000 300000 40404000
  //   100000 10400100 f111f100 80f10000 7151d100 1151b100 c140f100 d1517100 f1517100 171c100 f151f100
  //   d151f100 a00000 a00000 40a00000 a0a00000 a0400000 151c100 151c100 f141f100 f151a000 f1111100
  //   f111e000 f1515100 f1414100 f1317100 f140f100 11f11100 3010f100 f140b100 f1101000 f1c0f100 f101f100
  //   f111f100 f141c100 c141f100 f141b000 d1517100 1f10100 f110f100 e110e100 f120f100 b140b100 81708100
  //   31519100 f1110000 1401000 11ff0000 40804000 10101000 80400000
  //   contents of rom_16 (hex, n*v repeats v):
  //   32*151c100 0 d10000 81008100 4*151c100 810000 e0110000 11e00000 50205000 40e04000 300000 40404000
  //   100000 10400100 f111f100 80f10000 7151d100 1151b100 c140f100 d1517100 f1517100 171c100 f151f100
  //   d151f100 a00000 a00000 40a00000 a0a00000 a0400000 151c100 151c100 f141f100 f151a000 f1111100
  //   f111e000 f1515100 f1414100 f1317100 f140f100 11f11100 3010f100 f140b100 f1101000 f1c0f100 f101f100
  //   f111f100 f141c100 c141f100 f141b000 d1517100 1f10100 f110f100 e110e100 f120f100 b140b100 81708100
  //   31519100 f1110000 1401000 11ff0000 40804000 10101000 80400000
  //   contents of rom_17 (hex, n*v repeats v):
  //   32*151c100 0 d10000 81008100 4*151c100 810000 e0110000 11e00000 50205000 40e04000 300000 40404000
  //   100000 10400100 f111f100 80f10000 7151d100 1151b100 c140f100 d1517100 f1517100 171c100 f151f100
  //   d151f100 a00000 a00000 40a00000 a0a00000 a0400000 151c100 151c100 f141f100 f151a000 f1111100
  //   f111e000 f1515100 f1414100 f1317100 f140f100 11f11100 3010f100 f140b100 f1101000 f1c0f100 f101f100
  //   f111f100 f141c100 c141f100 f141b000 d1517100 1f10100 f110f100 e110e100 f120f100 b140b100 81708100
  //   31519100 f1110000 1401000 11ff0000 40804000 10101000 80400000
  //   contents of rom_18 (hex, n*v repeats v):
  //   32*151c100 0 d10000 81008100 4*151c100 810000 e0110000 11e00000 50205000 40e04000 300000 40404000
  //   100000 10400100 f111f100 80f10000 7151d100 1151b100 c140f100 d1517100 f1517100 171c100 f151f100
  //   d151f100 a00000 a00000 40a00000 a0a00000 a0400000 151c100 151c100 f141f100 f151a000 f1111100
  //   f111e000 f1515100 f1414100 f1317100 f140f100 11f11100 3010f100 f140b100 f1101000 f1c0f100 f101f100
  //   f111f100 f141c100 c141f100 f141b000 d1517100 1f10100 f110f100 e110e100 f120f100 b140b100 81708100
  //   31519100 f1110000 1401000 11ff0000 40804000 10101000 80400000
  //   Arguments
endmodule

module letter_matriz_decode (
  input  [31:0] \input ,
  output [4:0] output_3,
  output [4:0] output_2,
  output [4:0] output_1,
  output [4:0] output_0
);

  buf buffer_1 (output_3[4], \input [0]);
  buf buffer_2 (output_3[0], \input [4]);
  buf buffer_3 (output_3[1], \input [5]);
  buf buffer_4 (output_3[2], \input [6]);
  buf buffer_5 (output_2[4], \input [8]);
  buf buffer_6 (output_2[0], \input [12]);
  buf buffer_7 (output_2[1], \input [13]);
  buf buffer_8 (output_2[2], \input [14]);
  buf buffer_9 (output_3[3], \input [7]);
  buf buffer_10 (output_2[3], \input [15]);

  assign output_0 = {\input [24], \input [31:28]};
  assign output_1 = {\input [16], \input [23:20]};

  // Notes on the sheet:
  //   output_1: pull=down
  //   output_0: pull=down
  //   output_3: pull=down
  //   output_2: pull=down
  //   input: pull=down
endmodule

module MUX_funct_1b (
  input  in_1,
  input  in_2,
  input  in_3,
  input  in_4,
  input  in_5,
  input  in_6,
  input  in_7,
  input  in_8,
  input  in_9,
  input  in_10,
  input  in_11,
  input  in_12,
  input  in_13,
  input  in_14,
  input  in_15,
  input  in_16,
  input  in_17,
  input  in_18,
  input  in_19,
  input  in_20,
  input  in_21,
  input  in_22,
  input  in_23,
  input  in_24,
  input  in_25,
  input  in_26,
  input  in_27,
  input  in_28,
  input  in_29,
  input  in_30,
  input  in_31,
  input  in_32,
  input  [5:0] sel,
  input  in_34,
  input  in_35,
  input  in_36,
  input  in_37,
  input  in_38,
  input  in_39,
  input  in_40,
  input  in_41,
  input  in_42,
  input  in_43,
  input  in_44,
  input  in_45,
  input  in_46,
  input  in_47,
  input  in_48,
  input  in_49,
  input  in_50,
  input  in_51,
  input  in_52,
  input  in_53,
  input  in_54,
  input  in_55,
  input  in_56,
  input  in_57,
  input  in_58,
  input  in_59,
  input  in_60,
  input  in_61,
  input  in_62,
  input  in_63,
  input  in_64,
  input  in_65,
  output \output 
);

  wire multiplexer_1_out, multiplexer_2_out;

  Multiplexer #(.select(5), .enable("false")) multiplexer_1 (
    .in0(in_1), .in1(in_2), .in2(in_3), .in3(in_4), .in4(in_5), .in5(in_6), .in6(in_7), .in7(in_8),
    .in8(in_9), .in9(in_10), .in10(in_11), .in11(in_12), .in12(in_13), .in13(in_14), .in14(in_15),
    .in15(in_16), .in16(in_17), .in17(in_18), .in18(in_19), .in19(in_20), .in20(in_21), .in21(in_22),
    .in22(in_23), .in23(in_24), .in24(in_25), .in25(in_26), .in26(in_27), .in27(in_28), .in28(in_29),
    .in29(in_30), .in30(in_31), .in31(in_32), .out(multiplexer_1_out), .sel(sel[4:0]));
  Multiplexer #(.select(5), .enable("false")) multiplexer_2 (
    .in0(in_34), .in1(in_35), .in2(in_36), .in3(in_37), .in4(in_38), .in5(in_39), .in6(in_40), .in7(in_41),
    .in8(in_42), .in9(in_43), .in10(in_44), .in11(in_45), .in12(in_46), .in13(in_47), .in14(in_48),
    .in15(in_49), .in16(in_50), .in17(in_51), .in18(in_52), .in19(in_53), .in20(in_54), .in21(in_55),
    .in22(in_56), .in23(in_57), .in24(in_58), .in25(in_59), .in26(in_60), .in27(in_61), .in28(in_62),
    .in29(in_63), .in30(in_64), .in31(in_65), .out(multiplexer_2_out), .sel(sel[4:0]));
  Multiplexer #(.enable("false")) multiplexer_3 (
    .in0(multiplexer_1_out), .in1(multiplexer_2_out), .out(\output ), .sel(sel[5]));
endmodule

module MUX_funct_8b (
  input  [7:0] in_1,
  input  [7:0] in_2,
  input  [7:0] in_3,
  input  [7:0] in_4,
  input  [7:0] in_5,
  input  [7:0] in_6,
  input  [7:0] in_7,
  input  [7:0] in_8,
  input  [7:0] in_9,
  input  [7:0] in_10,
  input  [7:0] in_11,
  input  [7:0] in_12,
  input  [7:0] in_13,
  input  [7:0] in_14,
  input  [7:0] in_15,
  input  [7:0] in_16,
  input  [7:0] in_17,
  input  [7:0] in_18,
  input  [7:0] in_19,
  input  [7:0] in_20,
  input  [7:0] in_21,
  input  [7:0] in_22,
  input  [7:0] in_23,
  input  [7:0] in_24,
  input  [7:0] in_25,
  input  [7:0] in_26,
  input  [7:0] in_27,
  input  [7:0] in_28,
  input  [7:0] in_29,
  input  [7:0] in_30,
  input  [7:0] in_31,
  input  [7:0] in_32,
  input  [5:0] sel,
  input  [7:0] in_34,
  input  [7:0] in_35,
  input  [7:0] in_36,
  input  [7:0] in_37,
  input  [7:0] in_38,
  input  [7:0] in_39,
  input  [7:0] in_40,
  input  [7:0] in_41,
  input  [7:0] in_42,
  input  [7:0] in_43,
  input  [7:0] in_44,
  input  [7:0] in_45,
  input  [7:0] in_46,
  input  [7:0] in_47,
  input  [7:0] in_48,
  input  [7:0] in_49,
  input  [7:0] in_50,
  input  [7:0] in_51,
  input  [7:0] in_52,
  input  [7:0] in_53,
  input  [7:0] in_54,
  input  [7:0] in_55,
  input  [7:0] in_56,
  input  [7:0] in_57,
  input  [7:0] in_58,
  input  [7:0] in_59,
  input  [7:0] in_60,
  input  [7:0] in_61,
  input  [7:0] in_62,
  input  [7:0] in_63,
  input  [7:0] in_64,
  input  [7:0] in_65,
  output [7:0] \output 
);

  wire [7:0] multiplexer_1_out, multiplexer_2_out;

  Multiplexer #(.select(5), .width(8), .enable("false")) multiplexer_1 (
    .in0(in_1), .in1(in_2), .in2(in_3), .in3(in_4), .in4(in_5), .in5(in_6), .in6(in_7), .in7(in_8),
    .in8(in_9), .in9(in_10), .in10(in_11), .in11(in_12), .in12(in_13), .in13(in_14), .in14(in_15),
    .in15(in_16), .in16(in_17), .in17(in_18), .in18(in_19), .in19(in_20), .in20(in_21), .in21(in_22),
    .in22(in_23), .in23(in_24), .in24(in_25), .in25(in_26), .in26(in_27), .in27(in_28), .in28(in_29),
    .in29(in_30), .in30(in_31), .in31(in_32), .out(multiplexer_1_out), .sel(sel[4:0]));
  Multiplexer #(.select(5), .width(8), .enable("false")) multiplexer_2 (
    .in0(in_34), .in1(in_35), .in2(in_36), .in3(in_37), .in4(in_38), .in5(in_39), .in6(in_40), .in7(in_41),
    .in8(in_42), .in9(in_43), .in10(in_44), .in11(in_45), .in12(in_46), .in13(in_47), .in14(in_48),
    .in15(in_49), .in16(in_50), .in17(in_51), .in18(in_52), .in19(in_53), .in20(in_54), .in21(in_55),
    .in22(in_56), .in23(in_57), .in24(in_58), .in25(in_59), .in26(in_60), .in27(in_61), .in28(in_62),
    .in29(in_63), .in30(in_64), .in31(in_65), .out(multiplexer_2_out), .sel(sel[4:0]));
  Multiplexer #(.width(8), .enable("false")) multiplexer_3 (
    .in0(multiplexer_1_out), .in1(multiplexer_2_out), .out(\output ), .sel(sel[5]));
endmodule

module MUX_funct_16b (
  input  [31:0] in_1,
  input  [31:0] in_2,
  input  [31:0] in_3,
  input  [31:0] in_4,
  input  [31:0] in_5,
  input  [31:0] in_6,
  input  [31:0] in_7,
  input  [31:0] in_8,
  input  [31:0] in_9,
  input  [31:0] in_10,
  input  [31:0] in_11,
  input  [31:0] in_12,
  input  [31:0] in_13,
  input  [31:0] in_14,
  input  [31:0] in_15,
  input  [31:0] in_16,
  input  [31:0] in_17,
  input  [31:0] in_18,
  input  [31:0] in_19,
  input  [31:0] in_20,
  input  [31:0] in_21,
  input  [31:0] in_22,
  input  [31:0] in_23,
  input  [31:0] in_24,
  input  [31:0] in_25,
  input  [31:0] in_26,
  input  [31:0] in_27,
  input  [31:0] in_28,
  input  [31:0] in_29,
  input  [31:0] in_30,
  input  [31:0] in_31,
  input  [31:0] in_32,
  input  [5:0] sel,
  input  [31:0] in_34,
  input  [31:0] in_35,
  input  [31:0] in_36,
  input  [31:0] in_37,
  input  [31:0] in_38,
  input  [31:0] in_39,
  input  [31:0] in_40,
  input  [31:0] in_41,
  input  [31:0] in_42,
  input  [31:0] in_43,
  input  [31:0] in_44,
  input  [31:0] in_45,
  input  [31:0] in_46,
  input  [31:0] in_47,
  input  [31:0] in_48,
  input  [31:0] in_49,
  input  [31:0] in_50,
  input  [31:0] in_51,
  input  [31:0] in_52,
  input  [31:0] in_53,
  input  [31:0] in_54,
  input  [31:0] in_55,
  input  [31:0] in_56,
  input  [31:0] in_57,
  input  [31:0] in_58,
  input  [31:0] in_59,
  input  [31:0] in_60,
  input  [31:0] in_61,
  input  [31:0] in_62,
  input  [31:0] in_63,
  input  [31:0] in_64,
  input  [31:0] in_65,
  output [31:0] \output 
);

  wire [31:0] multiplexer_1_out, multiplexer_2_out;

  Multiplexer #(.select(5), .width(32), .enable("false")) multiplexer_1 (
    .in0(in_1), .in1(in_2), .in2(in_3), .in3(in_4), .in4(in_5), .in5(in_6), .in6(in_7), .in7(in_8),
    .in8(in_9), .in9(in_10), .in10(in_11), .in11(in_12), .in12(in_13), .in13(in_14), .in14(in_15),
    .in15(in_16), .in16(in_17), .in17(in_18), .in18(in_19), .in19(in_20), .in20(in_21), .in21(in_22),
    .in22(in_23), .in23(in_24), .in24(in_25), .in25(in_26), .in26(in_27), .in27(in_28), .in28(in_29),
    .in29(in_30), .in30(in_31), .in31(in_32), .out(multiplexer_1_out), .sel(sel[4:0]));
  Multiplexer #(.select(5), .width(32), .enable("false")) multiplexer_2 (
    .in0(in_34), .in1(in_35), .in2(in_36), .in3(in_37), .in4(in_38), .in5(in_39), .in6(in_40), .in7(in_41),
    .in8(in_42), .in9(in_43), .in10(in_44), .in11(in_45), .in12(in_46), .in13(in_47), .in14(in_48),
    .in15(in_49), .in16(in_50), .in17(in_51), .in18(in_52), .in19(in_53), .in20(in_54), .in21(in_55),
    .in22(in_56), .in23(in_57), .in24(in_58), .in25(in_59), .in26(in_60), .in27(in_61), .in28(in_62),
    .in29(in_63), .in30(in_64), .in31(in_65), .out(multiplexer_2_out), .sel(sel[4:0]));
  Multiplexer #(.width(32), .enable("false")) multiplexer_3 (
    .in0(multiplexer_1_out), .in1(multiplexer_2_out), .out(\output ), .sel(sel[5]));
endmodule
module MUX_funct_20b (
  input  [31:0] in_1,
  input  [31:0] in_2,
  input  [31:0] in_3,
  input  [31:0] in_4,
  input  [31:0] in_5,
  input  [31:0] in_6,
  input  [31:0] in_7,
  input  [31:0] in_8,
  input  [31:0] in_9,
  input  [31:0] in_10,
  input  [31:0] in_11,
  input  [31:0] in_12,
  input  [31:0] in_13,
  input  [31:0] in_14,
  input  [31:0] in_15,
  input  [31:0] in_16,
  input  [31:0] in_17,
  input  [31:0] in_18,
  input  [31:0] in_19,
  input  [31:0] in_20,
  input  [31:0] in_21,
  input  [31:0] in_22,
  input  [31:0] in_23,
  input  [31:0] in_24,
  input  [31:0] in_25,
  input  [31:0] in_26,
  input  [31:0] in_27,
  input  [31:0] in_28,
  input  [31:0] in_29,
  input  [31:0] in_30,
  input  [31:0] in_31,
  input  [31:0] in_32,
  input  [5:0] sel,
  input  [31:0] in_34,
  input  [31:0] in_35,
  input  [31:0] in_36,
  input  [31:0] in_37,
  input  [31:0] in_38,
  input  [31:0] in_39,
  input  [31:0] in_40,
  input  [31:0] in_41,
  input  [31:0] in_42,
  input  [31:0] in_43,
  input  [31:0] in_44,
  input  [31:0] in_45,
  input  [31:0] in_46,
  input  [31:0] in_47,
  input  [31:0] in_48,
  input  [31:0] in_49,
  input  [31:0] in_50,
  input  [31:0] in_51,
  input  [31:0] in_52,
  input  [31:0] in_53,
  input  [31:0] in_54,
  input  [31:0] in_55,
  input  [31:0] in_56,
  input  [31:0] in_57,
  input  [31:0] in_58,
  input  [31:0] in_59,
  input  [31:0] in_60,
  input  [31:0] in_61,
  input  [31:0] in_62,
  input  [31:0] in_63,
  input  [31:0] in_64,
  input  [31:0] in_65,
  output [31:0] \output 
);

  wire [31:0] multiplexer_1_out, multiplexer_2_out;

  Multiplexer #(.select(5), .width(32), .enable("false")) multiplexer_1 (
    .in0(in_1), .in1(in_2), .in2(in_3), .in3(in_4), .in4(in_5), .in5(in_6), .in6(in_7), .in7(in_8),
    .in8(in_9), .in9(in_10), .in10(in_11), .in11(in_12), .in12(in_13), .in13(in_14), .in14(in_15),
    .in15(in_16), .in16(in_17), .in17(in_18), .in18(in_19), .in19(in_20), .in20(in_21), .in21(in_22),
    .in22(in_23), .in23(in_24), .in24(in_25), .in25(in_26), .in26(in_27), .in27(in_28), .in28(in_29),
    .in29(in_30), .in30(in_31), .in31(in_32), .out(multiplexer_1_out), .sel(sel[4:0]));
  Multiplexer #(.select(5), .width(32), .enable("false")) multiplexer_2 (
    .in0(in_34), .in1(in_35), .in2(in_36), .in3(in_37), .in4(in_38), .in5(in_39), .in6(in_40), .in7(in_41),
    .in8(in_42), .in9(in_43), .in10(in_44), .in11(in_45), .in12(in_46), .in13(in_47), .in14(in_48),
    .in15(in_49), .in16(in_50), .in17(in_51), .in18(in_52), .in19(in_53), .in20(in_54), .in21(in_55),
    .in22(in_56), .in23(in_57), .in24(in_58), .in25(in_59), .in26(in_60), .in27(in_61), .in28(in_62),
    .in29(in_63), .in30(in_64), .in31(in_65), .out(multiplexer_2_out), .sel(sel[4:0]));
  Multiplexer #(.width(32), .enable("false")) multiplexer_3 (
    .in0(multiplexer_1_out), .in1(multiplexer_2_out), .out(\output ), .sel(sel[5]));
endmodule

module MUX_funct_32b (
  input  [31:0] in_1,
  input  [31:0] in_2,
  input  [31:0] in_3,
  input  [31:0] in_4,
  input  [31:0] in_5,
  input  [31:0] in_6,
  input  [31:0] in_7,
  input  [31:0] in_8,
  input  [31:0] in_9,
  input  [31:0] in_10,
  input  [31:0] in_11,
  input  [31:0] in_12,
  input  [31:0] in_13,
  input  [31:0] in_14,
  input  [31:0] in_15,
  input  [31:0] in_16,
  input  [31:0] in_17,
  input  [31:0] in_18,
  input  [31:0] in_19,
  input  [31:0] in_20,
  input  [31:0] in_21,
  input  [31:0] in_22,
  input  [31:0] in_23,
  input  [31:0] in_24,
  input  [31:0] in_25,
  input  [31:0] in_26,
  input  [31:0] in_27,
  input  [31:0] in_28,
  input  [31:0] in_29,
  input  [31:0] in_30,
  input  [31:0] in_31,
  input  [31:0] in_32,
  input  [5:0] sel,
  input  [31:0] in_34,
  input  [31:0] in_35,
  input  [31:0] in_36,
  input  [31:0] in_37,
  input  [31:0] in_38,
  input  [31:0] in_39,
  input  [31:0] in_40,
  input  [31:0] in_41,
  input  [31:0] in_42,
  input  [31:0] in_43,
  input  [31:0] in_44,
  input  [31:0] in_45,
  input  [31:0] in_46,
  input  [31:0] in_47,
  input  [31:0] in_48,
  input  [31:0] in_49,
  input  [31:0] in_50,
  input  [31:0] in_51,
  input  [31:0] in_52,
  input  [31:0] in_53,
  input  [31:0] in_54,
  input  [31:0] in_55,
  input  [31:0] in_56,
  input  [31:0] in_57,
  input  [31:0] in_58,
  input  [31:0] in_59,
  input  [31:0] in_60,
  input  [31:0] in_61,
  input  [31:0] in_62,
  input  [31:0] in_63,
  input  [31:0] in_64,
  input  [31:0] in_65,
  output [31:0] \output 
);

  wire [31:0] multiplexer_1_out, multiplexer_2_out;

  Multiplexer #(.select(5), .width(32), .enable("false")) multiplexer_1 (
    .in0(in_1), .in1(in_2), .in2(in_3), .in3(in_4), .in4(in_5), .in5(in_6), .in6(in_7), .in7(in_8),
    .in8(in_9), .in9(in_10), .in10(in_11), .in11(in_12), .in12(in_13), .in13(in_14), .in14(in_15),
    .in15(in_16), .in16(in_17), .in17(in_18), .in18(in_19), .in19(in_20), .in20(in_21), .in21(in_22),
    .in22(in_23), .in23(in_24), .in24(in_25), .in25(in_26), .in26(in_27), .in27(in_28), .in28(in_29),
    .in29(in_30), .in30(in_31), .in31(in_32), .out(multiplexer_1_out), .sel(sel[4:0]));
  Multiplexer #(.select(5), .width(32), .enable("false")) multiplexer_2 (
    .in0(in_34), .in1(in_35), .in2(in_36), .in3(in_37), .in4(in_38), .in5(in_39), .in6(in_40), .in7(in_41),
    .in8(in_42), .in9(in_43), .in10(in_44), .in11(in_45), .in12(in_46), .in13(in_47), .in14(in_48),
    .in15(in_49), .in16(in_50), .in17(in_51), .in18(in_52), .in19(in_53), .in20(in_54), .in21(in_55),
    .in22(in_56), .in23(in_57), .in24(in_58), .in25(in_59), .in26(in_60), .in27(in_61), .in28(in_62),
    .in29(in_63), .in30(in_64), .in31(in_65), .out(multiplexer_2_out), .sel(sel[4:0]));
  Multiplexer #(.width(32), .enable("false")) multiplexer_3 (
    .in0(multiplexer_1_out), .in1(multiplexer_2_out), .out(\output ), .sel(sel[5]));
endmodule

module MUX_opCode_1b (
  input  in_1,
  input  in_2,
  input  in_3,
  input  in_4,
  input  in_5,
  input  in_6,
  input  in_7,
  input  in_8,
  input  in_9,
  input  in_10,
  input  in_11,
  input  in_12,
  input  in_13,
  input  in_14,
  input  in_15,
  input  in_16,
  input  in_17,
  input  in_18,
  input  in_19,
  input  in_20,
  input  in_21,
  input  in_22,
  input  in_23,
  input  in_24,
  input  in_25,
  input  in_26,
  input  in_27,
  input  in_28,
  input  in_29,
  input  in_30,
  input  in_31,
  input  in_32,
  input  [5:0] sel,
  input  in_34,
  input  in_35,
  input  in_36,
  input  in_37,
  input  in_38,
  input  in_39,
  input  in_40,
  input  in_41,
  input  in_42,
  input  in_43,
  input  in_44,
  input  in_45,
  input  in_46,
  input  in_47,
  input  in_48,
  input  in_49,
  input  in_50,
  input  in_51,
  input  in_52,
  input  in_53,
  input  in_54,
  input  in_55,
  input  in_56,
  input  in_57,
  input  in_58,
  input  in_59,
  input  in_60,
  input  in_61,
  input  in_62,
  input  in_63,
  input  in_64,
  input  in_65,
  output \output 
);

  wire multiplexer_1_out, multiplexer_2_out;
  wire [5:0] opCode;

  Multiplexer #(.select(5), .enable("false")) multiplexer_1 (
    .in0(in_1), .in1(in_2), .in2(in_3), .in3(in_4), .in4(in_5), .in5(in_6), .in6(in_7), .in7(in_8),
    .in8(in_9), .in9(in_10), .in10(in_11), .in11(in_12), .in12(in_13), .in13(in_14), .in14(in_15),
    .in15(in_16), .in16(in_17), .in17(in_18), .in18(in_19), .in19(in_20), .in20(in_21), .in21(in_22),
    .in22(in_23), .in23(in_24), .in24(in_25), .in25(in_26), .in26(in_27), .in27(in_28), .in28(in_29),
    .in29(in_30), .in30(in_31), .in31(in_32), .out(multiplexer_1_out), .sel(sel[4:0]));
  Multiplexer #(.select(5), .enable("false")) multiplexer_2 (
    .in0(in_34), .in1(in_35), .in2(in_36), .in3(in_37), .in4(in_38), .in5(in_39), .in6(in_40), .in7(in_41),
    .in8(in_42), .in9(in_43), .in10(in_44), .in11(in_45), .in12(in_46), .in13(in_47), .in14(in_48),
    .in15(in_49), .in16(in_50), .in17(in_51), .in18(in_52), .in19(in_53), .in20(in_54), .in21(in_55),
    .in22(in_56), .in23(in_57), .in24(in_58), .in25(in_59), .in26(in_60), .in27(in_61), .in28(in_62),
    .in29(in_63), .in30(in_64), .in31(in_65), .out(multiplexer_2_out), .sel(sel[4:0]));
  Multiplexer #(.enable("false")) multiplexer_3 (
    .in0(multiplexer_1_out), .in1(multiplexer_2_out), .out(\output ), .sel(sel[5]));
  // Probe on opCode
endmodule

module MUX_opCode_2b (
  input  [1:0] in_1,
  input  [1:0] in_2,
  input  [1:0] in_3,
  input  [1:0] in_4,
  input  [1:0] in_5,
  input  [1:0] in_6,
  input  [1:0] in_7,
  input  [1:0] in_8,
  input  [1:0] in_9,
  input  [1:0] in_10,
  input  [1:0] in_11,
  input  [1:0] in_12,
  input  [1:0] in_13,
  input  [1:0] in_14,
  input  [1:0] in_15,
  input  [1:0] in_16,
  input  [1:0] in_17,
  input  [1:0] in_18,
  input  [1:0] in_19,
  input  [1:0] in_20,
  input  [1:0] in_21,
  input  [1:0] in_22,
  input  [1:0] in_23,
  input  [1:0] in_24,
  input  [1:0] in_25,
  input  [1:0] in_26,
  input  [1:0] in_27,
  input  [1:0] in_28,
  input  [1:0] in_29,
  input  [1:0] in_30,
  input  [1:0] in_31,
  input  [1:0] in_32,
  input  [5:0] sel,
  input  [1:0] in_34,
  input  [1:0] in_35,
  input  [1:0] in_36,
  input  [1:0] in_37,
  input  [1:0] in_38,
  input  [1:0] in_39,
  input  [1:0] in_40,
  input  [1:0] in_41,
  input  [1:0] in_42,
  input  [1:0] in_43,
  input  [1:0] in_44,
  input  [1:0] in_45,
  input  [1:0] in_46,
  input  [1:0] in_47,
  input  [1:0] in_48,
  input  [1:0] in_49,
  input  [1:0] in_50,
  input  [1:0] in_51,
  input  [1:0] in_52,
  input  [1:0] in_53,
  input  [1:0] in_54,
  input  [1:0] in_55,
  input  [1:0] in_56,
  input  [1:0] in_57,
  input  [1:0] in_58,
  input  [1:0] in_59,
  input  [1:0] in_60,
  input  [1:0] in_61,
  input  [1:0] in_62,
  input  [1:0] in_63,
  input  [1:0] in_64,
  input  [1:0] in_65,
  output [1:0] \output 
);

  wire [1:0] multiplexer_1_out, multiplexer_2_out;

  Multiplexer #(.select(5), .width(2), .enable("false")) multiplexer_1 (
    .in0(in_1), .in1(in_2), .in2(in_3), .in3(in_4), .in4(in_5), .in5(in_6), .in6(in_7), .in7(in_8),
    .in8(in_9), .in9(in_10), .in10(in_11), .in11(in_12), .in12(in_13), .in13(in_14), .in14(in_15),
    .in15(in_16), .in16(in_17), .in17(in_18), .in18(in_19), .in19(in_20), .in20(in_21), .in21(in_22),
    .in22(in_23), .in23(in_24), .in24(in_25), .in25(in_26), .in26(in_27), .in27(in_28), .in28(in_29),
    .in29(in_30), .in30(in_31), .in31(in_32), .out(multiplexer_1_out), .sel(sel[4:0]));
  Multiplexer #(.select(5), .width(2), .enable("false")) multiplexer_2 (
    .in0(in_34), .in1(in_35), .in2(in_36), .in3(in_37), .in4(in_38), .in5(in_39), .in6(in_40), .in7(in_41),
    .in8(in_42), .in9(in_43), .in10(in_44), .in11(in_45), .in12(in_46), .in13(in_47), .in14(in_48),
    .in15(in_49), .in16(in_50), .in17(in_51), .in18(in_52), .in19(in_53), .in20(in_54), .in21(in_55),
    .in22(in_56), .in23(in_57), .in24(in_58), .in25(in_59), .in26(in_60), .in27(in_61), .in28(in_62),
    .in29(in_63), .in30(in_64), .in31(in_65), .out(multiplexer_2_out), .sel(sel[4:0]));
  Multiplexer #(.width(2), .enable("false")) multiplexer_3 (
    .in0(multiplexer_1_out), .in1(multiplexer_2_out), .out(\output ), .sel(sel[5]));
endmodule

module MUX_opCode_8b (
  input  [7:0] in_1,
  input  [7:0] in_2,
  input  [7:0] in_3,
  input  [7:0] in_4,
  input  [7:0] in_5,
  input  [7:0] in_6,
  input  [7:0] in_7,
  input  [7:0] in_8,
  input  [7:0] in_9,
  input  [7:0] in_10,
  input  [7:0] in_11,
  input  [7:0] in_12,
  input  [7:0] in_13,
  input  [7:0] in_14,
  input  [7:0] in_15,
  input  [7:0] in_16,
  input  [7:0] in_17,
  input  [7:0] in_18,
  input  [7:0] in_19,
  input  [7:0] in_20,
  input  [7:0] in_21,
  input  [7:0] in_22,
  input  [7:0] in_23,
  input  [7:0] in_24,
  input  [7:0] in_25,
  input  [7:0] in_26,
  input  [7:0] in_27,
  input  [7:0] in_28,
  input  [7:0] in_29,
  input  [7:0] in_30,
  input  [7:0] in_31,
  input  [7:0] in_32,
  input  [5:0] sel,
  input  [7:0] in_34,
  input  [7:0] in_35,
  input  [7:0] in_36,
  input  [7:0] in_37,
  input  [7:0] in_38,
  input  [7:0] in_39,
  input  [7:0] in_40,
  input  [7:0] in_41,
  input  [7:0] in_42,
  input  [7:0] in_43,
  input  [7:0] in_44,
  input  [7:0] in_45,
  input  [7:0] in_46,
  input  [7:0] in_47,
  input  [7:0] in_48,
  input  [7:0] in_49,
  input  [7:0] in_50,
  input  [7:0] in_51,
  input  [7:0] in_52,
  input  [7:0] in_53,
  input  [7:0] in_54,
  input  [7:0] in_55,
  input  [7:0] in_56,
  input  [7:0] in_57,
  input  [7:0] in_58,
  input  [7:0] in_59,
  input  [7:0] in_60,
  input  [7:0] in_61,
  input  [7:0] in_62,
  input  [7:0] in_63,
  input  [7:0] in_64,
  input  [7:0] in_65,
  output [7:0] \output 
);

  wire [7:0] multiplexer_1_out, multiplexer_2_out;

  Multiplexer #(.select(5), .width(8), .enable("false")) multiplexer_1 (
    .in0(in_1), .in1(in_2), .in2(in_3), .in3(in_4), .in4(in_5), .in5(in_6), .in6(in_7), .in7(in_8),
    .in8(in_9), .in9(in_10), .in10(in_11), .in11(in_12), .in12(in_13), .in13(in_14), .in14(in_15),
    .in15(in_16), .in16(in_17), .in17(in_18), .in18(in_19), .in19(in_20), .in20(in_21), .in21(in_22),
    .in22(in_23), .in23(in_24), .in24(in_25), .in25(in_26), .in26(in_27), .in27(in_28), .in28(in_29),
    .in29(in_30), .in30(in_31), .in31(in_32), .out(multiplexer_1_out), .sel(sel[4:0]));
  Multiplexer #(.select(5), .width(8), .enable("false")) multiplexer_2 (
    .in0(in_34), .in1(in_35), .in2(in_36), .in3(in_37), .in4(in_38), .in5(in_39), .in6(in_40), .in7(in_41),
    .in8(in_42), .in9(in_43), .in10(in_44), .in11(in_45), .in12(in_46), .in13(in_47), .in14(in_48),
    .in15(in_49), .in16(in_50), .in17(in_51), .in18(in_52), .in19(in_53), .in20(in_54), .in21(in_55),
    .in22(in_56), .in23(in_57), .in24(in_58), .in25(in_59), .in26(in_60), .in27(in_61), .in28(in_62),
    .in29(in_63), .in30(in_64), .in31(in_65), .out(multiplexer_2_out), .sel(sel[4:0]));
  Multiplexer #(.width(8), .enable("false")) multiplexer_3 (
    .in0(multiplexer_1_out), .in1(multiplexer_2_out), .out(\output ), .sel(sel[5]));
endmodule

module MUX_opCode_32b (
  input  [31:0] in_1,
  input  [31:0] in_2,
  input  [31:0] in_3,
  input  [31:0] in_4,
  input  [31:0] in_5,
  input  [31:0] in_6,
  input  [31:0] in_7,
  input  [31:0] in_8,
  input  [31:0] in_9,
  input  [31:0] in_10,
  input  [31:0] in_11,
  input  [31:0] in_12,
  input  [31:0] in_13,
  input  [31:0] in_14,
  input  [31:0] in_15,
  input  [31:0] in_16,
  input  [31:0] in_17,
  input  [31:0] in_18,
  input  [31:0] in_19,
  input  [31:0] in_20,
  input  [31:0] in_21,
  input  [31:0] in_22,
  input  [31:0] in_23,
  input  [31:0] in_24,
  input  [31:0] in_25,
  input  [31:0] in_26,
  input  [31:0] in_27,
  input  [31:0] in_28,
  input  [31:0] in_29,
  input  [31:0] in_30,
  input  [31:0] in_31,
  input  [31:0] in_32,
  input  [5:0] sel,
  input  [31:0] in_34,
  input  [31:0] in_35,
  input  [31:0] in_36,
  input  [31:0] in_37,
  input  [31:0] in_38,
  input  [31:0] in_39,
  input  [31:0] in_40,
  input  [31:0] in_41,
  input  [31:0] in_42,
  input  [31:0] in_43,
  input  [31:0] in_44,
  input  [31:0] in_45,
  input  [31:0] in_46,
  input  [31:0] in_47,
  input  [31:0] in_48,
  input  [31:0] in_49,
  input  [31:0] in_50,
  input  [31:0] in_51,
  input  [31:0] in_52,
  input  [31:0] in_53,
  input  [31:0] in_54,
  input  [31:0] in_55,
  input  [31:0] in_56,
  input  [31:0] in_57,
  input  [31:0] in_58,
  input  [31:0] in_59,
  input  [31:0] in_60,
  input  [31:0] in_61,
  input  [31:0] in_62,
  input  [31:0] in_63,
  input  [31:0] in_64,
  input  [31:0] in_65,
  output [31:0] \output 
);

  wire [31:0] multiplexer_1_out, multiplexer_2_out;

  // Probe on sel
  // Probe on sel[4:0]
  // Probe on sel[5]
  Multiplexer #(.select(5), .width(32), .enable("false")) multiplexer_1 (
    .in0(in_1), .in1(in_2), .in2(in_3), .in3(in_4), .in4(in_5), .in5(in_6), .in6(in_7), .in7(in_8),
    .in8(in_9), .in9(in_10), .in10(in_11), .in11(in_12), .in12(in_13), .in13(in_14), .in14(in_15),
    .in15(in_16), .in16(in_17), .in17(in_18), .in18(in_19), .in19(in_20), .in20(in_21), .in21(in_22),
    .in22(in_23), .in23(in_24), .in24(in_25), .in25(in_26), .in26(in_27), .in27(in_28), .in28(in_29),
    .in29(in_30), .in30(in_31), .in31(in_32), .out(multiplexer_1_out), .sel(sel[4:0]));
  Multiplexer #(.select(5), .width(32), .enable("false")) multiplexer_2 (
    .in0(in_34), .in1(in_35), .in2(in_36), .in3(in_37), .in4(in_38), .in5(in_39), .in6(in_40), .in7(in_41),
    .in8(in_42), .in9(in_43), .in10(in_44), .in11(in_45), .in12(in_46), .in13(in_47), .in14(in_48),
    .in15(in_49), .in16(in_50), .in17(in_51), .in18(in_52), .in19(in_53), .in20(in_54), .in21(in_55),
    .in22(in_56), .in23(in_57), .in24(in_58), .in25(in_59), .in26(in_60), .in27(in_61), .in28(in_62),
    .in29(in_63), .in30(in_64), .in31(in_65), .out(multiplexer_2_out), .sel(sel[4:0]));
  Multiplexer #(.width(32), .enable("false")) multiplexer_3 (
    .in0(multiplexer_1_out), .in1(multiplexer_2_out), .out(\output ), .sel(sel[5]));
endmodule

module _4_letters_merge_interface (
  input  [7:0] letter_0,
  input  [7:0] letter_1,
  input  [7:0] letter_2,
  input  [7:0] letter_3,
  output [31:0] word_4_letters
);


  assign word_4_letters = {letter_3, letter_2, letter_1, letter_0};
endmodule

module _2_letters_merge_interface (
  input  [7:0] letter_0,
  input  [7:0] letter_1,
  output [15:0] word_4_letters
);


  assign word_4_letters = {letter_1, letter_0};
endmodule

module register_32b (
  input  [31:0] D,
  input  load,
  input  clk,
  input  rst,
  output [31:0] Q,
  output [31:0] Q_for_visulization
);

  Register #(.width(32), .Select("high")) register_1 (
    .D(D), .en(load), .Q(Q), .clk(clk), .clr(rst), .cs(1'b1), .preset(1'b0));

  assign Q_for_visulization = Q;
endmodule

module memory (
  input  [31:0] Adress,
  input  [31:0] Input,
  input  wrt,
  input  clk,
  input  ld,
  input  rst,
  output [31:0] Output
);

  wire comparator_1_gt;
  wire [31:0] ram_1_data, ram_2_data;

  Comparator #(.width(32)) comparator_1 (.a(Adress), .b(32'hffff), .gt(comparator_1_gt));  // open: eq, lt
  RAM #(.addrWidth(16), .dataWidth(32), .bus("separate"), .Select("high"), .simpleMode("false")) ram_1 (
    .addr(Adress[15:0]), .din(Input), .data(ram_1_data), .str(wrt), .sel(1'b1), .clk(clk), .ld(ld), .clr(rst));
  RAM #(.addrWidth(16), .dataWidth(32), .bus("separate"), .Select("high"), .simpleMode("false")) ram_2 (
    .addr(Adress[31:16]), .din(Input), .data(ram_2_data), .str(wrt), .sel(1'b1), .clk(clk), .ld(ld), .clr(rst));
  Multiplexer #(.width(32), .enable("false")) multiplexer_1 (
    .in0(ram_1_data), .in1(ram_2_data), .out(Output), .sel(comparator_1_gt));
endmodule

module Instruction_Register_32b (
  input  [31:0] D,
  input  load,
  input  clk,
  input  rst,
  output [5:0] opCode,
  output isOpALU,
  output [4:0] Rs,
  output [31:0] Q,
  output [4:0] Rt,
  output [4:0] Rd,
  output [4:0] SHAMT,
  output [31:0] Q_for_visulization,
  output [5:0] funct,
  output [15:0] immd,
  output [25:0] adrJMP
);

  Register #(.width(32), .Select("high")) register_1 (
    .D(D), .en(load), .Q({opCode, adrJMP}), .clk(clk), .clr(rst), .cs(1'b1), .preset(1'b0));
  Comparator #(.width(6)) comparator_1 (.a(opCode), .b({6{1'b0}}), .eq(isOpALU));  // open: gt, lt

  assign funct = adrJMP[5:0];
  assign immd = adrJMP[15:0];
  assign Q = {opCode, adrJMP};
  assign Q_for_visulization = {opCode, adrJMP};
  assign Rd = adrJMP[15:11];
  assign Rs = adrJMP[25:21];
  assign Rt = adrJMP[20:16];
  assign SHAMT = adrJMP[10:6];
endmodule
